# Fritzing sketch VGA (saved by Fritzing 0.9.6b)
breadboards: 1

parts:
  74LS85 = IC, DIP package, 16 pins [chip_label=IC]
  74LS86 = IC, DIP package, 16 pins [chip_label=IC]
  74LS87 = IC, DIP package, 16 pins [chip_label=IC]

nets:
  N1: 74LS85.pin1, 74LS85.pin8, 74LS86.pin1, 74LS86.pin8, 74LS87.pin8
  N2: 74LS85.pin5, 74LS86.pin4
  N3: 74LS85.pin6, 74LS86.pin3
  N4: 74LS85.pin7, 74LS86.pin2
  N5: 74LS85.pin9, 74LS85.pin11, 74LS85.pin14, 74LS86.pin11, 74LS86.pin14, 74LS87.pin9, 74LS87.pin11, 74LS87.pin14
  N6: 74LS85.pin16, 74LS86.pin9, 74LS86.pin16, 74LS87.pin16
  N7: 74LS86.pin5, 74LS87.pin4
  N8: 74LS86.pin6, 74LS87.pin3
  N9: 74LS86.pin7, 74LS87.pin2

notes:
  RESET
  1000010000
