// Logisim project 8-bit-computer.circ as structural Verilog
module TTL_74LS169 (
  input  UP_DOWN,
  input  LOAD,
  input  ENP,
  input  ENT,
  input  CLOCK,
  input  [3:0] Data_In,
  output [3:0] Q,
  output CO
);

  wire and_1_out, and_2_out, and_3_out, and_4_out, and_5_out, and_6_out, and_7_out, and_8_out, and_9_out,
       and_10_out, and_11_out, and_12_out, and_13_out, and_14_out, and_15_out, and_16_out, and_17_out,
       d_ff_1_q, d_ff_1_qn, d_ff_2_q, d_ff_2_qn, d_ff_3_q, d_ff_3_qn, d_ff_4_q, d_ff_4_qn, nor_1_out,
       nor_2_out, nor_3_out, nor_4_out, nor_5_out, nor_6_out, nor_7_out, nor_8_out, nor_9_out, nor_10_out,
       nor_11_out, nor_12_out, not_1_out, not_2_out, not_3_out, not_4_out, not_5_out, not_6_out, not_7_out,
       not_8_out, not_9_out, not_10_out, not_11_out, not_12_out, not_13_out, not_14_out, not_15_out,
       not_16_out, not_17_out, not_18_out, or_1_out, or_2_out, or_3_out;

  not not_1 (not_1_out, UP_DOWN);
  not not_2 (not_2_out, LOAD);
  not not_3 (not_3_out, not_1_out);
  not not_4 (not_4_out, not_2_out);
  not not_5 (not_5_out, not_2_out);
  not not_6 (not_6_out, ENP);
  and and_1 (and_1_out, not_5_out, not_6_out, not_7_out);
  not not_7 (not_7_out, ENT);
  not not_8 (not_8_out, ENT);
  nor nor_1 (nor_1_out, not_4_out, Data_In[0]);
  nor nor_2 (nor_2_out, not_4_out, Data_In[1]);
  nor nor_3 (nor_3_out, not_4_out, Data_In[2]);
  nor nor_4 (nor_4_out, not_4_out, Data_In[3]);
  and and_2 (and_2_out, d_ff_3_q, not_3_out);
  and and_3 (and_3_out, not_1_out, d_ff_3_qn);
  and and_4 (and_4_out, d_ff_4_q, not_3_out);
  and and_5 (and_5_out, not_1_out, d_ff_4_qn);
  and and_6 (and_6_out, d_ff_1_q, not_3_out);
  and and_7 (and_7_out, not_1_out, d_ff_1_qn);
  and and_8 (and_8_out, d_ff_2_q, not_3_out);
  and and_9 (and_9_out, not_1_out, d_ff_2_qn);
  nor nor_5 (nor_5_out, and_2_out, and_3_out);
  nor nor_6 (nor_6_out, and_4_out, and_5_out);
  nor nor_7 (nor_7_out, and_6_out, and_7_out);
  nor nor_8 (nor_8_out, and_8_out, and_9_out);
  not not_9 (not_9_out, and_1_out);
  not not_10 (not_10_out, nor_7_out);
  not not_11 (not_11_out, nor_8_out);
  not not_12 (not_12_out, and_1_out);
  not not_13 (not_13_out, nor_7_out);
  or or_1 (or_1_out, not_9_out, not_10_out, not_11_out);
  not not_14 (not_14_out, and_1_out);
  not not_15 (not_15_out, nor_7_out);
  or or_2 (or_2_out, not_14_out, not_15_out, not_16_out, not_17_out);
  not not_16 (not_16_out, nor_8_out);
  not not_17 (not_17_out, nor_5_out);
  nand nand_1 (CO, nor_7_out, nor_8_out, nor_5_out, nor_6_out, not_8_out);
  not not_18 (not_18_out, and_1_out);
  or or_3 (or_3_out, not_12_out, not_13_out);
  and and_10 (and_10_out, d_ff_1_q, and_1_out);
  and and_11 (and_11_out, not_18_out, not_4_out, d_ff_1_qn);
  and and_12 (and_12_out, d_ff_2_q, and_1_out, nor_7_out);
  and and_13 (and_13_out, or_3_out, not_4_out, d_ff_2_qn);
  and and_14 (and_14_out, d_ff_3_q, and_1_out, nor_7_out, nor_8_out);
  and and_15 (and_15_out, or_1_out, not_4_out, d_ff_3_qn);
  and and_16 (and_16_out, d_ff_4_q, and_1_out, nor_7_out, nor_8_out, nor_5_out);
  and and_17 (and_17_out, or_2_out, not_4_out, d_ff_4_qn);
  nor nor_9 (nor_9_out, and_10_out, and_11_out, nor_1_out);
  nor nor_10 (nor_10_out, and_12_out, and_13_out, nor_2_out);
  nor nor_11 (nor_11_out, and_14_out, and_15_out, nor_3_out);
  nor nor_12 (nor_12_out, and_16_out, and_17_out, nor_4_out);
  D_Flip_Flop d_ff_1 (.D(nor_9_out), .clk(CLOCK), .Q(d_ff_1_q), .Qn(d_ff_1_qn), .preset(1'b0), .reset(1'b0));
  D_Flip_Flop d_ff_2 (.D(nor_10_out), .clk(CLOCK), .Q(d_ff_2_q), .Qn(d_ff_2_qn), .preset(1'b0), .reset(1'b0));
  D_Flip_Flop d_ff_3 (.D(nor_11_out), .clk(CLOCK), .Q(d_ff_3_q), .Qn(d_ff_3_qn), .preset(1'b0), .reset(1'b0));
  D_Flip_Flop d_ff_4 (.D(nor_12_out), .clk(CLOCK), .Q(d_ff_4_q), .Qn(d_ff_4_qn), .preset(1'b0), .reset(1'b0));
  not not_19 (Q[0], d_ff_1_qn);
  not not_20 (Q[1], d_ff_2_qn);
  not not_21 (Q[2], d_ff_3_qn);
  not not_22 (Q[3], d_ff_4_qn);
endmodule

module TTL_74LS193 (
  input  P3,
  input  P2,
  input  P1,
  input  P0,
  input  LOAD,
  input  UP,
  input  DOWN,
  input  CLEAR,
  output Q3,
  output Q2,
  output Q1,
  output QO,
  output CO,
  output BO
);

  wire and_1_out, and_2_out, and_3_out, and_4_out, and_5_out, and_6_out, nand_1_out, nand_2_out, nand_3_out,
       nand_4_out, nand_5_out, nand_6_out, nand_7_out, nand_8_out, nor_1_out, nor_2_out, nor_3_out,
       nor_4_out, not_1_out, not_2_out, not_3_out, not_4_out, not_5_out, not_6_out, not_7_out, not_8_out,
       not_9_out, not_10_out, not_11_out, not_12_out, not_13_out, not_14_out, not_15_out, not_16_out,
       not_17_out, not_18_out, not_19_out, not_20_out, not_21_out, not_22_out, or_1_out, or_2_out, or_3_out,
       or_4_out, t_ff_1_qn, t_ff_2_qn, t_ff_3_qn, t_ff_4_qn;

  not not_1 (not_1_out, UP);
  not not_2 (not_2_out, DOWN);
  nor nor_1 (nor_1_out, not_1_out, not_2_out);
  not not_3 (not_3_out, LOAD);
  nand nand_1 (nand_1_out, not_3_out, not_7_out, P0);
  not not_4 (not_4_out, nand_1_out);
  T_Flip_Flop t_ff_1 (.T(nor_1_out), .clk(nor_1_out), .Q(QO), .Qn(t_ff_1_qn), .reset(or_1_out), .preset(not_4_out));
  or or_1 (or_1_out, not_5_out, not_6_out);
  not not_5 (not_5_out, not_7_out);
  not not_6 (not_6_out, nand_2_out);
  not not_7 (not_7_out, CLEAR);
  nand nand_2 (nand_2_out, nand_1_out, not_3_out);
  and and_1 (and_1_out, not_1_out, QO);
  and and_2 (and_2_out, t_ff_1_qn, not_2_out);
  nor nor_2 (nor_2_out, and_1_out, and_2_out);
  LED led_1 (.in(Q3));
  not not_8 (not_8_out, LOAD);
  nand nand_3 (nand_3_out, not_8_out, not_12_out, P1);
  not not_9 (not_9_out, nand_3_out);
  T_Flip_Flop t_ff_2 (.T(nor_2_out), .clk(nor_2_out), .Q(Q1), .Qn(t_ff_2_qn), .reset(or_2_out), .preset(not_9_out));
  or or_2 (or_2_out, not_10_out, not_11_out);
  not not_10 (not_10_out, not_12_out);
  not not_11 (not_11_out, nand_4_out);
  not not_12 (not_12_out, CLEAR);
  LED led_2 (.in(Q2));
  LED led_3 (.in(Q1));
  LED led_4 (.in(QO));
  nand nand_4 (nand_4_out, nand_3_out, not_8_out);
  and and_3 (and_3_out, not_1_out, QO, Q1);
  and and_4 (and_4_out, t_ff_2_qn, t_ff_1_qn, not_2_out);
  nor nor_3 (nor_3_out, and_3_out, and_4_out);
  not not_13 (not_13_out, LOAD);
  nand nand_5 (nand_5_out, not_13_out, not_17_out, P2);
  not not_14 (not_14_out, nand_5_out);
  T_Flip_Flop t_ff_3 (.T(nor_3_out), .clk(nor_3_out), .Q(Q2), .Qn(t_ff_3_qn), .reset(or_3_out), .preset(not_14_out));
  or or_3 (or_3_out, not_15_out, not_16_out);
  not not_15 (not_15_out, not_17_out);
  not not_16 (not_16_out, nand_6_out);
  not not_17 (not_17_out, CLEAR);
  nand nand_6 (nand_6_out, nand_5_out, not_13_out);
  and and_5 (and_5_out, not_1_out, QO, Q1, Q2);
  and and_6 (and_6_out, t_ff_3_qn, t_ff_2_qn, t_ff_1_qn, not_2_out);
  nor nor_4 (nor_4_out, and_5_out, and_6_out);
  not not_18 (not_18_out, LOAD);
  nand nand_7 (nand_7_out, not_18_out, not_20_out, P3);
  T_Flip_Flop t_ff_4 (.T(nor_4_out), .clk(nor_4_out), .Q(Q3), .Qn(t_ff_4_qn), .reset(or_4_out), .preset(not_21_out));
  not not_19 (not_19_out, not_20_out);
  not not_20 (not_20_out, CLEAR);
  nand nand_8 (nand_8_out, nand_7_out, not_18_out);
  not not_21 (not_21_out, nand_7_out);
  or or_4 (or_4_out, not_19_out, not_22_out);
  not not_22 (not_22_out, nand_8_out);
  LED led_5 (.in(CO));
  nand nand_9 (CO, not_1_out, QO, Q1, Q2, Q3);
  LED led_6 (.in(BO));
  nand nand_10 (BO, t_ff_4_qn, t_ff_3_qn, t_ff_2_qn, t_ff_1_qn, not_2_out);
endmodule

module Module_IndexRegister (
  input  [15:0] DATA_IN,
  input  LOAD,
  input  UP,
  input  DOWN,
  input  CLEAR,
  input  IDX_OUT,
  input  [2:0] IDX_CONTROL,
  output [15:0] PORTA,
  output [15:0] PORTB
);

  wire decoder_1_out0, decoder_1_out1, decoder_1_out2, decoder_1_out3, decoder_2_out0, decoder_2_out1,
       decoder_2_out2, decoder_2_out3, not_1_out, not_2_out, not_3_out, not_4_out, not_5_out, not_6_out,
       not_7_out, not_10_out, not_11_out, not_12_out, not_13_out, not_14_out, not_15_out, not_16_out,
       ttl_74ls193_1_bo, ttl_74ls193_1_co, ttl_74ls193_2_bo, ttl_74ls193_2_co, ttl_74ls193_3_bo,
       ttl_74ls193_3_co;
  wire [15:0] controlled_buffer_1_out, ttl_74ls193_4_q3;

  TTL_74LS193 ttl_74ls193_1 (
    .P3(DATA_IN[3]), .P2(DATA_IN[2]), .P1(DATA_IN[1]), .P0(DATA_IN[0]), .LOAD(LOAD), .UP(UP), .DOWN(DOWN),
    .CLEAR(CLEAR), .Q3(ttl_74ls193_4_q3[3]), .Q2(ttl_74ls193_4_q3[2]), .Q1(ttl_74ls193_4_q3[1]),
    .QO(ttl_74ls193_4_q3[0]), .CO(ttl_74ls193_1_co), .BO(ttl_74ls193_1_bo));
  TTL_74LS193 ttl_74ls193_2 (
    .P3(DATA_IN[7]), .P2(DATA_IN[6]), .P1(DATA_IN[5]), .P0(DATA_IN[4]), .LOAD(LOAD), .UP(ttl_74ls193_1_co),
    .DOWN(ttl_74ls193_1_bo), .CLEAR(CLEAR), .Q3(ttl_74ls193_4_q3[7]), .Q2(ttl_74ls193_4_q3[6]),
    .Q1(ttl_74ls193_4_q3[5]), .QO(ttl_74ls193_4_q3[4]), .CO(ttl_74ls193_2_co), .BO(ttl_74ls193_2_bo));
  TTL_74LS193 ttl_74ls193_3 (
    .P3(DATA_IN[11]), .P2(DATA_IN[10]), .P1(DATA_IN[9]), .P0(DATA_IN[8]), .LOAD(LOAD), .UP(ttl_74ls193_2_co),
    .DOWN(ttl_74ls193_2_bo), .CLEAR(CLEAR), .Q3(ttl_74ls193_4_q3[11]), .Q2(ttl_74ls193_4_q3[10]),
    .Q1(ttl_74ls193_4_q3[9]), .QO(ttl_74ls193_4_q3[8]), .CO(ttl_74ls193_3_co), .BO(ttl_74ls193_3_bo));
  TTL_74LS193 ttl_74ls193_4 (
    .P3(DATA_IN[15]), .P2(DATA_IN[14]), .P1(DATA_IN[13]), .P0(DATA_IN[12]), .LOAD(LOAD),
    .UP(ttl_74ls193_3_co), .DOWN(ttl_74ls193_3_bo), .CLEAR(CLEAR), .Q3(ttl_74ls193_4_q3[15]),
    .Q2(ttl_74ls193_4_q3[14]), .Q1(ttl_74ls193_4_q3[13]), .QO(ttl_74ls193_4_q3[12]));  // open: CO, BO
  not not_1 (not_1_out, decoder_1_out0);
  not not_2 (not_2_out, decoder_1_out1);
  not not_3 (not_3_out, decoder_1_out2);
  not not_4 (not_4_out, decoder_1_out3);
  Decoder #(.select(2)) decoder_1 (
    .out0(decoder_1_out0), .out1(decoder_1_out1), .out2(decoder_1_out2), .out3(decoder_1_out3),
    .sel(IDX_CONTROL[1:0]), .en(not_5_out));
  not not_5 (not_5_out, IDX_OUT);
  not not_6 (not_6_out, decoder_2_out0);
  not not_7 (not_7_out, decoder_2_out1);
  // NOT_Gate not_8 has open pins: in=decoder_2_out2, out=open
  // NOT_Gate not_9 has open pins: in=decoder_2_out3, out=open
  Decoder #(.select(2)) decoder_2 (
    .out0(decoder_2_out0), .out1(decoder_2_out1), .out2(decoder_2_out2), .out3(decoder_2_out3),
    .sel({1'b0, IDX_CONTROL[2]}), .en(not_10_out));
  not not_10 (not_10_out, IDX_OUT);
  assign controlled_buffer_1_out = not_11_out ? ttl_74ls193_4_q3 : 16'bz;  // Controlled_Buffer controlled_buffer_1
  not not_11 (not_11_out, not_1_out);
  not not_12 (not_12_out, not_2_out);
  assign controlled_buffer_1_out = not_12_out ? {ttl_74ls193_4_q3[14:0], 1'b0} : 16'bz;  // Controlled_Buffer controlled_buffer_2
  assign controlled_buffer_1_out = not_13_out ? {ttl_74ls193_4_q3[13:0], 2'b00} : 16'bz;  // Controlled_Buffer controlled_buffer_3
  not not_13 (not_13_out, not_3_out);
  assign controlled_buffer_1_out = not_14_out ? {ttl_74ls193_4_q3[12:0], 3'b000} : 16'bz;  // Controlled_Buffer controlled_buffer_4
  not not_14 (not_14_out, not_4_out);
  assign PORTA = not_15_out ? controlled_buffer_1_out : 16'bz;  // Controlled_Buffer controlled_buffer_5
  not not_15 (not_15_out, not_6_out);
  assign PORTB = not_16_out ? controlled_buffer_1_out : 16'bz;  // Controlled_Buffer controlled_buffer_6
  not not_16 (not_16_out, not_7_out);

  // Notes on the sheet:
  //   x1
  //   x2
  //   x4
  //   x8
endmodule

module Module_TimerInterrupt (
  input  [7:0] DATA,
  input  LATCH_RELOAD,
  input  CLOCK,
  input  CLEAR_IRQ,
  output IRQ
);

  wire nand_2_out, not_1_out, or_1_out, ttl_74ls169_1_co, ttl_74ls169_2_co;
  wire [3:0] ledbar_1_p1, ledbar_2_p1;
  wire [7:0] register_1_q;

  Register register_1 (.D(DATA), .en(not_1_out), .clk(CLOCK), .Q(register_1_q), .clr(1'b0));
  not not_1 (not_1_out, LATCH_RELOAD);
  or or_1 (or_1_out, ttl_74ls169_2_co, ttl_74ls169_1_co);
  // LedBar #(.inputtype("row"), .matrixcols(4)) ledbar_1: pin names not known; wires that end beside it: ledbar_1_p1
  TTL_74LS169 ttl_74ls169_1 (
    .UP_DOWN(1'b0), .LOAD(or_1_out), .ENP(1'b0), .ENT(1'b0), .CLOCK(CLOCK), .Data_In(register_1_q[3:0]),
    .Q(ledbar_1_p1), .CO(ttl_74ls169_1_co));
  // LedBar #(.inputtype("row"), .matrixcols(4)) ledbar_2: pin names not known; wires that end beside it: ledbar_2_p1
  TTL_74LS169 ttl_74ls169_2 (
    .UP_DOWN(1'b0), .LOAD(or_1_out), .ENP(1'b0), .ENT(ttl_74ls169_1_co), .CLOCK(CLOCK),
    .Data_In(register_1_q[7:4]), .Q(ledbar_2_p1), .CO(ttl_74ls169_2_co));
  nand nand_1 (IRQ, or_1_out, nand_2_out);
  nand nand_2 (nand_2_out, IRQ, CLEAR_IRQ);
  LED led_1 (.in(IRQ));
endmodule

module Module_InstructionRegister (
  input  LD_INST_LOW,
  input  IRQ_LOW,
  input  [7:0] DATA_BUS,
  input  RESET_LOW,
  input  CLOCK,
  input  RESET_STEP_LOW,
  output [7:0] OPCODE,
  output [3:0] STEP
);

  wire and_1_out, and_2_out, n74161_1_pin1, n74161_1_pin2, n74161_1_pin3, n74161_1_pin7, n74161_1_pin10,
       n74161_1_pin15, not_2_out, not_3_out, not_4_out, not_5_out, or_1_out, or_2_out, or_3_out;
  wire [7:0] ledbar_2_p1;

  // NoConnect on n74161_1_pin15
  _74161 u_74161_1 (
    .pin1(n74161_1_pin1), .pin2(n74161_1_pin2), .pin3(n74161_1_pin3), .pin4(n74161_1_pin3),
    .pin5(n74161_1_pin3), .pin6(n74161_1_pin3), .pin7(n74161_1_pin7), .pin15(n74161_1_pin15),
    .pin14(STEP[0]), .pin13(STEP[1]), .pin12(STEP[2]), .pin11(STEP[3]), .pin10(n74161_1_pin10),
    .pin9(RESET_STEP_LOW));
  not not_1 (n74161_1_pin2, CLOCK);
  // LedBar #(.inputtype("row"), .matrixcols(4)) ledbar_1: pin names not known; wires that end beside it: STEP
  or or_1 (or_1_out, STEP[0], STEP[1], STEP[2], STEP[3]);
  or or_2 (or_2_out, IRQ_LOW, or_1_out);
  or or_3 (or_3_out, or_1_out, RESET_LOW);
  and and_1 (and_1_out, or_2_out, or_3_out);
  // LedBar #(.inputtype("row")) ledbar_2: pin names not known; wires that end beside it: ledbar_2_p1
  assign ledbar_2_p1 = not_2_out ? DATA_BUS : 8'bz;  // Controlled_Buffer controlled_buffer_1
  not not_2 (not_2_out, not_3_out);
  not not_3 (not_3_out, and_1_out);
  assign ledbar_2_p1 = not_4_out ? {{7{1'b1}}, RESET_LOW} : 8'bz;  // Controlled_Buffer controlled_buffer_2
  not not_4 (not_4_out, and_1_out);
  and and_2 (and_2_out, LD_INST_LOW, and_1_out);
  Register register_1 (.D(ledbar_2_p1), .en(not_5_out), .clk(CLOCK), .Q(OPCODE), .clr(1'b0));
  not not_5 (not_5_out, and_2_out);
  // LedBar #(.inputtype("row")) ledbar_3: pin names not known; wires that end beside it: OPCODE
  // also tied to GND on the sheet: n74161_1_pin3
  // also tied to VCC on the sheet: {n74161_1_pin1, n74161_1_pin10, n74161_1_pin7}

  // Notes on the sheet:
  //   DATA_BUS: pull=down
  //   LD_INST_LOW: pull=up
  //   IRQ_LOW: pull=up
  //   RESET_LOW: pull=up
  //   RESET_STEP_LOW: pull=up
  //   ZF
  //   VECTOR
  //   0xfe - Reset
  //   0xff - Interrupt Request
endmodule

module Module_16bitAdder (
  input  [15:0] A,
  input  [15:0] B,
  input  CI,
  output CO,
  output [15:0] out_5
);

  wire n74283_1_pin9, n74283_2_pin9, n74283_3_pin9;

  _74283 u_74283_1 (
    .pin1(out_5[1]), .pin2(B[1]), .pin3(A[1]), .pin4(out_5[0]), .pin5(A[0]), .pin6(B[0]), .pin7(CI),
    .pin15(B[2]), .pin14(A[2]), .pin13(out_5[2]), .pin12(A[3]), .pin11(B[3]), .pin10(out_5[3]),
    .pin9(n74283_1_pin9));
  _74283 u_74283_2 (
    .pin1(out_5[5]), .pin2(B[5]), .pin3(A[5]), .pin4(out_5[4]), .pin5(A[4]), .pin6(B[4]),
    .pin7(n74283_1_pin9), .pin15(B[6]), .pin14(A[6]), .pin13(out_5[6]), .pin12(A[7]), .pin11(B[7]),
    .pin10(out_5[7]), .pin9(n74283_2_pin9));
  _74283 u_74283_3 (
    .pin1(out_5[9]), .pin2(B[9]), .pin3(A[9]), .pin4(out_5[8]), .pin5(A[8]), .pin6(B[8]),
    .pin7(n74283_2_pin9), .pin15(B[10]), .pin14(A[10]), .pin13(out_5[10]), .pin12(A[11]), .pin11(B[11]),
    .pin10(out_5[11]), .pin9(n74283_3_pin9));
  _74283 u_74283_4 (
    .pin1(out_5[13]), .pin2(B[13]), .pin3(A[13]), .pin4(out_5[12]), .pin5(A[12]), .pin6(B[12]),
    .pin7(n74283_3_pin9), .pin15(B[14]), .pin14(A[14]), .pin13(out_5[14]), .pin12(A[15]), .pin11(B[15]),
    .pin10(out_5[15]), .pin9(CO));
endmodule

module Module_8bitRegisterGPR (
  input  [7:0] D,
  input  CLOCK,
  input  LATCH,
  input  OE,
  input  RESET,
  output [15:0] Q
);

  wire not_1_out, not_2_out;
  wire [7:0] register_1_q, register_2_q;

  not not_1 (not_1_out, LATCH);
  Register register_1 (.D(D), .en(not_1_out), .clk(CLOCK), .Q(register_1_q), .clr(RESET));
  Register register_2 (.D({8{D[7]}}), .en(not_1_out), .clk(CLOCK), .Q(register_2_q), .clr(RESET));
  assign Q = not_2_out ? {register_2_q, register_1_q} : 16'bz;  // Controlled_Buffer controlled_buffer_1
  not not_2 (not_2_out, OE);
  Pull_Resistor pull_resistor_1 (.node(Q));
endmodule

module FULL_BUILD (
  input  LOAD_FROM_BUS,
  input  INDEX_OUT,
  input  [2:0] INDEX_CONTROL,
  input  OFFSET_LATCH,
  input  OFFSET_OE
);

  wire CLEAR_out, clock_1_out, INDEX_DEC_out, INDEX_INC_out, INDEX_LATCH_out, module_16bitadder_1_co,
       not_1_out;
  wire [7:0] dipswitch_2_sw8;
  wire [15:0] controlled_buffer_1_out, dipswitch_1_sw16, ledbar_1_p1, module_indexregister_1_portb;

  DipSwitch #(.number(16)) dipswitch_1 (
    .sw1(dipswitch_1_sw16[15]), .sw2(dipswitch_1_sw16[14]), .sw3(dipswitch_1_sw16[13]),
    .sw4(dipswitch_1_sw16[12]), .sw5(dipswitch_1_sw16[11]), .sw6(dipswitch_1_sw16[10]),
    .sw7(dipswitch_1_sw16[9]), .sw8(dipswitch_1_sw16[8]), .sw9(dipswitch_1_sw16[7]),
    .sw10(dipswitch_1_sw16[6]), .sw11(dipswitch_1_sw16[5]), .sw12(dipswitch_1_sw16[4]),
    .sw13(dipswitch_1_sw16[3]), .sw14(dipswitch_1_sw16[2]), .sw15(dipswitch_1_sw16[1]),
    .sw16(dipswitch_1_sw16[0]));
  DipSwitch dipswitch_2 (
    .sw1(dipswitch_2_sw8[7]), .sw2(dipswitch_2_sw8[6]), .sw3(dipswitch_2_sw8[5]), .sw4(dipswitch_2_sw8[4]),
    .sw5(dipswitch_2_sw8[3]), .sw6(dipswitch_2_sw8[2]), .sw7(dipswitch_2_sw8[1]), .sw8(dipswitch_2_sw8[0]));
  Button #(.press("passive")) INDEX_LATCH (.out(INDEX_LATCH_out));
  Button #(.press("passive")) INDEX_INC (.out(INDEX_INC_out));
  Button #(.press("passive")) INDEX_DEC (.out(INDEX_DEC_out));
  Button CLEAR (.out(CLEAR_out));
  Clock clock_1 (.out(clock_1_out));
  not not_1 (not_1_out, LOAD_FROM_BUS);
  assign controlled_buffer_1_out = not_1_out ? dipswitch_1_sw16 : 16'bz;  // Controlled_Buffer controlled_buffer_1
  Module_IndexRegister module_indexregister_1 (
    .DATA_IN(dipswitch_1_sw16), .LOAD(INDEX_LATCH_out), .UP(INDEX_INC_out), .DOWN(INDEX_DEC_out),
    .CLEAR(CLEAR_out), .IDX_OUT(INDEX_OUT), .IDX_CONTROL(INDEX_CONTROL), .PORTA(controlled_buffer_1_out),
    .PORTB(module_indexregister_1_portb));
  Module_8bitRegisterGPR module_8bitregistergpr_1 (
    .D(dipswitch_2_sw8), .CLOCK(clock_1_out), .LATCH(OFFSET_LATCH), .OE(OFFSET_OE), .RESET(CLEAR_out),
    .Q(module_indexregister_1_portb));
  // LedBar #(.inputtype("row"), .matrixcols(16)) ledbar_1: pin names not known; wires that end beside it: ledbar_1_p1
  // NoConnect on module_16bitadder_1_co
  Module_16bitAdder module_16bitadder_1 (
    .A(controlled_buffer_1_out), .B(module_indexregister_1_portb), .CI(1'b0), .CO(module_16bitadder_1_co),
    .out_5(ledbar_1_p1));
endmodule
