// Logisim project ADSR.circ as structural Verilog: 1 circuit, main circuit main
module main (
);

  wire clock_1_out, ttl_74ls169_1_co;
  wire [3:0] ttl_74ls169_1_q;

  Clock clock_1 (.out(clock_1_out));
  TTL_74LS169 ttl_74ls169_1 (
    .UP_DOWN(1'b1), .LOAD(1'b1), .ENP(1'b0), .ENT(1'b0), .CLOCK(clock_1_out), .Data_In(4'b1111),
    .Q(ttl_74ls169_1_q), .CO(ttl_74ls169_1_co));
  // LedBar #(.inputtype("row"), .matrixcols(4)) ledbar_1: pin names not known; wires that end beside it: ttl_74ls169_1_co, ttl_74ls169_1_q
endmodule
