// Logisim project ALU.circ as structural Verilog: 10 circuits, main circuit main
module main (
  input  MODE,
  input  Carry,
  output O0,
  output O1,
  output O2,
  output O3,
  output O4,
  output O5,
  output O6,
  output O7,
  output CF,
  output SF,
  output ZF,
  output OVF
);

  wire alu_1_carry_flag, alu_1_o0, alu_1_o1, alu_1_o2, alu_1_o3, alu_1_o4, alu_1_o5, alu_1_o6, alu_1_o7,
       alu_1_overflow, alu_1_sign_flag, alu_1_zero_flag, ALU_Out_out, and_1_out, BUSDATA_p1, BUSDATA_p2,
       BUSDATA_p3, BUSDATA_p4, BUSDATA_p5, BUSDATA_p6, BUSDATA_p7, BUSDATA_p8, clock_1_out, Func0_out,
       Func1_out, Func2_out, Func3_out, Load_A_out, Load_ALU_out, Load_B_out, nand_1_out, not_1_out,
       not_2_out, or_1_out, or_2_out, or_3_out, or_4_out, or_5_out, register_5bit_1_carryincn,
       register_5bit_1_func0, register_5bit_1_func1, register_5bit_1_func2, register_5bit_1_func3, Reset_out,
       Rotate_Left_out, Rotate_Right_out, Shift_Left_out, Shift_Right_out;

  Button #(.press("passive")) Reset (.out(Reset_out));
  Button #(.press("passive")) Func0 (.out(Func0_out));
  Button Func1 (.out(Func1_out));
  Button #(.press("passive")) Func2 (.out(Func2_out));
  Button Func3 (.out(Func3_out));
  Button #(.press("passive")) Rotate_Right (.out(Rotate_Right_out));
  Button #(.press("passive")) Rotate_Left (.out(Rotate_Left_out));
  Button #(.press("passive")) Shift_Right (.out(Shift_Right_out));
  Button #(.press("passive")) Shift_Left (.out(Shift_Left_out));
  Button Load_ALU (.out(Load_ALU_out));
  Button #(.press("passive")) Load_A (.out(Load_A_out));
  Button Load_B (.out(Load_B_out));
  Button ALU_Out (.out(ALU_Out_out));
  Clock clock_1 (.out(clock_1_out));
  nand nand_1 (nand_1_out, Rotate_Right_out, Rotate_Left_out, Shift_Right_out, Shift_Left_out);
  not not_1 (not_1_out, nand_1_out);
  or or_1 (or_1_out, Func0_out, nand_1_out);
  or or_2 (or_2_out, Func1_out, nand_1_out);
  or or_3 (or_3_out, Func2_out, nand_1_out);
  or or_4 (or_4_out, Func3_out, nand_1_out);
  and and_1 (and_1_out, not_1_out, Carry);
  or or_5 (or_5_out, nand_1_out, Load_ALU_out);
  // DipSwitch BUSDATA: pin names not known; wires that end beside it: BUSDATA_p1, BUSDATA_p2, BUSDATA_p3, BUSDATA_p4, BUSDATA_p5, BUSDATA_p6, BUSDATA_p7, BUSDATA_p8
  register_5bit register_5bit_1 (
    .D0(or_1_out), .D1(or_2_out), .D2(or_3_out), .D3(or_4_out), .Carry_In(and_1_out), .Write(or_5_out),
    .Clock(clock_1_out), .Func0(register_5bit_1_func0), .Func1(register_5bit_1_func1),
    .Func2(register_5bit_1_func2), .Func3(register_5bit_1_func3), .CarryInCn(register_5bit_1_carryincn));
  ALU alu_1 (
    .S3(register_5bit_1_func3), .S2(register_5bit_1_func2), .S1(register_5bit_1_func1),
    .S0(register_5bit_1_func0), .MODE(MODE), .CI(register_5bit_1_carryincn), .BUS7(BUSDATA_p1),
    .BUS6(BUSDATA_p2), .BUS5(BUSDATA_p3), .BUS4(BUSDATA_p4), .BUS3(BUSDATA_p5), .BUS2(BUSDATA_p6),
    .BUS1(BUSDATA_p7), .BUS0(BUSDATA_p8), .RESET(Reset_out), .CLOCK(clock_1_out), .ROTL(Rotate_Right_out),
    .ROTR(Rotate_Left_out), .LDA(Load_A_out), .SHR(Shift_Left_out), .SHL(Shift_Right_out), .LDB(Load_B_out),
    .O0(alu_1_o0), .O1(alu_1_o1), .O2(alu_1_o2), .O3(alu_1_o3), .O4(alu_1_o4), .O5(alu_1_o5), .O6(alu_1_o6),
    .O7(alu_1_o7), .CARRY_FLAG(alu_1_carry_flag), .SIGN_FLAG(alu_1_sign_flag), .ZERO_FLAG(alu_1_zero_flag),
    .OVERFLOW(alu_1_overflow));
  not not_2 (not_2_out, ALU_Out_out);
  LedBar ALU_OUTPUT (
    .led0(alu_1_o7), .led1(alu_1_o6), .led2(alu_1_o5), .led3(alu_1_o4), .led4(alu_1_o3), .led5(alu_1_o2),
    .led6(alu_1_o1), .led7(alu_1_o0));
  LED led_1 (.in(CF));
  register_4bit register_4bit_1 (
    .D0(alu_1_carry_flag), .D1(alu_1_sign_flag), .D2(alu_1_zero_flag), .D3(alu_1_overflow), .WRITE(or_5_out),
    .CLOCK(clock_1_out), .Q0(CF), .Q1(SF), .Q2(ZF), .Q3(OVF));
  LED led_2 (.in(SF));
  LED led_3 (.in(ZF));
  LED led_4 (.in(OVF));
  BUS_BUFFER bus_buffer_1 (
    .D0(alu_1_o0), .D1(alu_1_o1), .D2(alu_1_o2), .D3(alu_1_o3), .D4(alu_1_o4), .D5(alu_1_o5), .D6(alu_1_o6),
    .D7(alu_1_o7), .EN(not_2_out), .BUS0(O0), .BUS1(O1), .BUS2(O2), .BUS3(O3), .BUS4(O4), .BUS5(O5),
    .BUS6(O6), .BUS7(O7));
endmodule

module LEFT_HAND_SIDE_ALU (
  input  D0,
  input  D1,
  input  D2,
  input  D3,
  input  D4,
  input  D5,
  input  LD,
  input  D6,
  input  SHL,
  input  D7,
  input  RST,
  input  SHR,
  input  ROTL,
  input  ROTR,
  input  CP,
  output Q0,
  output Q1,
  output Q2,
  output Q3,
  output Q4,
  output Q5,
  output Q6,
  output Q7
);

  wire mux_74l258_1_q0, mux_74l258_1_q1, mux_74l258_1_q2, mux_74l258_1_q3, n7404_1_pin2, n7404_1_pin4,
       n7432_1_pin3, n7432_1_pin11, n7486_1_pin3, n7486_1_pin8, n7486_1_pin11, not_1_out;

  _7486 u_7486_1 (
    .pin1(ROTL), .pin2(ROTR), .pin3(n7486_1_pin3), .pin13(LD), .pin12(SHL), .pin11(n7486_1_pin11),
    .pin10(LD), .pin9(SHR), .pin8(n7486_1_pin8));  // open: pin4, pin5, pin6
  _7404 u_7404_1 (
    .pin1(ROTL), .pin2(n7404_1_pin2), .pin3(ROTR), .pin4(n7404_1_pin4));  // open: pin5, pin6, pin13, pin12, pin11, pin10, pin9, pin8
  _7432 u_7432_1 (
    .pin1(n7404_1_pin4), .pin2(n7486_1_pin8), .pin3(n7432_1_pin3), .pin13(n7486_1_pin11),
    .pin12(n7404_1_pin2), .pin11(n7432_1_pin11));  // open: pin4, pin5, pin6, pin10, pin9, pin8
  not not_1 (not_1_out, 1'b0);
  MUX_74L258 mux_74l258_1 (
    .A0(1'b0), .A1(1'b0), .A2(1'b0), .A3(1'b0), .B0(Q0), .B1(Q7), .B2(1'b0), .B3(1'b0), .SEL(n7486_1_pin3),
    .EN(not_1_out), .Q0(mux_74l258_1_q0), .Q1(mux_74l258_1_q1), .Q2(mux_74l258_1_q2), .Q3(mux_74l258_1_q3));
  // NoConnect on mux_74l258_1_q2
  // NoConnect on mux_74l258_1_q3
  ACCUMULATOR accumulator_1 (
    .SHR(mux_74l258_1_q0), .D0(D0), .D1(D1), .D2(D2), .D3(D3), .D4(D4), .D5(D5), .D6(D6), .D7(D7), .CLR(RST),
    .SHL(mux_74l258_1_q1), .S0(n7432_1_pin11), .S1(n7432_1_pin3), .CP(CP), .Q0(Q7), .Q1(Q6), .Q2(Q5),
    .Q3(Q4), .Q4(Q3), .Q5(Q2), .Q6(Q1), .Q7(Q0));
endmodule

module SHIFTER_74LS194 (
  input  SHR,
  input  SHL,
  input  A,
  input  B,
  input  C,
  input  D,
  input  S0,
  input  S1,
  input  CP,
  input  CLEAR,
  output QA,
  output QB,
  output QC,
  output QD
);

  wire and_1_out, and_2_out, and_3_out, and_4_out, and_5_out, and_6_out, and_7_out, and_8_out, and_9_out,
       and_10_out, and_11_out, and_12_out, and_13_out, nor_1_out, nor_2_out, nor_3_out, nor_4_out, nor_5_out,
       nor_6_out, not_1_out, not_2_out, not_3_out, not_4_out, not_5_out, not_6_out, not_7_out, not_8_out;

  not not_1 (not_1_out, S0);
  not not_2 (not_2_out, S1);
  nor nor_1 (nor_1_out, not_1_out, not_2_out);
  and and_1 (and_1_out, not_1_out, not_2_out);
  not not_3 (not_3_out, CP);
  and and_2 (and_2_out, SHR, not_2_out);
  nor nor_2 (nor_2_out, and_1_out, not_3_out);
  not not_4 (not_4_out, CLEAR);
  and and_3 (and_3_out, nor_1_out, A);
  nor nor_3 (nor_3_out, and_2_out, and_3_out, and_4_out);
  and and_4 (and_4_out, not_1_out, QB);
  S_R_Flip_Flop s_r_ff_1 (
    .S(not_5_out), .R(nor_3_out), .clk(nor_2_out), .Q(QA), .reset(not_4_out));  // open: Qn, preset
  not not_5 (not_5_out, nor_3_out);
  and and_5 (and_5_out, QA, not_2_out);
  and and_6 (and_6_out, nor_1_out, B);
  nor nor_4 (nor_4_out, and_5_out, and_6_out, and_7_out);
  and and_7 (and_7_out, not_1_out, QC);
  S_R_Flip_Flop s_r_ff_2 (
    .S(not_6_out), .R(nor_4_out), .clk(nor_2_out), .Q(QB), .reset(not_4_out));  // open: Qn, preset
  not not_6 (not_6_out, nor_4_out);
  and and_8 (and_8_out, QB, not_2_out);
  and and_9 (and_9_out, nor_1_out, C);
  nor nor_5 (nor_5_out, and_8_out, and_9_out, and_10_out);
  and and_10 (and_10_out, not_1_out, QD);
  S_R_Flip_Flop s_r_ff_3 (
    .S(not_7_out), .R(nor_5_out), .clk(nor_2_out), .Q(QC), .reset(not_4_out));  // open: Qn, preset
  not not_7 (not_7_out, nor_5_out);
  and and_11 (and_11_out, QC, not_2_out);
  and and_12 (and_12_out, nor_1_out, D);
  nor nor_6 (nor_6_out, and_11_out, and_12_out, and_13_out);
  and and_13 (and_13_out, not_1_out, SHL);
  S_R_Flip_Flop s_r_ff_4 (
    .S(not_8_out), .R(nor_6_out), .clk(nor_2_out), .Q(QD), .reset(not_4_out));  // open: Qn, preset
  not not_8 (not_8_out, nor_6_out);

  // Notes on the sheet:
  //   CLEAR: pull=up
  //   RESET
endmodule

module ACCUMULATOR (
  input  SHR,
  input  D0,
  input  D1,
  input  D2,
  input  D3,
  input  D4,
  input  D5,
  input  D6,
  input  D7,
  input  CLR,
  input  SHL,
  input  S0,
  input  S1,
  input  CP,
  output Q0,
  output Q1,
  output Q2,
  output Q3,
  output Q4,
  output Q5,
  output Q6,
  output Q7
);

  SHIFTER_74LS194 shifter_74ls194_1 (
    .SHR(SHR), .SHL(Q4), .A(D0), .B(D1), .C(D2), .D(D3), .S0(S0), .S1(S1), .CP(CP), .CLEAR(CLR), .QA(Q0),
    .QB(Q1), .QC(Q2), .QD(Q3));
  SHIFTER_74LS194 shifter_74ls194_2 (
    .SHR(Q3), .SHL(SHL), .A(D4), .B(D5), .C(D6), .D(D7), .S0(S0), .S1(S1), .CP(CP), .CLEAR(CLR), .QA(Q4),
    .QB(Q5), .QC(Q6), .QD(Q7));

  // Notes on the sheet:
  //   CLR: pull=up
endmodule

module MUX_74L258 (
  input  A0,
  input  A1,
  input  A2,
  input  A3,
  input  B0,
  input  B1,
  input  B2,
  input  B3,
  input  SEL,
  input  EN,
  output Q0,
  output Q1,
  output Q2,
  output Q3
);

  Multiplexer #(.enable("true")) multiplexer_1 (.in0(A0), .in1(B0), .out(Q0), .sel(SEL), .en(EN));
  Multiplexer #(.enable("true")) multiplexer_2 (.in0(A1), .in1(B1), .out(Q1), .sel(SEL), .en(EN));
  Multiplexer #(.enable("true")) multiplexer_3 (.in0(A2), .in1(B2), .out(Q2), .sel(SEL), .en(EN));
  Multiplexer #(.enable("true")) multiplexer_4 (.in0(A3), .in1(B3), .out(Q3), .sel(SEL), .en(EN));
endmodule

module ALU_74181 (
  input  B0,
  input  B1,
  input  B2,
  input  B3,
  input  Cn,
  input  Mode,
  input  A0,
  input  A1,
  input  A2,
  input  A3,
  input  S0,
  input  S1,
  input  S2,
  input  S3,
  output F0,
  output F1,
  output F2,
  output F3,
  output P,
  output Cn4,
  output G,
  output AeqB
);

  wire and_1_out, and_2_out, and_3_out, and_4_out, and_5_out, and_6_out, and_7_out, and_8_out, and_9_out,
       and_11_out, and_12_out, and_13_out, and_14_out, and_15_out, and_16_out, and_17_out, and_18_out,
       and_19_out, and_20_out, and_21_out, and_22_out, and_23_out, and_24_out, and_25_out, and_26_out,
       and_27_out, and_28_out, and_29_out, and_30_out, and_31_out, and_32_out, and_33_out, and_34_out,
       and_35_out, and_36_out, and_37_out, and_38_out, nand_1_out, nand_3_out, nor_1_out, nor_2_out,
       nor_3_out, nor_4_out, nor_5_out, nor_6_out, nor_7_out, nor_8_out, nor_9_out, nor_10_out, nor_11_out,
       not_1_out, not_2_out, not_3_out, not_4_out, not_5_out, not_6_out, not_7_out, not_8_out, not_9_out,
       not_10_out, not_11_out;

  nand nand_1 (nand_1_out, Cn, not_1_out);
  not not_1 (not_1_out, Mode);
  xor xor_1 (F0, nand_1_out, and_3_out);
  and and_1 (and_1_out, A0, A0);
  not not_2 (not_2_out, nor_1_out);
  and and_2 (and_2_out, B0, S0);
  nor nor_1 (nor_1_out, and_1_out, and_2_out, and_4_out);
  and and_3 (and_3_out, not_2_out, nor_3_out);
  not not_3 (not_3_out, B0);
  and and_4 (and_4_out, S1, not_3_out);
  and and_5 (and_5_out, not_1_out, nor_1_out);
  nor nor_2 (nor_2_out, and_5_out, and_7_out);
  and and_6 (and_6_out, not_3_out, S2, A0);
  nor nor_3 (nor_3_out, and_6_out, and_8_out);
  and and_7 (and_7_out, not_1_out, nor_3_out, Cn);
  xor xor_2 (F1, nor_2_out, and_9_out);
  and and_8 (and_8_out, A0, B0, S3);
  not not_4 (not_4_out, nor_4_out);
  and and_9 (and_9_out, not_4_out, nor_6_out);
  and and_10 (AeqB, F0, F1, F2, F3);
  and and_11 (and_11_out, A1, A1);
  and and_12 (and_12_out, not_1_out, nor_4_out);
  and and_13 (and_13_out, B1, S0);
  nor nor_4 (nor_4_out, and_11_out, and_13_out, and_15_out);
  and and_14 (and_14_out, not_1_out, nor_1_out, nor_6_out);
  nor nor_5 (nor_5_out, and_12_out, and_14_out, and_16_out);
  and and_15 (and_15_out, S1, not_5_out);
  and and_16 (and_16_out, not_1_out, Cn, nor_3_out, nor_6_out);
  xor xor_3 (F2, nor_5_out, and_19_out);
  not not_5 (not_5_out, B1);
  and and_17 (and_17_out, not_5_out, S2, A1);
  not not_6 (not_6_out, nor_8_out);
  and and_18 (and_18_out, A1, B1, S3);
  nor nor_6 (nor_6_out, and_17_out, and_18_out);
  and and_19 (and_19_out, not_6_out, nor_9_out);
  and and_20 (and_20_out, not_1_out, nor_8_out);
  and and_21 (and_21_out, A2, A2);
  and and_22 (and_22_out, not_1_out, nor_4_out, nor_9_out);
  nor nor_7 (nor_7_out, and_20_out, and_22_out, and_25_out, and_26_out);
  and and_23 (and_23_out, B2, S0);
  and and_24 (and_24_out, S1, not_7_out);
  nor nor_8 (nor_8_out, and_21_out, and_23_out, and_24_out);
  and and_25 (and_25_out, not_1_out, nor_1_out, nor_6_out, nor_9_out);
  xor xor_4 (F3, nor_7_out, and_28_out);
  not not_7 (not_7_out, B2);
  and and_26 (and_26_out, not_1_out, Cn, nor_3_out, nor_6_out, nor_9_out);
  and and_27 (and_27_out, not_7_out, S2, A2);
  nor nor_9 (nor_9_out, and_27_out, and_29_out);
  not not_8 (not_8_out, nor_10_out);
  and and_28 (and_28_out, not_8_out, nor_11_out);
  and and_29 (and_29_out, A2, B2, S3);
  and and_30 (and_30_out, A3, A3);
  nand nand_2 (P, nor_3_out, nor_6_out, nor_9_out, nor_11_out);
  and and_31 (and_31_out, B3, S0);
  nor nor_10 (nor_10_out, and_30_out, and_31_out, and_32_out);
  nand nand_3 (nand_3_out, Cn, nor_3_out, nor_6_out, nor_9_out, nor_11_out);
  not not_9 (not_9_out, nand_3_out);
  and and_32 (and_32_out, S1, not_11_out);
  not not_10 (not_10_out, G);
  or or_1 (Cn4, not_9_out, not_10_out);
  not not_11 (not_11_out, B3);
  and and_33 (and_33_out, not_11_out, S2, A3);
  and and_34 (and_34_out, nor_1_out, nor_6_out, nor_9_out, nor_11_out);
  and and_35 (and_35_out, A3, B3, S3);
  nor nor_11 (nor_11_out, and_33_out, and_35_out);
  and and_36 (and_36_out, nor_4_out, nor_9_out, nor_11_out);
  nor nor_12 (G, and_34_out, and_36_out, and_37_out, and_38_out);
  and and_37 (and_37_out, nor_8_out, nor_11_out);
  and and_38 (and_38_out, nor_10_out, nor_10_out);

  // Notes on the sheet:
  //   Cn: pull=down
  //   Mode: pull=down
endmodule

module ALU (
  input  S3,
  input  S2,
  input  S1,
  input  S0,
  input  MODE,
  input  CI,
  input  BUS7,
  input  BUS6,
  input  BUS5,
  input  BUS4,
  input  BUS3,
  input  BUS2,
  input  BUS1,
  input  BUS0,
  input  RESET,
  input  CLOCK,
  input  ROTL,
  input  ROTR,
  input  LDA,
  input  SHR,
  input  SHL,
  input  LDB,
  output O0,
  output O1,
  output O2,
  output O3,
  output O4,
  output O5,
  output O6,
  output O7,
  output CARRY_FLAG,
  output SIGN_FLAG,
  output ZERO_FLAG,
  output OVERFLOW
);

  wire alu_74181_1_cn4, alu_74181_2_cn4, left_hand_side_alu_1_q0, left_hand_side_alu_1_q1,
       left_hand_side_alu_1_q2, left_hand_side_alu_1_q3, left_hand_side_alu_1_q4, left_hand_side_alu_1_q5,
       left_hand_side_alu_1_q6, left_hand_side_alu_1_q7, not_1_out, xor_1_out, xor_2_out;
  wire [7:0] register_1_q;

  LedBar ledbar_1 (
    .led0(left_hand_side_alu_1_q0), .led1(left_hand_side_alu_1_q1), .led2(left_hand_side_alu_1_q2),
    .led3(left_hand_side_alu_1_q3), .led4(left_hand_side_alu_1_q4), .led5(left_hand_side_alu_1_q5),
    .led6(left_hand_side_alu_1_q6), .led7(left_hand_side_alu_1_q7));
  LEFT_HAND_SIDE_ALU left_hand_side_alu_1 (
    .D0(ROTL), .D1(ROTR), .D2(LDA), .D3(SHR), .D4(BUS0), .D5(SHL), .LD(BUS1), .D6(BUS2), .SHL(BUS3),
    .D7(BUS4), .RST(BUS5), .SHR(BUS6), .ROTL(BUS7), .ROTR(RESET), .CP(CLOCK), .Q0(left_hand_side_alu_1_q0),
    .Q1(left_hand_side_alu_1_q1), .Q2(left_hand_side_alu_1_q2), .Q3(left_hand_side_alu_1_q3),
    .Q4(left_hand_side_alu_1_q4), .Q5(left_hand_side_alu_1_q5), .Q6(left_hand_side_alu_1_q6),
    .Q7(left_hand_side_alu_1_q7));
  LedBar ledbar_2 (
    .led0(register_1_q[7]), .led1(register_1_q[6]), .led2(register_1_q[5]), .led3(register_1_q[4]),
    .led4(register_1_q[3]), .led5(register_1_q[2]), .led6(register_1_q[1]), .led7(register_1_q[0]));
  Register register_1 (
    .D({BUS7, BUS6, BUS5, BUS4, BUS3, BUS2, BUS1, BUS0}), .en(LDB), .clk(CLOCK), .Q(register_1_q),
    .clr(not_1_out));
  not not_1 (not_1_out, RESET);
  ALU_74181 alu_74181_1 (
    .B0(register_1_q[0]), .B1(register_1_q[1]), .B2(register_1_q[2]), .B3(register_1_q[3]), .Cn(CI),
    .Mode(MODE), .A0(left_hand_side_alu_1_q7), .A1(left_hand_side_alu_1_q6), .A2(left_hand_side_alu_1_q5),
    .A3(left_hand_side_alu_1_q4), .S0(S0), .S1(S1), .S2(S2), .S3(S3), .F0(O0), .F1(O1), .F2(O2), .F3(O3),
    .Cn4(alu_74181_1_cn4));  // open: P, G, AeqB
  ALU_74181 alu_74181_2 (
    .B0(register_1_q[4]), .B1(register_1_q[5]), .B2(register_1_q[6]), .B3(register_1_q[7]),
    .Cn(alu_74181_1_cn4), .Mode(MODE), .A0(left_hand_side_alu_1_q3), .A1(left_hand_side_alu_1_q2),
    .A2(left_hand_side_alu_1_q1), .A3(left_hand_side_alu_1_q0), .S0(S0), .S1(S1), .S2(S2), .S3(S3), .F0(O4),
    .F1(O5), .F2(O6), .F3(O7), .Cn4(alu_74181_2_cn4));  // open: P, G, AeqB
  LedBar ledbar_3 (.led0(O7), .led1(O6), .led2(O5), .led3(O4), .led4(O3), .led5(O2), .led6(O1), .led7(O0));
  xor xor_1 (xor_1_out, O7, register_1_q[7]);
  xor xor_2 (xor_2_out, O7, left_hand_side_alu_1_q0);
  not not_2 (CARRY_FLAG, alu_74181_2_cn4);
  and and_1 (OVERFLOW, xor_1_out, xor_2_out);
  nor nor_1 (ZERO_FLAG, O0, O1, O2, O3, O4, O5, O6, O7);

  assign SIGN_FLAG = O7;

  // Notes on the sheet:
  //   ROTL: pull=up
  //   ROTR: pull=up
  //   LDA: pull=up
  //   SHR: pull=up
  //   SHL: pull=up
  //   LDB: pull=down
endmodule

module register_4bit (
  input  D0,
  input  D1,
  input  D2,
  input  D3,
  input  WRITE,
  input  CLOCK,
  output Q0,
  output Q1,
  output Q2,
  output Q3
);

  Register #(.width(1)) register_1 (.D(D0), .en(WRITE), .clk(CLOCK), .Q(Q0), .clr(1'b0));
  Register #(.width(1)) register_2 (.D(D1), .en(WRITE), .clk(CLOCK), .Q(Q1), .clr(1'b0));
  Register #(.width(1)) register_3 (.D(D2), .en(WRITE), .clk(CLOCK), .Q(Q2), .clr(1'b0));
  Register #(.width(1)) register_4 (.D(D3), .en(WRITE), .clk(CLOCK), .Q(Q3), .clr(1'b0));
endmodule

module register_5bit (
  input  D0,
  input  D1,
  input  D2,
  input  D3,
  input  Carry_In,
  input  Write,
  input  Clock,
  output Func0,
  output Func1,
  output Func2,
  output Func3,
  output CarryInCn
);

  Register #(.width(1)) register_1 (.D(D0), .en(Write), .clk(Clock), .Q(Func0), .clr(1'b0));
  Register #(.width(1)) register_2 (.D(D1), .en(Write), .clk(Clock), .Q(Func1), .clr(1'b0));
  Register #(.width(1)) register_3 (.D(D2), .en(Write), .clk(Clock), .Q(Func2), .clr(1'b0));
  Register #(.width(1)) register_4 (.D(D3), .en(Write), .clk(Clock), .Q(Func3), .clr(1'b0));
  Register #(.width(1)) register_5 (.D(Carry_In), .en(Write), .clk(Clock), .Q(CarryInCn), .clr(1'b0));

  // Notes on the sheet:
  //   Func3: pull=down
  //   CarryInCn: pull=down
  //   Func0: pull=down
  //   Func1: pull=down
  //   Func2: pull=down
endmodule

module BUS_BUFFER (
  input  D0,
  input  D1,
  input  D2,
  input  D3,
  input  D4,
  input  D5,
  input  D6,
  input  D7,
  input  EN,
  output BUS0,
  output BUS1,
  output BUS2,
  output BUS3,
  output BUS4,
  output BUS5,
  output BUS6,
  output BUS7
);

  assign BUS0 = EN ? D0 : 1'bz;  // Controlled_Buffer controlled_buffer_1
  assign BUS1 = EN ? D1 : 1'bz;  // Controlled_Buffer controlled_buffer_2
  assign BUS2 = EN ? D2 : 1'bz;  // Controlled_Buffer controlled_buffer_3
  assign BUS3 = EN ? D3 : 1'bz;  // Controlled_Buffer controlled_buffer_4
  assign BUS4 = EN ? D4 : 1'bz;  // Controlled_Buffer controlled_buffer_5
  assign BUS5 = EN ? D5 : 1'bz;  // Controlled_Buffer controlled_buffer_6
  assign BUS6 = EN ? D6 : 1'bz;  // Controlled_Buffer controlled_buffer_7
  assign BUS7 = EN ? D7 : 1'bz;  // Controlled_Buffer controlled_buffer_8

  // Notes on the sheet:
  //   EN: pull=down
endmodule
