// Logisim project CPU.circ as structural Verilog: 11 circuits, main circuit TTL_74LS157
module main (
  input  Restore_Flags,
  input  Load_Operand
);

  wire clock_1_out, Operand_p1, Result_p2;
  wire [3:0] alu_module_1_cf;
  wire [7:0] alu_module_1_alu_out, undriven, undriven_2;

  // DipSwitch Control_Word: pin names not known
  Clock clock_1 (.out(clock_1_out));
  // DipSwitch Data_Bus: pin names not known
  ALU_Module alu_module_1 (
    .Data_Bus(undriven_2), .Flags_Restore(Restore_Flags), .LDB(Load_Operand),
    .Micocode_ControlWord(undriven), .Clock(clock_1_out), .SF(alu_module_1_cf[3]), .OVF(alu_module_1_cf[2]),
    .ZF(alu_module_1_cf[1]), .CF(alu_module_1_cf[0]), .ALU_Out(alu_module_1_alu_out));
  // LedBar #(.inputtype("row")) Accumulator: pin names not known; wires that end beside it: alu_module_1_alu_out
  // LedBar #(.inputtype("row")) Operand: pin names not known; wires that end beside it: Operand_p1
  // LedBar #(.inputtype("row")) Result: pin names not known; wires that end beside it: Operand_p1, Result_p2, Result_p2
  // LedBar #(.inputtype("row"), .matrixcols(4)) Flags: pin names not known; wires that end beside it: alu_module_1_cf

  // Notes on the sheet:
  //   Arithmetic
  //   0001_xxxx LDA
  //   0010_xxxx SHR
  //   0011_xxxx SHL
  //   0100_xxxx ROTR
  //   0101_xxxx ROTL
  //   0110_xxxx ADD
  //   1000_xxxx ADC
  //   1001_xxxx SBC
  //   1010_xxxx DEC A
  //   1011_xxxx INC A
  //   0111_0000 SUB/CMP
  //   Bitwise
  //   0000_1010 B
  //   0000_1110 OR
  //   0000_1100 ONES
  //   0000_0011 ZERO
  //   0000_0000 NOT A
  //   0000_0101 NOT B
  //   0000_1011 AND/TST
  //   0000_0100 NAND
  //   0000_0001 NOR
  //   0000_0110 XOR
  //   0000_1001 XNOR
  //   S|O|Z|C
endmodule

module TTL_74LS157 (
  input  A1,
  input  B1,
  input  A2,
  input  B2,
  input  A3,
  input  B3,
  input  A4,
  input  B4,
  input  Sel,
  input  En,
  output Y1,
  output Y2,
  output Y3,
  output Y4
);

  wire and_1_out, and_2_out, and_3_out, and_4_out, and_5_out, and_6_out, and_7_out, and_8_out, not_1_out,
       not_2_out, not_3_out;

  not not_1 (not_1_out, Sel);
  not not_2 (not_2_out, not_1_out);
  not not_3 (not_3_out, En);
  and and_1 (and_1_out, A1, not_1_out, not_3_out);
  and and_2 (and_2_out, B1, not_2_out, not_3_out);
  and and_3 (and_3_out, A2, not_1_out, not_3_out);
  and and_4 (and_4_out, B2, not_2_out, not_3_out);
  and and_5 (and_5_out, A3, not_1_out, not_3_out);
  and and_6 (and_6_out, B3, not_2_out, not_3_out);
  and and_7 (and_7_out, A4, not_1_out, not_3_out);
  and and_8 (and_8_out, B4, not_2_out, not_3_out);
  or or_1 (Y1, and_1_out, and_2_out);
  or or_2 (Y2, and_3_out, and_4_out);
  or or_3 (Y3, and_5_out, and_6_out);
  or or_4 (Y4, and_7_out, and_8_out);
endmodule

module TTL_74LS194 (
  input  SHL,
  input  SHR,
  input  A,
  input  B,
  input  C,
  input  D,
  input  S0,
  input  S1,
  input  CP,
  input  CLEAR,
  output QA,
  output QB,
  output QC,
  output QD
);

  wire and_1_out, and_2_out, and_3_out, and_4_out, and_5_out, and_6_out, and_7_out, and_8_out, and_9_out,
       and_10_out, and_11_out, and_12_out, and_13_out, nor_1_out, nor_2_out, nor_3_out, nor_4_out, nor_5_out,
       nor_6_out, not_1_out, not_2_out, not_3_out, not_4_out, not_5_out, not_6_out, not_7_out, not_8_out;

  not not_1 (not_1_out, S0);
  not not_2 (not_2_out, S1);
  not not_3 (not_3_out, CP);
  nor nor_1 (nor_1_out, not_1_out, not_2_out);
  and and_1 (and_1_out, not_1_out, not_2_out);
  and and_2 (and_2_out, SHL, not_2_out);
  nor nor_2 (nor_2_out, and_1_out, not_3_out);
  not not_4 (not_4_out, CLEAR);
  and and_3 (and_3_out, nor_1_out, A);
  nor nor_3 (nor_3_out, and_2_out, and_3_out, and_4_out);
  not not_5 (not_5_out, nor_3_out);
  and and_4 (and_4_out, not_1_out, QB);
  S_R_Flip_Flop s_r_ff_1 (
    .S(not_5_out), .R(nor_3_out), .clk(nor_2_out), .Q(QA), .reset(not_4_out));  // open: Qn, preset
  and and_5 (and_5_out, QA, not_2_out);
  and and_6 (and_6_out, nor_1_out, B);
  and and_7 (and_7_out, not_1_out, QC);
  nor nor_4 (nor_4_out, and_5_out, and_6_out, and_7_out);
  not not_6 (not_6_out, nor_4_out);
  S_R_Flip_Flop s_r_ff_2 (
    .S(not_6_out), .R(nor_4_out), .clk(nor_2_out), .Q(QB), .reset(not_4_out));  // open: Qn, preset
  and and_8 (and_8_out, QB, not_2_out);
  and and_9 (and_9_out, nor_1_out, C);
  and and_10 (and_10_out, not_1_out, QD);
  nor nor_5 (nor_5_out, and_8_out, and_9_out, and_10_out);
  not not_7 (not_7_out, nor_5_out);
  S_R_Flip_Flop s_r_ff_3 (
    .S(not_7_out), .R(nor_5_out), .clk(nor_2_out), .Q(QC), .reset(not_4_out));  // open: Qn, preset
  and and_11 (and_11_out, QC, not_2_out);
  and and_12 (and_12_out, nor_1_out, D);
  and and_13 (and_13_out, not_1_out, SHR);
  nor nor_6 (nor_6_out, and_11_out, and_12_out, and_13_out);
  not not_8 (not_8_out, nor_6_out);
  S_R_Flip_Flop s_r_ff_4 (
    .S(not_8_out), .R(nor_6_out), .clk(nor_2_out), .Q(QD), .reset(not_4_out));  // open: Qn, preset

  // Notes on the sheet:
  //   CLEAR: pull=up
  //   RESET
endmodule

module Accumulator (
  input  LDA,
  input  SHR,
  input  SHL,
  input  ROTR,
  input  ROTL,
  input  CLK,
  input  D7,
  input  D6,
  input  D5,
  input  D4,
  input  D3,
  input  D2,
  input  D1,
  input  D0,
  output Q7,
  output Q6,
  output Q5,
  output Q4,
  output Q3,
  output Q2,
  output Q1,
  output Q0,
  output Carry_Out
);

  wire not_1_out, not_2_out, or_1_out, or_2_out, or_3_out, ttl_74ls157_1_y1, ttl_74ls157_1_y2,
       ttl_74ls194_3_qa, ttl_74ls194_3_qd, xor_1_out, xor_2_out, xor_3_out, xor_4_out;

  xor xor_1 (xor_1_out, LDA, SHR);
  xor xor_2 (xor_2_out, LDA, SHL);
  xor xor_3 (xor_3_out, ROTR, ROTL);
  not not_1 (not_1_out, ROTR);
  not not_2 (not_2_out, ROTL);
  or or_1 (or_1_out, xor_1_out, not_1_out);
  or or_2 (or_2_out, xor_2_out, not_2_out);
  TTL_74LS157 ttl_74ls157_1 (
    .Y1(ttl_74ls157_1_y1), .Y2(ttl_74ls157_1_y2), .A1(1'b0), .B1(Q0), .A2(1'b0), .B2(Q7), .Sel(xor_3_out),
    .En(1'b0));  // open: Y3, Y4, A3, B3, A4, B4
  LedBar ledbar_1 (.led0(Q7), .led1(Q6), .led2(Q5), .led3(Q4), .led4(Q3), .led5(Q2), .led6(Q1), .led7(Q0));
  TTL_74LS194 ttl_74ls194_1 (
    .QA(Q0), .QB(Q1), .QC(Q2), .QD(Q3), .S0(or_2_out), .S1(or_1_out), .CP(CLK), .CLEAR(1'b1), .SHR(Q4),
    .SHL(ttl_74ls157_1_y2), .A(D0), .B(D1), .C(D2), .D(D3));
  TTL_74LS194 ttl_74ls194_2 (
    .QA(Q4), .QB(Q5), .QC(Q6), .QD(Q7), .S0(or_2_out), .S1(or_1_out), .CP(CLK), .CLEAR(1'b1),
    .SHR(ttl_74ls157_1_y1), .SHL(Q3), .A(D4), .B(D5), .C(D6), .D(D7));
  or or_3 (or_3_out, ttl_74ls194_3_qa, ttl_74ls194_3_qd);
  xor xor_4 (xor_4_out, or_1_out, or_2_out);
  TTL_74LS194 ttl_74ls194_3 (
    .QA(ttl_74ls194_3_qa), .QD(ttl_74ls194_3_qd), .S0(or_2_out), .S1(or_1_out), .CP(CLK), .CLEAR(1'b1),
    .SHR(Q0), .SHL(Q7), .A(1'b0), .B(1'b0), .C(1'b0), .D(1'b0));  // open: QB, QC
  and and_1 (Carry_Out, or_3_out, xor_4_out);
endmodule

module TTL_74LS374 (
  input  OE,
  input  CLK,
  input  D0,
  input  D1,
  input  D2,
  input  D3,
  input  D4,
  input  D5,
  input  D6,
  input  D7,
  output Q0,
  output Q1,
  output Q2,
  output Q3,
  output Q4,
  output Q5,
  output Q6,
  output Q7
);

  wire d_ff_1_qn, d_ff_2_qn, d_ff_3_qn, d_ff_4_qn, d_ff_5_qn, d_ff_6_qn, d_ff_7_qn, d_ff_8_qn, not_1_out,
       not_2_out;

  not not_1 (not_1_out, OE);
  not not_2 (not_2_out, CLK);
  D_Flip_Flop d_ff_1 (.D(D0), .clk(not_2_out), .Qn(d_ff_1_qn));  // open: Q, preset, reset
  D_Flip_Flop d_ff_2 (.D(D1), .clk(not_2_out), .Qn(d_ff_2_qn));  // open: Q, preset, reset
  D_Flip_Flop d_ff_3 (.D(D2), .clk(not_2_out), .Qn(d_ff_3_qn));  // open: Q, preset, reset
  D_Flip_Flop d_ff_4 (.D(D3), .clk(not_2_out), .Qn(d_ff_4_qn));  // open: Q, preset, reset
  D_Flip_Flop d_ff_5 (.D(D4), .clk(not_2_out), .Qn(d_ff_5_qn));  // open: Q, preset, reset
  D_Flip_Flop d_ff_6 (.D(D5), .clk(not_2_out), .Qn(d_ff_6_qn));  // open: Q, preset, reset
  D_Flip_Flop d_ff_7 (.D(D6), .clk(not_2_out), .Qn(d_ff_7_qn));  // open: Q, preset, reset
  D_Flip_Flop d_ff_8 (.D(D7), .clk(not_2_out), .Qn(d_ff_8_qn));  // open: Q, preset, reset
  assign Q0 = not_1_out ? ~d_ff_1_qn : 1'bz;  // Controlled_Inverter controlled_inverter_1
  assign Q1 = not_1_out ? ~d_ff_2_qn : 1'bz;  // Controlled_Inverter controlled_inverter_2
  assign Q2 = not_1_out ? ~d_ff_3_qn : 1'bz;  // Controlled_Inverter controlled_inverter_3
  assign Q3 = not_1_out ? ~d_ff_4_qn : 1'bz;  // Controlled_Inverter controlled_inverter_4
  assign Q4 = not_1_out ? ~d_ff_5_qn : 1'bz;  // Controlled_Inverter controlled_inverter_5
  assign Q5 = not_1_out ? ~d_ff_6_qn : 1'bz;  // Controlled_Inverter controlled_inverter_6
  assign Q6 = not_1_out ? ~d_ff_7_qn : 1'bz;  // Controlled_Inverter controlled_inverter_7
  assign Q7 = not_1_out ? ~d_ff_8_qn : 1'bz;  // Controlled_Inverter controlled_inverter_8
endmodule

module A_B_Register_Modules (
  input  LDA,
  input  SHR,
  input  SHL,
  input  ROTR,
  input  ROTL,
  input  CLK,
  input  [7:0] BUS0,
  input  LDB,
  output [7:0] A_Data,
  output [7:0] B_Data,
  output Logical_Carry_Out
);

  wire and_1_out, not_1_out;

  not not_1 (not_1_out, LDB);
  and and_1 (and_1_out, CLK, not_1_out);
  Accumulator accumulator_1 (
    .LDA(LDA), .SHR(SHR), .SHL(SHL), .ROTR(ROTR), .ROTL(ROTL), .CLK(CLK), .D7(BUS0[7]), .D6(BUS0[6]),
    .D5(BUS0[5]), .D4(BUS0[4]), .D3(BUS0[3]), .D2(BUS0[2]), .D1(BUS0[1]), .D0(BUS0[0]), .Q7(A_Data[7]),
    .Q6(A_Data[6]), .Q5(A_Data[5]), .Q4(A_Data[4]), .Q3(A_Data[3]), .Q2(A_Data[2]), .Q1(A_Data[1]),
    .Q0(A_Data[0]), .Carry_Out(Logical_Carry_Out));
  TTL_74LS374 ttl_74ls374_1 (
    .Q0(B_Data[0]), .Q1(B_Data[1]), .Q2(B_Data[2]), .Q3(B_Data[3]), .Q4(B_Data[4]), .Q5(B_Data[5]),
    .Q6(B_Data[6]), .Q7(B_Data[7]), .OE(1'b0), .CLK(and_1_out), .D0(BUS0[0]), .D1(BUS0[1]), .D2(BUS0[2]),
    .D3(BUS0[3]), .D4(BUS0[4]), .D5(BUS0[5]), .D6(BUS0[6]), .D7(BUS0[7]));
endmodule

module TTL_74LS181 (
  input  B0,
  input  B1,
  input  B2,
  input  B3,
  input  Cn,
  input  Mode,
  input  A0,
  input  A1,
  input  A2,
  input  A3,
  input  S0,
  input  S1,
  input  S2,
  input  S3,
  output F0,
  output F1,
  output F2,
  output F3,
  output P,
  output Cn4,
  output G,
  output AeqB
);

  wire and_1_out, and_2_out, and_3_out, and_4_out, and_5_out, and_6_out, and_7_out, and_8_out, and_9_out,
       and_11_out, and_12_out, and_13_out, and_14_out, and_15_out, and_16_out, and_17_out, and_18_out,
       and_19_out, and_20_out, and_21_out, and_22_out, and_23_out, and_24_out, and_25_out, and_26_out,
       and_27_out, and_28_out, and_29_out, and_30_out, and_31_out, and_32_out, and_33_out, and_34_out,
       and_35_out, and_36_out, and_37_out, and_38_out, nand_1_out, nand_3_out, nor_1_out, nor_2_out,
       nor_3_out, nor_4_out, nor_5_out, nor_6_out, nor_7_out, nor_8_out, nor_9_out, nor_10_out, nor_11_out,
       not_1_out, not_2_out, not_3_out, not_4_out, not_5_out, not_6_out, not_7_out, not_8_out, not_9_out,
       not_10_out, not_11_out;

  nand nand_1 (nand_1_out, Cn, not_1_out);
  not not_1 (not_1_out, Mode);
  xor xor_1 (F0, nand_1_out, and_3_out);
  and and_1 (and_1_out, A0, A0);
  not not_2 (not_2_out, nor_1_out);
  and and_2 (and_2_out, B0, S0);
  nor nor_1 (nor_1_out, and_1_out, and_2_out, and_4_out);
  and and_3 (and_3_out, not_2_out, nor_3_out);
  not not_3 (not_3_out, B0);
  and and_4 (and_4_out, S1, not_3_out);
  and and_5 (and_5_out, not_1_out, nor_1_out);
  nor nor_2 (nor_2_out, and_5_out, and_7_out);
  and and_6 (and_6_out, not_3_out, S2, A0);
  nor nor_3 (nor_3_out, and_6_out, and_8_out);
  and and_7 (and_7_out, not_1_out, nor_3_out, Cn);
  xor xor_2 (F1, nor_2_out, and_9_out);
  and and_8 (and_8_out, A0, B0, S3);
  not not_4 (not_4_out, nor_4_out);
  and and_9 (and_9_out, not_4_out, nor_6_out);
  and and_10 (AeqB, F0, F1, F2, F3);
  and and_11 (and_11_out, A1, A1);
  and and_12 (and_12_out, not_1_out, nor_4_out);
  and and_13 (and_13_out, B1, S0);
  nor nor_4 (nor_4_out, and_11_out, and_13_out, and_15_out);
  and and_14 (and_14_out, not_1_out, nor_1_out, nor_6_out);
  nor nor_5 (nor_5_out, and_12_out, and_14_out, and_16_out);
  and and_15 (and_15_out, S1, not_5_out);
  and and_16 (and_16_out, not_1_out, Cn, nor_3_out, nor_6_out);
  xor xor_3 (F2, nor_5_out, and_19_out);
  not not_5 (not_5_out, B1);
  and and_17 (and_17_out, not_5_out, S2, A1);
  not not_6 (not_6_out, nor_8_out);
  and and_18 (and_18_out, A1, B1, S3);
  nor nor_6 (nor_6_out, and_17_out, and_18_out);
  and and_19 (and_19_out, not_6_out, nor_9_out);
  and and_20 (and_20_out, not_1_out, nor_8_out);
  and and_21 (and_21_out, A2, A2);
  and and_22 (and_22_out, not_1_out, nor_4_out, nor_9_out);
  nor nor_7 (nor_7_out, and_20_out, and_22_out, and_25_out, and_26_out);
  and and_23 (and_23_out, B2, S0);
  and and_24 (and_24_out, S1, not_7_out);
  nor nor_8 (nor_8_out, and_21_out, and_23_out, and_24_out);
  and and_25 (and_25_out, not_1_out, nor_1_out, nor_6_out, nor_9_out);
  xor xor_4 (F3, nor_7_out, and_28_out);
  not not_7 (not_7_out, B2);
  and and_26 (and_26_out, not_1_out, Cn, nor_3_out, nor_6_out, nor_9_out);
  and and_27 (and_27_out, not_7_out, S2, A2);
  nor nor_9 (nor_9_out, and_27_out, and_29_out);
  not not_8 (not_8_out, nor_10_out);
  and and_28 (and_28_out, not_8_out, nor_11_out);
  and and_29 (and_29_out, A2, B2, S3);
  and and_30 (and_30_out, A3, A3);
  nand nand_2 (P, nor_3_out, nor_6_out, nor_9_out, nor_11_out);
  and and_31 (and_31_out, B3, S0);
  nor nor_10 (nor_10_out, and_30_out, and_31_out, and_32_out);
  nand nand_3 (nand_3_out, Cn, nor_3_out, nor_6_out, nor_9_out, nor_11_out);
  not not_9 (not_9_out, nand_3_out);
  and and_32 (and_32_out, S1, not_11_out);
  not not_10 (not_10_out, G);
  or or_1 (Cn4, not_9_out, not_10_out);
  not not_11 (not_11_out, B3);
  and and_33 (and_33_out, not_11_out, S2, A3);
  and and_34 (and_34_out, nor_1_out, nor_6_out, nor_9_out, nor_11_out);
  and and_35 (and_35_out, A3, B3, S3);
  nor nor_11 (nor_11_out, and_33_out, and_35_out);
  and and_36 (and_36_out, nor_4_out, nor_9_out, nor_11_out);
  nor nor_12 (G, and_34_out, and_36_out, and_37_out, and_38_out);
  and and_37 (and_37_out, nor_8_out, nor_11_out);
  and and_38 (and_38_out, nor_10_out, nor_10_out);

  // Notes on the sheet:
  //   Cn: pull=down
  //   Mode: pull=down
endmodule

module ALU (
  input  [7:0] A_data,
  input  [7:0] B_Data,
  input  Mode,
  input  [3:0] ALU_Func,
  input  Cn,
  output [7:0] ALU_Result,
  output Cn4
);

  wire ttl_74ls181_2_cn4;

  TTL_74LS181 ttl_74ls181_1 (
    .F2(ALU_Result[6]), .F3(ALU_Result[7]), .Cn4(Cn4), .F0(ALU_Result[4]), .F1(ALU_Result[5]),
    .B1(B_Data[5]), .A2(A_data[6]), .B2(B_Data[6]), .A3(A_data[7]), .B3(B_Data[7]), .S0(ALU_Func[0]),
    .S1(ALU_Func[1]), .S2(ALU_Func[2]), .S3(ALU_Func[3]), .Cn(ttl_74ls181_2_cn4), .Mode(Mode),
    .A0(A_data[4]), .B0(B_Data[4]), .A1(A_data[5]));  // open: P, G, AeqB
  TTL_74LS181 ttl_74ls181_2 (
    .F2(ALU_Result[2]), .F3(ALU_Result[3]), .Cn4(ttl_74ls181_2_cn4), .F0(ALU_Result[0]), .F1(ALU_Result[1]),
    .B1(B_Data[1]), .A2(A_data[2]), .B2(B_Data[2]), .A3(A_data[3]), .B3(B_Data[3]), .S0(ALU_Func[0]),
    .S1(ALU_Func[1]), .S2(ALU_Func[2]), .S3(ALU_Func[3]), .Cn(Cn), .Mode(Mode), .A0(A_data[0]),
    .B0(B_Data[0]), .A1(A_data[1]));  // open: P, G, AeqB
  LedBar ledbar_1 (
    .led0(ALU_Result[7]), .led1(ALU_Result[6]), .led2(ALU_Result[5]), .led3(ALU_Result[4]),
    .led4(ALU_Result[3]), .led5(ALU_Result[2]), .led6(ALU_Result[1]), .led7(ALU_Result[0]));

  // Notes on the sheet:
  //   ADDITION
  //   CI: active low
  //   CO: Active Low
  //   SUBTRACTION
  //   CI: active High
  //   CO: Active High
  //   DO SAME FOR CARRY IN
  //   BITWISE
  //   CF: 0
  //   or ~Mode
endmodule

module Flags_Register (
  input  Clock,
  input  Enable_Latch,
  input  Restore_flags,
  input  [3:0] BUS_LSB_Nibble,
  input  [7:0] A_Data,
  input  [7:0] B_Data,
  input  [7:0] Result_Data,
  input  Carry,
  output SF,
  output OVF,
  output ZF,
  output CF
);

  wire and_1_out, and_2_out, nor_1_out, not_1_out, not_2_out, or_1_out, ttl_74ls157_1_y1, ttl_74ls157_1_y2,
       ttl_74ls157_1_y3, ttl_74ls157_1_y4, ttl_74ls374_1_q4, ttl_74ls374_1_q5, ttl_74ls374_1_q6,
       ttl_74ls374_1_q7, xor_1_out, xor_2_out;

  not not_1 (not_1_out, Enable_Latch);
  not not_2 (not_2_out, Restore_flags);
  xor xor_1 (xor_1_out, Result_Data[7], B_Data[7]);
  xor xor_2 (xor_2_out, Result_Data[7], A_Data[7]);
  and and_1 (and_1_out, xor_1_out, xor_2_out);
  nor nor_1 (nor_1_out, Result_Data[7], Result_Data[6], Result_Data[5], Result_Data[4], Result_Data[3], Result_Data[2], Result_Data[1], Result_Data[0]);
  or or_1 (or_1_out, not_1_out, not_2_out);
  TTL_74LS157 ttl_74ls157_1 (
    .Y1(ttl_74ls157_1_y1), .Y2(ttl_74ls157_1_y2), .Y3(ttl_74ls157_1_y3), .Y4(ttl_74ls157_1_y4), .A1(Carry),
    .B1(BUS_LSB_Nibble[0]), .A2(and_1_out), .B2(BUS_LSB_Nibble[2]), .A3(nor_1_out), .B3(BUS_LSB_Nibble[1]),
    .A4(Result_Data[7]), .B4(BUS_LSB_Nibble[3]), .Sel(not_2_out), .En(1'b0));
  and and_2 (and_2_out, Clock, or_1_out);
  // NoConnect on ttl_74ls374_1_q7
  // NoConnect on ttl_74ls374_1_q6
  // NoConnect on ttl_74ls374_1_q5
  // NoConnect on ttl_74ls374_1_q4
  TTL_74LS374 ttl_74ls374_1 (
    .Q0(CF), .Q1(ZF), .Q2(OVF), .Q3(SF), .Q4(ttl_74ls374_1_q4), .Q5(ttl_74ls374_1_q5), .Q6(ttl_74ls374_1_q6),
    .Q7(ttl_74ls374_1_q7), .OE(1'b0), .CLK(and_2_out), .D0(ttl_74ls157_1_y1), .D1(ttl_74ls157_1_y3),
    .D2(ttl_74ls157_1_y2), .D3(ttl_74ls157_1_y4), .D4(1'b0), .D5(1'b0), .D6(1'b0), .D7(1'b0));
endmodule

module ALU_Controller_Alt (
  input  [7:0] EEPROM_ControlWord,
  input  Carry_Flag,
  output ALU_Func_3,
  output ALU_Func_2,
  output ALU_Func_1,
  output ALU_Func_0,
  output ALU_Mode,
  output ALU_Carry_in
);

  LED led_1 ();  // open: in
  LED led_2 ();  // open: in
  LED led_3 ();  // open: in
  LED led_4 ();  // open: in
  LED led_5 ();  // open: in
  LED led_6 ();  // open: in
endmodule

module ALU_Module (
  input  [7:0] Data_Bus,
  input  Flags_Restore,
  input  LDB,
  input  [7:0] Micocode_ControlWord,
  input  Clock,
  output SF,
  output OVF,
  output ZF,
  output CF,
  output [7:0] ALU_Out
);

  wire a_b_register_modules_1_logical_carry_out;
  wire [7:0] a_b_register_modules_1_a_data, a_b_register_modules_1_b_data, A_p2;

  ALU_Controller_Alt alu_controller_alt_1 ();  // open: EEPROM_ControlWord, Carry_Flag, ALU_Func_3, ALU_Func_2, ALU_Func_1, ALU_Func_0, ALU_Mode, ALU_Carry_in
  LED led_1 (.in(SF));
  A_B_Register_Modules a_b_register_modules_1 (
    .A_Data(a_b_register_modules_1_a_data), .B_Data(a_b_register_modules_1_b_data),
    .Logical_Carry_Out(a_b_register_modules_1_logical_carry_out));  // open: LDA, SHR, SHL, ROTR, ROTL, CLK, BUS0, LDB
  LED led_2 (.in(OVF));
  // LedBar #(.inputtype("row")) A: pin names not known; wires that end beside it: a_b_register_modules_1_a_data, A_p2
  // LedBar #(.inputtype("row")) B: pin names not known; wires that end beside it: a_b_register_modules_1_b_data
  LED led_3 (.in(ZF));
  ALU alu_1 (.ALU_Result(A_p2));  // open: A_data, B_Data, Mode, ALU_Func, Cn, Cn4
  LED led_4 (.in(a_b_register_modules_1_logical_carry_out));
  Flags_Register flags_register_1 ();  // open: Clock, Enable_Latch, Restore_flags, BUS_LSB_Nibble, A_Data, B_Data, Result_Data, Carry, SF, OVF, ZF, CF
  LED led_5 (.in(CF));
endmodule
