// Logisim project ControlUnit.circ as structural Verilog: 14 circuits, main circuit main
module main (
);

  wire button_1_out, clock_1_out, combinedcontrol_1_latch_a, combinedcontrol_1_latch_b,
       combinedcontrol_1_latch_inst_reg, JCC_JP_EN_out, opcodedisplay_1_clear, opcodedisplay_1_clk,
       opcodedisplay_1_we, switch_1_p2;
  wire [2:0] combinedcontrol_1_flags_out, combinedcontrol_1_io_request, combinedcontrol_1_mem_request;
  wire [3:0] combinedcontrol_1_irq_handler_en, combinedcontrol_1_jcc_0_3, combinedcontrol_1_latch_pc,
       combinedcontrol_1_sp_out, ledbar_3_p1, ledbar_4_p1;
  wire [5:0] combinedcontrol_1_alu_0_5;
  wire [6:0] combinedcontrol_1_gpr, opcodedisplay_1_data;
  wire [7:0] dipswitch_3_sw6, dipswitch_4_sw6, multiplexer_1_out, multiplexer_2_out, OPCODE_sw8,
       opcodedisplay_1_opcode_out, rom_1_data, rom_2_data;
  wire [11:0] combinedcontrol_1_latch_mar, ledbar_5_p1;

  Clock clock_1 (.out(clock_1_out));
  LED led_1 (.in(switch_1_p2));
  // Switch switch_1: pin names not known; wires that end beside it: 1'b1, switch_1_p2
  DipSwitch OPCODE (
    .sw1(OPCODE_sw8[7]), .sw2(OPCODE_sw8[6]), .sw3(OPCODE_sw8[5]), .sw4(OPCODE_sw8[4]), .sw5(OPCODE_sw8[3]),
    .sw6(OPCODE_sw8[2]), .sw7(OPCODE_sw8[1]), .sw8(OPCODE_sw8[0]));
  LED led_2 (.in(switch_1_p2));
  DipSwitch #(.number(2)) dipswitch_1 (.sw1(dipswitch_3_sw6[7]), .sw2(dipswitch_3_sw6[6]));
  Pull_Resistor pull_resistor_1 (.node(switch_1_p2));
  DipSwitch #(.number(2)) dipswitch_2 (.sw1(dipswitch_4_sw6[7]), .sw2(dipswitch_4_sw6[6]));
  Hex_Digit_Display hex_digit_display_1 (.value(OPCODE_sw8[7:4]));  // open: dp
  Hex_Digit_Display hex_digit_display_2 (.value(OPCODE_sw8[3:0]));  // open: dp
  Hex_Digit_Display hex_digit_display_3 (.value(dipswitch_3_sw6[7:4]));  // open: dp
  Hex_Digit_Display hex_digit_display_4 (.value(dipswitch_3_sw6[3:0]));  // open: dp
  DipSwitch #(.number(6)) dipswitch_3 (
    .sw1(dipswitch_3_sw6[5]), .sw2(dipswitch_3_sw6[4]), .sw3(dipswitch_3_sw6[3]), .sw4(dipswitch_3_sw6[2]),
    .sw5(dipswitch_3_sw6[1]), .sw6(dipswitch_3_sw6[0]));
  Hex_Digit_Display hex_digit_display_5 (.value(dipswitch_4_sw6[7:4]));  // open: dp
  Hex_Digit_Display hex_digit_display_6 (.value(dipswitch_4_sw6[3:0]));  // open: dp
  DipSwitch #(.number(6)) dipswitch_4 (
    .sw1(dipswitch_4_sw6[5]), .sw2(dipswitch_4_sw6[4]), .sw3(dipswitch_4_sw6[3]), .sw4(dipswitch_4_sw6[2]),
    .sw5(dipswitch_4_sw6[1]), .sw6(dipswitch_4_sw6[0]));
  Button button_1 (.out(button_1_out));
  OpcodeDisplay opcodedisplay_1 (
    .OPCODE_IN(OPCODE_sw8), .LATCH_OPCODE(button_1_out), .CLK_IN(clock_1_out),
    .OPCODE_OUT(opcodedisplay_1_opcode_out), .DATA(opcodedisplay_1_data), .WE(opcodedisplay_1_we),
    .CLEAR(opcodedisplay_1_clear), .CLK(opcodedisplay_1_clk));
  Counter4Bit counter4bit_1 (.CLK(clock_1_out), .Reset(1'b1));  // open: EndFlag, STEP, StartFlag
  TTY #(.rows(2)) tty_1 (
    .data(opcodedisplay_1_data), .clk(opcodedisplay_1_clk), .we(opcodedisplay_1_we),
    .clr(opcodedisplay_1_clear));
  ROM #(.addrWidth(12)) rom_1 (.addr({opcodedisplay_1_opcode_out, ledbar_3_p1}), .data(rom_1_data));
  ROM #(.addrWidth(12)) rom_2 (.addr({opcodedisplay_1_opcode_out, ledbar_3_p1}), .data(rom_2_data));
  LED led_3 (.in(multiplexer_2_out[7]));
  LED led_4 (.in(combinedcontrol_1_latch_inst_reg));
  // LedBar #(.inputtype("row")) ledbar_1: pin names not known; wires that end beside it: rom_1_data
  // LedBar #(.inputtype("row")) ledbar_2: pin names not known; wires that end beside it: rom_2_data
  LED led_5 (.in(combinedcontrol_1_gpr[4]));
  LED led_6 (.in(combinedcontrol_1_gpr[3]));
  LED led_7 (.in(combinedcontrol_1_gpr[6]));
  LED led_8 (.in(combinedcontrol_1_gpr[5]));
  // LedBar #(.inputtype("row"), .matrixcols(4)) ledbar_3: pin names not known; wires that end beside it: ledbar_3_p1
  OpCounter opcounter_1 (.Reset(multiplexer_2_out[7]), .Clock(clock_1_out), .Step(ledbar_3_p1));
  LED led_9 (.in(combinedcontrol_1_gpr[2]));
  LED led_10 (.in(combinedcontrol_1_gpr[1]));
  LED led_11 (.in(combinedcontrol_1_gpr[0]));
  LED led_12 (.in(combinedcontrol_1_latch_a));
  Hex_Digit_Display hex_digit_display_7 (.value(opcodedisplay_1_opcode_out[7:4]));  // open: dp
  LED led_13 (.in(combinedcontrol_1_latch_b));
  LED led_14 (.in(combinedcontrol_1_alu_0_5[5]));
  LED led_15 (.in(combinedcontrol_1_alu_0_5[4]));
  LED led_16 (.in(combinedcontrol_1_alu_0_5[3]));
  Button #(.press("passive")) JCC_JP_EN (.out(JCC_JP_EN_out));
  // NoConnect on multiplexer_1_out[6]
  not not_1 (combinedcontrol_1_latch_pc[3], multiplexer_1_out[7]);
  Multiplexer #(.width(8)) multiplexer_1 (
    .in0(rom_1_data), .in1(dipswitch_3_sw6), .out(multiplexer_1_out), .sel(switch_1_p2));
  // NoConnect on multiplexer_2_out[6]
  Multiplexer #(.width(8)) multiplexer_2 (
    .in0(rom_2_data), .in1(dipswitch_4_sw6), .out(multiplexer_2_out), .sel(switch_1_p2));
  LED led_17 (.in(combinedcontrol_1_latch_mar[11]));
  Hex_Digit_Display hex_digit_display_8 (.value(opcodedisplay_1_opcode_out[3:0]));  // open: dp
  LED led_18 (.in(combinedcontrol_1_alu_0_5[2]));
  LED led_19 (.in(combinedcontrol_1_alu_0_5[1]));
  LED led_20 (.in(combinedcontrol_1_alu_0_5[0]));
  Pull_Resistor #(.pull(1)) pull_resistor_2 (.node(JCC_JP_EN_out));
  LED led_21 (.in(combinedcontrol_1_latch_mar[10]));
  LED led_22 (.in(combinedcontrol_1_latch_mar[9]));
  LED led_23 (.in(combinedcontrol_1_latch_mar[8]));
  LED led_24 (.in(combinedcontrol_1_latch_mar[7]));
  LED led_25 (.in(combinedcontrol_1_flags_out[2]));
  LED led_26 (.in(combinedcontrol_1_flags_out[1]));
  LED led_27 (.in(combinedcontrol_1_flags_out[0]));
  LED led_28 (.in(combinedcontrol_1_jcc_0_3[3]));
  // LedBar #(.inputtype("row"), .matrixcols(4)) ledbar_4: pin names not known; wires that end beside it: ledbar_4_p1
  // LedBar #(.inputtype("row"), .matrixcols(12)) ledbar_5: pin names not known; wires that end beside it: ledbar_5_p1
  LED led_29 (.in(combinedcontrol_1_latch_mar[6]));
  LED led_30 (.in(combinedcontrol_1_latch_mar[5]));
  LED led_31 (.in(combinedcontrol_1_latch_mar[4]));
  LED led_32 (.in(combinedcontrol_1_latch_mar[3]));
  LED led_33 (.in(combinedcontrol_1_jcc_0_3[2]));
  LED led_34 (.in(combinedcontrol_1_jcc_0_3[1]));
  LED led_35 (.in(combinedcontrol_1_jcc_0_3[0]));
  CombinedControl combinedcontrol_1 (
    .EXTRA_READ(ledbar_4_p1), .USE_DATA_SEGMENT(combinedcontrol_1_latch_mar[7]),
    .MEM_OUT(combinedcontrol_1_latch_mar[1]), .CODE_SEG_OUT(combinedcontrol_1_latch_mar[11]),
    .DATA_SEG_OUT(combinedcontrol_1_latch_mar[8]), .STACK_SEG_OUT(combinedcontrol_1_latch_mar[5]),
    .IRQ_HANDLER_EN(combinedcontrol_1_irq_handler_en[0]), .IRQ_READ(combinedcontrol_1_irq_handler_en[3]),
    .PC_OUT(combinedcontrol_1_latch_pc[2]), .SP_OUT(combinedcontrol_1_sp_out[0]),
    .FLAGS_OUT(combinedcontrol_1_flags_out[0]), .ALU_0_5(combinedcontrol_1_alu_0_5),
    .LATCH_A(combinedcontrol_1_latch_a), .LATCH_B(combinedcontrol_1_latch_b),
    .IRQ_REG_SEL(combinedcontrol_1_irq_handler_en[2]), .IRQ_WRITE(combinedcontrol_1_irq_handler_en[1]),
    .WRITE_MEM(combinedcontrol_1_latch_mar[2]), .RESTORE_FLAGS(combinedcontrol_1_flags_out[1]),
    .LATCH_FLAGS(combinedcontrol_1_flags_out[2]), .LATCH_MAR(combinedcontrol_1_latch_mar[0]),
    .LATCH_STACK_SEG(combinedcontrol_1_latch_mar[3]), .LATCH_CODE_SEF(combinedcontrol_1_latch_mar[9]),
    .LATCH_DATA_SEG(combinedcontrol_1_latch_mar[6]), .LATCH_INST_REG(combinedcontrol_1_latch_inst_reg),
    .DEC_PC(combinedcontrol_1_latch_pc[1]), .INC_SP(combinedcontrol_1_sp_out[2]),
    .DEC_SP(combinedcontrol_1_sp_out[3]), .LATCH_PC(combinedcontrol_1_latch_pc[0]),
    .LATCH_SP(combinedcontrol_1_sp_out[1]), .EXTRA_WRITE(ledbar_5_p1), .JCC_0_3(combinedcontrol_1_jcc_0_3),
    .GPR(combinedcontrol_1_gpr), .USE_CODE_SEGMENT(combinedcontrol_1_latch_mar[10]),
    .USE_STACK_SEGMENT(combinedcontrol_1_latch_mar[4]), .MEM_REQUEST(combinedcontrol_1_mem_request[0]),
    .MEM_READ(combinedcontrol_1_mem_request[1]), .MEM_WRITE(combinedcontrol_1_mem_request[2]),
    .IO_REQUEST(combinedcontrol_1_io_request[0]), .IO_READ(combinedcontrol_1_io_request[1]),
    .IO_WRITE(combinedcontrol_1_io_request[2]), .JCC_COND_PCI(JCC_JP_EN_out),
    .EEPROM0(multiplexer_1_out[5:0]), .EEPROM1(multiplexer_2_out[5:0]));
  LED led_36 (.in(combinedcontrol_1_latch_mar[2]));
  LED led_37 (.in(combinedcontrol_1_latch_mar[1]));
  LED led_38 (.in(combinedcontrol_1_latch_mar[0]));
  LED led_39 (.in(combinedcontrol_1_latch_pc[3]));
  LED led_40 (.in(combinedcontrol_1_latch_pc[2]));
  LED led_41 (.in(combinedcontrol_1_latch_pc[1]));
  LED led_42 (.in(combinedcontrol_1_latch_pc[0]));
  LED led_43 (.in(combinedcontrol_1_sp_out[3]));
  LED led_44 (.in(combinedcontrol_1_sp_out[2]));
  LED led_45 (.in(combinedcontrol_1_sp_out[1]));
  LED led_46 (.in(combinedcontrol_1_sp_out[0]));
  LED led_47 (.in(combinedcontrol_1_irq_handler_en[3]));
  LED led_48 (.in(combinedcontrol_1_irq_handler_en[2]));
  LED led_49 (.in(combinedcontrol_1_irq_handler_en[1]));
  LED led_50 (.in(combinedcontrol_1_irq_handler_en[0]));
  LED led_51 (.in(combinedcontrol_1_io_request[2]));
  LED led_52 (.in(combinedcontrol_1_io_request[1]));
  LED led_53 (.in(combinedcontrol_1_io_request[0]));
  LED led_54 (.in(combinedcontrol_1_mem_request[2]));
  LED led_55 (.in(combinedcontrol_1_mem_request[1]));
  LED led_56 (.in(combinedcontrol_1_mem_request[0]));

  // Notes on the sheet:
  //   Manual
  //   Auto
  //   Inc PC
  //   ResetOp
  //   WRITES
  //   READS
  //   Latch
  //   contents of rom_1 (hex, n*v repeats v):
  //   99 20 90 12*80 0 16*80 240*0 99 20 90
  //   contents of rom_2 (hex, n*v repeats v):
  //   96 90 1 29*80 224*0 96 90 1 13*0 96 90 2
  //   CPU
  //   Rst Op
  //   Inst In
  //   CURRENT INSTRUCTION
  //   MICROCODE
  //   GPR
  //   Read
  //   Write
  //   Ai
  //   ALU
  //   Bi
  //   En
  //   Inv
  //   f3
  //   CSo
  //   CSu
  //   f2
  //   f1
  //   In
  //   f0
  //   CSi
  //   DSo
  //   DSu
  //   DSi
  //   Flags
  //   Res
  //   Out
  //   Memory
  //   SSo
  //   SSu
  //   SSi
  //   Wr
  //   JCC
  //   Inc
  //   Function
  //   INSTRUCTION
  //   DECODE UNIT
  //   Extra Read Control Lines
  //   Extra Write Control Lines
  //   Oe
  //   MARi
  //   PC
  //   Out
  //   Dec
  //   In
  //   SP
  //   Dec
  //   Inc
  //   In
  //   Out
  //   IRQ
  //   Rd
  //   Sel
  //   Wr
  //   IO
  //   En
  //   Wr
  //   Rd
  //   IoRq
  //   Mem Cart
  //   Wr
  //   Rd
  //   MRq
endmodule

module WriteGroup0 (
  input  [2:0] A0_A2,
  input  Enable,
  output [2:0] GPR_0_2
);

  wire not_1_out;
  wire [7:3] pull_resistor_1_node;

  not not_1 (not_1_out, Enable);
  // NoConnect on pull_resistor_1_node[3]
  // NoConnect on pull_resistor_1_node[4]
  // NoConnect on pull_resistor_1_node[5]
  // NoConnect on pull_resistor_1_node[6]
  // NoConnect on pull_resistor_1_node[7]
  Pull_Resistor pull_resistor_1 (.node({pull_resistor_1_node, GPR_0_2}));
  assign {pull_resistor_1_node, GPR_0_2} = not_1_out ? {{5{1'b0}}, A0_A2} : 8'bz;  // Controlled_Buffer controlled_buffer_1
endmodule

module WriteGroup1 (
  input  ENABLE,
  input  [3:0] A0_A3,
  output LATCH_A,
  output LATCH_B,
  output IO_WRITE,
  output LATCH_IRQ_MASK,
  output LATCH_IRQ_PRIORITY,
  output USE_STACK_SEG,
  output USE_DATA_SEG,
  output MEM_WRITE,
  output RESTORE_FLAGS,
  output LATCH_FLAGS,
  output LATCH_MAR,
  output LATCH_STACK_SEG,
  output LATCH_CODE_SEG,
  output LATCH_DATA_SEG,
  output MEMRQ_WRITE,
  output NC1,
  output NC2
);

  wire decoder_1_out0, decoder_1_out1, decoder_1_out2, decoder_1_out3, decoder_1_out4, decoder_1_out5,
       decoder_1_out6, decoder_1_out7, decoder_1_out8, decoder_1_out9, decoder_1_out10, decoder_1_out11,
       decoder_1_out12, decoder_1_out13, decoder_1_out14, decoder_1_out15, not_9_out, not_17_out;

  not not_1 (LATCH_A, decoder_1_out0);
  not not_2 (LATCH_B, decoder_1_out1);
  not not_3 (IO_WRITE, decoder_1_out2);
  not not_4 (LATCH_IRQ_MASK, decoder_1_out3);
  not not_5 (LATCH_IRQ_PRIORITY, decoder_1_out4);
  not not_6 (USE_STACK_SEG, decoder_1_out5);
  not not_7 (USE_DATA_SEG, decoder_1_out6);
  not not_8 (RESTORE_FLAGS, decoder_1_out7);
  not not_9 (not_9_out, decoder_1_out8);
  not not_10 (LATCH_MAR, decoder_1_out9);
  not not_11 (LATCH_STACK_SEG, decoder_1_out10);
  not not_12 (LATCH_CODE_SEG, decoder_1_out11);
  not not_13 (LATCH_DATA_SEG, decoder_1_out12);
  not not_14 (MEMRQ_WRITE, decoder_1_out13);
  not not_15 (NC1, decoder_1_out14);
  not not_16 (NC2, decoder_1_out15);
  not not_17 (not_17_out, ENABLE);
  Decoder #(.select(4)) decoder_1 (
    .out0(decoder_1_out0), .out1(decoder_1_out1), .out2(decoder_1_out2), .out3(decoder_1_out3),
    .out4(decoder_1_out4), .out5(decoder_1_out5), .out6(decoder_1_out6), .out7(decoder_1_out7),
    .out8(decoder_1_out8), .out9(decoder_1_out9), .out10(decoder_1_out10), .out11(decoder_1_out11),
    .out12(decoder_1_out12), .out13(decoder_1_out13), .out14(decoder_1_out14), .out15(decoder_1_out15),
    .sel(A0_A3), .en(not_17_out));
  and and_1 (MEM_WRITE, USE_DATA_SEG, USE_STACK_SEG);
  and and_2 (LATCH_FLAGS, RESTORE_FLAGS, not_9_out);
endmodule

module WriteGroup2 (
  input  ENABLE,
  input  [3:0] A0_A3,
  output LATCH_INSTRUCTION,
  output PC_DEC,
  output LATCH_PC,
  output SP_INC,
  output SP_DEC,
  output LATCH_SP,
  output NC0,
  output NC1,
  output NC2,
  output NC3,
  output NC4,
  output NC5,
  output NC6,
  output NC7,
  output NC8,
  output NC9
);

  wire decoder_1_out0, decoder_1_out1, decoder_1_out2, decoder_1_out3, decoder_1_out4, decoder_1_out5,
       decoder_1_out6, decoder_1_out7, decoder_1_out8, decoder_1_out9, decoder_1_out10, decoder_1_out11,
       decoder_1_out12, decoder_1_out13, decoder_1_out14, decoder_1_out15, not_17_out;

  not not_1 (LATCH_INSTRUCTION, decoder_1_out0);
  not not_2 (PC_DEC, decoder_1_out1);
  not not_3 (LATCH_PC, decoder_1_out2);
  not not_4 (SP_INC, decoder_1_out3);
  not not_5 (SP_DEC, decoder_1_out4);
  not not_6 (LATCH_SP, decoder_1_out5);
  not not_7 (NC0, decoder_1_out6);
  not not_8 (NC1, decoder_1_out7);
  not not_9 (NC2, decoder_1_out8);
  not not_10 (NC3, decoder_1_out9);
  not not_11 (NC4, decoder_1_out10);
  not not_12 (NC5, decoder_1_out11);
  not not_13 (NC6, decoder_1_out12);
  not not_14 (NC7, decoder_1_out13);
  not not_15 (NC8, decoder_1_out14);
  not not_16 (NC9, decoder_1_out15);
  not not_17 (not_17_out, ENABLE);
  Decoder #(.select(4)) decoder_1 (
    .out0(decoder_1_out0), .out1(decoder_1_out1), .out2(decoder_1_out2), .out3(decoder_1_out3),
    .out4(decoder_1_out4), .out5(decoder_1_out5), .out6(decoder_1_out6), .out7(decoder_1_out7),
    .out8(decoder_1_out8), .out9(decoder_1_out9), .out10(decoder_1_out10), .out11(decoder_1_out11),
    .out12(decoder_1_out12), .out13(decoder_1_out13), .out14(decoder_1_out14), .out15(decoder_1_out15),
    .sel(A0_A3), .en(not_17_out));
endmodule

module WriteGroup3 (
  input  [3:0] A0_A3,
  input  Enable,
  output [3:0] JCC_0_3
);

  wire not_1_out;
  wire [7:4] pull_resistor_1_node;

  not not_1 (not_1_out, Enable);
  Pull_Resistor pull_resistor_1 (.node({pull_resistor_1_node, JCC_0_3}));
  assign {pull_resistor_1_node, JCC_0_3} = not_1_out ? {4'b0000, A0_A3} : 8'bz;  // Controlled_Buffer controlled_buffer_1
endmodule

module WriteGroups (
  input  [5:0] EEPROM0,
  output [2:0] GPR_0_2,
  output LATCH_A,
  output LATCH_B,
  output IO_WRITE,
  output IRQ_MASK_IN,
  output IRQ_PRIORITY_IN,
  output USE_STACK_SEG,
  output USE_DATA_SEG,
  output MEM_WRITE,
  output RESTORE_FLAGS,
  output LATCH_FLAGS,
  output LATCH_MAR,
  output LATCH_STACK_SEG,
  output LATCH_CODE_SEG,
  output LATCH_DATA_SEG,
  output MEMRQ_WRITE,
  output NC_1_1,
  output NC_1_2,
  output LATCH_INST_REG,
  output DEC_PC,
  output LATCH_PC,
  output INC_SP,
  output DEC_SP,
  output LATCH_SP,
  output NC_2_0,
  output NC_2_1,
  output NC_2_2,
  output NC_2_3,
  output NC_2_4,
  output NC_2_5,
  output NC_2_6,
  output NC_2_7,
  output NC_2_8,
  output NC_2_9,
  output [3:0] JCC_0_3
);

  wire decoder_1_out0, decoder_1_out1, decoder_1_out2, decoder_1_out3, not_1_out, not_2_out, not_3_out,
       not_4_out, not_5_out;

  not not_1 (not_1_out, 1'b0);
  Decoder #(.select(2)) decoder_1 (
    .out0(decoder_1_out0), .out1(decoder_1_out1), .out2(decoder_1_out2), .out3(decoder_1_out3),
    .sel(EEPROM0[5:4]), .en(not_1_out));
  not not_2 (not_2_out, decoder_1_out0);
  not not_3 (not_3_out, decoder_1_out1);
  not not_4 (not_4_out, decoder_1_out2);
  not not_5 (not_5_out, decoder_1_out3);
  WriteGroup0 writegroup0_1 (.A0_A2(EEPROM0[2:0]), .Enable(not_2_out), .GPR_0_2(GPR_0_2));
  WriteGroup1 writegroup1_1 (
    .ENABLE(not_3_out), .A0_A3(EEPROM0[3:0]), .LATCH_A(LATCH_A), .LATCH_B(LATCH_B), .IO_WRITE(IO_WRITE),
    .LATCH_IRQ_MASK(IRQ_MASK_IN), .LATCH_IRQ_PRIORITY(IRQ_PRIORITY_IN), .USE_STACK_SEG(USE_STACK_SEG),
    .USE_DATA_SEG(USE_DATA_SEG), .MEM_WRITE(MEM_WRITE), .RESTORE_FLAGS(RESTORE_FLAGS),
    .LATCH_FLAGS(LATCH_FLAGS), .LATCH_MAR(LATCH_MAR), .LATCH_STACK_SEG(LATCH_STACK_SEG),
    .LATCH_CODE_SEG(LATCH_CODE_SEG), .LATCH_DATA_SEG(LATCH_DATA_SEG), .MEMRQ_WRITE(MEMRQ_WRITE),
    .NC1(NC_1_1), .NC2(NC_1_2));
  WriteGroup2 writegroup2_1 (
    .ENABLE(not_4_out), .A0_A3(EEPROM0[3:0]), .LATCH_INSTRUCTION(LATCH_INST_REG), .PC_DEC(DEC_PC),
    .LATCH_PC(LATCH_PC), .SP_INC(INC_SP), .SP_DEC(DEC_SP), .LATCH_SP(LATCH_SP), .NC0(NC_2_0), .NC1(NC_2_1),
    .NC2(NC_2_2), .NC3(NC_2_3), .NC4(NC_2_4), .NC5(NC_2_5), .NC6(NC_2_6), .NC7(NC_2_7), .NC8(NC_2_8),
    .NC9(NC_2_9));
  WriteGroup3 writegroup3_1 (.A0_A3(EEPROM0[3:0]), .Enable(not_5_out), .JCC_0_3(JCC_0_3));
endmodule

module ReadGroups (
  input  [5:0] EEPROM0,
  output [3:0] GPR_3_6,
  output MEM_OUT,
  output USE_CODE_SEG,
  output USE_DATA_SEG,
  output USE_STACK_SEG,
  output CODE_SEG_OUT,
  output DATA_SEG_OUT,
  output STACK_SEG_OUT,
  output PC_OUT,
  output SP_OUT,
  output FLAGS_OUT,
  output IO_READ,
  output IRQ_PORT_OUT,
  output MEMRQ_READ,
  output NC1,
  output NC2,
  output NC3,
  output NC4,
  output [5:0] ALU_0_5
);

  wire decoder_1_out0, decoder_1_out1, decoder_1_out2, decoder_1_out3, not_1_out, not_2_out, not_3_out,
       not_4_out, not_5_out;

  not not_1 (not_1_out, 1'b0);
  Decoder #(.select(2)) decoder_1 (
    .out0(decoder_1_out0), .out1(decoder_1_out1), .out2(decoder_1_out2), .out3(decoder_1_out3),
    .sel(EEPROM0[5:4]), .en(not_1_out));
  not not_2 (not_2_out, decoder_1_out0);
  not not_3 (not_3_out, decoder_1_out1);
  not not_4 (not_4_out, decoder_1_out2);
  not not_5 (not_5_out, decoder_1_out3);
  ReadGroup0 readgroup0_1 (.A0_A3(EEPROM0[3:0]), .Enable(not_2_out), .GPR_3_6(GPR_3_6));
  ReadGroup1 readgroup1_1 (
    .ENABLE(not_3_out), .A0_A3(EEPROM0[3:0]), .MEM_OUT(MEM_OUT), .USE_CODE_SEG(USE_CODE_SEG),
    .USE_DATA_SEG(USE_DATA_SEG), .USE_STACK_SEG(USE_STACK_SEG), .CODE_SEG_OUT(CODE_SEG_OUT),
    .DATA_SEG_OUT(DATA_SEG_OUT), .STACK_SEG_OUT(STACK_SEG_OUT), .PC_OUT(PC_OUT), .SP_OUT(SP_OUT),
    .FLAGS_OUT(FLAGS_OUT), .IO_READ(IO_READ), .IRQ_PORT_OUT(IRQ_PORT_OUT), .MEMRQ_READ(MEMRQ_READ),
    .NC1(NC1), .NC2(NC2), .NC3(NC3), .NC4(NC4));
  ReadGroup2 readgroup2_1 (.A0_A3(EEPROM0[3:0]), .EnableA(not_4_out), .EnableB(not_5_out), .ALU_0_5(ALU_0_5));
endmodule

module ReadGroup0 (
  input  [3:0] A0_A3,
  input  Enable,
  output [3:0] GPR_3_6
);

  wire not_1_out;
  wire [7:4] pull_resistor_1_node;

  // NoConnect on pull_resistor_1_node[4]
  // NoConnect on pull_resistor_1_node[5]
  // NoConnect on pull_resistor_1_node[6]
  // NoConnect on pull_resistor_1_node[7]
  Pull_Resistor pull_resistor_1 (.node({pull_resistor_1_node, GPR_3_6}));
  assign {pull_resistor_1_node, GPR_3_6} = not_1_out ? {4'b0000, A0_A3} : 8'bz;  // Controlled_Buffer controlled_buffer_1
  not not_1 (not_1_out, Enable);
endmodule

module ReadGroup1 (
  input  ENABLE,
  input  [3:0] A0_A3,
  output MEM_OUT,
  output USE_CODE_SEG,
  output USE_DATA_SEG,
  output USE_STACK_SEG,
  output CODE_SEG_OUT,
  output DATA_SEG_OUT,
  output STACK_SEG_OUT,
  output PC_OUT,
  output SP_OUT,
  output FLAGS_OUT,
  output IO_READ,
  output IRQ_PORT_OUT,
  output MEMRQ_READ,
  output NC1,
  output NC2,
  output NC3,
  output NC4
);

  wire and_1_out, decoder_1_out0, decoder_1_out1, decoder_1_out2, decoder_1_out3, decoder_1_out4,
       decoder_1_out5, decoder_1_out6, decoder_1_out7, decoder_1_out8, decoder_1_out9, decoder_1_out10,
       decoder_1_out11, decoder_1_out12, decoder_1_out13, decoder_1_out14, decoder_1_out15, not_1_out;

  not not_1 (not_1_out, ENABLE);
  not not_2 (USE_CODE_SEG, decoder_1_out0);
  not not_3 (USE_DATA_SEG, decoder_1_out1);
  not not_4 (USE_STACK_SEG, decoder_1_out2);
  not not_5 (CODE_SEG_OUT, decoder_1_out3);
  not not_6 (DATA_SEG_OUT, decoder_1_out4);
  not not_7 (STACK_SEG_OUT, decoder_1_out5);
  not not_8 (PC_OUT, decoder_1_out6);
  not not_9 (SP_OUT, decoder_1_out7);
  not not_10 (FLAGS_OUT, decoder_1_out8);
  not not_11 (IO_READ, decoder_1_out9);
  not not_12 (IRQ_PORT_OUT, decoder_1_out10);
  not not_13 (MEMRQ_READ, decoder_1_out11);
  not not_14 (NC1, decoder_1_out12);
  not not_15 (NC2, decoder_1_out13);
  not not_16 (NC3, decoder_1_out14);
  not not_17 (NC4, decoder_1_out15);
  Decoder #(.select(4)) decoder_1 (
    .out0(decoder_1_out0), .out1(decoder_1_out1), .out2(decoder_1_out2), .out3(decoder_1_out3),
    .out4(decoder_1_out4), .out5(decoder_1_out5), .out6(decoder_1_out6), .out7(decoder_1_out7),
    .out8(decoder_1_out8), .out9(decoder_1_out9), .out10(decoder_1_out10), .out11(decoder_1_out11),
    .out12(decoder_1_out12), .out13(decoder_1_out13), .out14(decoder_1_out14), .out15(decoder_1_out15),
    .sel(A0_A3), .en(not_1_out));
  and and_1 (and_1_out, USE_CODE_SEG, USE_DATA_SEG);
  and and_2 (MEM_OUT, and_1_out, USE_STACK_SEG);
endmodule

module ReadGroup2 (
  input  [3:0] A0_A3,
  input  EnableA,
  input  EnableB,
  output [5:0] ALU_0_5
);

  wire and_1_out, not_1_out;
  wire [7:6] pull_resistor_1_node;

  and and_1 (and_1_out, EnableA, EnableB);
  // NoConnect on pull_resistor_1_node[6]
  // NoConnect on pull_resistor_1_node[7]
  Pull_Resistor pull_resistor_1 (.node({pull_resistor_1_node, ALU_0_5}));
  assign {pull_resistor_1_node, ALU_0_5} = not_1_out ? {3'b001, EnableA, A0_A3} : 8'bz;  // Controlled_Buffer controlled_buffer_1
  not not_1 (not_1_out, and_1_out);
endmodule

module CombinedControl (
  input  JCC_COND_PCI,
  input  [5:0] EEPROM0,
  input  [5:0] EEPROM1,
  output [6:0] GPR,
  output LATCH_A,
  output LATCH_B,
  output IRQ_REG_SEL,
  output IRQ_WRITE,
  output WRITE_MEM,
  output RESTORE_FLAGS,
  output LATCH_FLAGS,
  output LATCH_MAR,
  output LATCH_STACK_SEG,
  output LATCH_CODE_SEF,
  output LATCH_DATA_SEG,
  output LATCH_INST_REG,
  output DEC_PC,
  output INC_SP,
  output DEC_SP,
  output LATCH_PC,
  output LATCH_SP,
  output [11:0] EXTRA_WRITE,
  output [3:0] JCC_0_3,
  output USE_CODE_SEGMENT,
  output USE_STACK_SEGMENT,
  output USE_DATA_SEGMENT,
  output MEM_OUT,
  output CODE_SEG_OUT,
  output DATA_SEG_OUT,
  output STACK_SEG_OUT,
  output IRQ_HANDLER_EN,
  output IRQ_READ,
  output PC_OUT,
  output SP_OUT,
  output FLAGS_OUT,
  output [5:0] ALU_0_5,
  output MEM_REQUEST,
  output MEM_READ,
  output MEM_WRITE,
  output IO_REQUEST,
  output IO_READ,
  output IO_WRITE,
  output [3:0] EXTRA_READ
);

  wire readgroups_1_use_data_seg, readgroups_1_use_stack_seg, writegroups_1_irq_priority_in,
       writegroups_1_latch_pc, writegroups_1_use_data_seg, writegroups_1_use_stack_seg;

  WriteGroups writegroups_1 (
    .EEPROM0(EEPROM0), .GPR_0_2(GPR[2:0]), .LATCH_A(LATCH_A), .LATCH_B(LATCH_B), .IO_WRITE(IO_WRITE),
    .IRQ_MASK_IN(IRQ_REG_SEL), .IRQ_PRIORITY_IN(writegroups_1_irq_priority_in),
    .USE_STACK_SEG(writegroups_1_use_stack_seg), .USE_DATA_SEG(writegroups_1_use_data_seg),
    .MEM_WRITE(WRITE_MEM), .RESTORE_FLAGS(RESTORE_FLAGS), .LATCH_FLAGS(LATCH_FLAGS), .LATCH_MAR(LATCH_MAR),
    .LATCH_STACK_SEG(LATCH_STACK_SEG), .LATCH_CODE_SEG(LATCH_CODE_SEF), .LATCH_DATA_SEG(LATCH_DATA_SEG),
    .MEMRQ_WRITE(MEM_WRITE), .NC_1_1(EXTRA_WRITE[0]), .NC_1_2(EXTRA_WRITE[1]),
    .LATCH_INST_REG(LATCH_INST_REG), .DEC_PC(DEC_PC), .LATCH_PC(writegroups_1_latch_pc), .INC_SP(INC_SP),
    .DEC_SP(DEC_SP), .LATCH_SP(LATCH_SP), .NC_2_0(EXTRA_WRITE[2]), .NC_2_1(EXTRA_WRITE[3]),
    .NC_2_2(EXTRA_WRITE[4]), .NC_2_3(EXTRA_WRITE[5]), .NC_2_4(EXTRA_WRITE[6]), .NC_2_5(EXTRA_WRITE[7]),
    .NC_2_6(EXTRA_WRITE[8]), .NC_2_7(EXTRA_WRITE[9]), .NC_2_8(EXTRA_WRITE[10]), .NC_2_9(EXTRA_WRITE[11]),
    .JCC_0_3(JCC_0_3));
  ReadGroups readgroups_1 (
    .EEPROM0(EEPROM1), .GPR_3_6(GPR[6:3]), .MEM_OUT(MEM_OUT), .USE_CODE_SEG(USE_CODE_SEGMENT),
    .USE_DATA_SEG(readgroups_1_use_data_seg), .USE_STACK_SEG(readgroups_1_use_stack_seg),
    .CODE_SEG_OUT(CODE_SEG_OUT), .DATA_SEG_OUT(DATA_SEG_OUT), .STACK_SEG_OUT(STACK_SEG_OUT), .PC_OUT(PC_OUT),
    .SP_OUT(SP_OUT), .FLAGS_OUT(FLAGS_OUT), .IO_READ(IO_READ), .IRQ_PORT_OUT(IRQ_READ),
    .MEMRQ_READ(MEM_READ), .NC1(EXTRA_READ[0]), .NC2(EXTRA_READ[1]), .NC3(EXTRA_READ[2]),
    .NC4(EXTRA_READ[3]), .ALU_0_5(ALU_0_5));
  and and_1 (LATCH_PC, writegroups_1_latch_pc, JCC_COND_PCI);
  and and_2 (IO_REQUEST, IO_WRITE, IO_READ);
  and and_3 (MEM_REQUEST, MEM_WRITE, MEM_READ);
  and and_4 (IRQ_WRITE, IRQ_REG_SEL, writegroups_1_irq_priority_in);
  and and_5 (USE_STACK_SEGMENT, writegroups_1_use_stack_seg, readgroups_1_use_stack_seg);
  and and_6 (USE_DATA_SEGMENT, writegroups_1_use_data_seg, readgroups_1_use_data_seg);
  and and_7 (IRQ_HANDLER_EN, IRQ_WRITE, IRQ_READ);

  // Notes on the sheet:
  //   GPR: pull=down
endmodule

module OpCounter (
  input  Reset,
  input  Clock,
  output [3:0] Step
);

  wire n74161_1_pin1, n74161_1_pin2, n74161_1_pin3, n74161_1_pin7, n74161_1_pin10, n74161_1_pin15;

  _74161 u_74161_1 (
    .pin1(n74161_1_pin1), .pin2(n74161_1_pin2), .pin3(n74161_1_pin3), .pin4(n74161_1_pin3),
    .pin5(n74161_1_pin3), .pin6(n74161_1_pin3), .pin7(n74161_1_pin7), .pin15(n74161_1_pin15),
    .pin14(Step[0]), .pin13(Step[1]), .pin12(Step[2]), .pin11(Step[3]), .pin10(n74161_1_pin10), .pin9(Reset));
  // NoConnect on n74161_1_pin15
  not not_1 (n74161_1_pin2, Clock);
  // also tied to GND on the sheet: n74161_1_pin3
  // also tied to VCC on the sheet: {n74161_1_pin1, n74161_1_pin10, n74161_1_pin7}
endmodule

module OpcodeDisplay (
  input  [7:0] OPCODE_IN,
  input  LATCH_OPCODE,
  input  CLK_IN,
  output [7:0] OPCODE_OUT,
  output [6:0] DATA,
  output WE,
  output CLEAR,
  output CLK
);

  wire counter4bit_1_endflag, nand_1_out, not_1_out, not_2_out;
  wire [3:0] counter4bit_1_step;
  wire [7:7] rom_1_data;

  Clock clock_1 (.out(CLK));
  Register register_1 (.D(OPCODE_IN), .en(LATCH_OPCODE), .clk(CLK), .Q(OPCODE_OUT), .clr(1'b0));
  not not_1 (not_1_out, LATCH_OPCODE);
  ROM #(.addrWidth(12)) rom_1 (.addr({OPCODE_OUT, counter4bit_1_step}), .data({rom_1_data[7], DATA}));
  Hex_Digit_Display hex_digit_display_1 (.value(OPCODE_OUT[7:4]));  // open: dp
  not not_2 (not_2_out, counter4bit_1_endflag);
  Hex_Digit_Display hex_digit_display_2 (.value(OPCODE_OUT[3:0]));  // open: dp
  nand nand_1 (nand_1_out, not_2_out, WE);
  nand nand_2 (WE, nand_1_out, not_1_out);
  // NoConnect on rom_1_data[7]
  Counter4Bit counter4bit_1 (
    .CLK(CLK), .Reset(not_1_out), .EndFlag(counter4bit_1_endflag), .STEP(counter4bit_1_step));  // open: StartFlag
  TTY #(.rows(2)) tty_1 (.data(DATA), .clk(CLK), .we(WE), .clr(LATCH_OPCODE));

  assign CLEAR = LATCH_OPCODE;

  // Notes on the sheet:
  //   CLK_IN: pull=up
  //   LATCH_OPCODE: pull=up
  //   contents of rom_1 (hex, n*v repeats v):
  //   256*0 4d 4f 56 20 41 2c 20 43 20 7*0 4d 4f 56 20 41 2c 20 44 20
  //   41: A
  //   42: B
  //   43: C
  //   44: D
  //   45: E
  //   46: F
  //   47: G
  //   48: H
  //   49: I
  //   4A: J
  //   4B: K
  //   4C: L
  //   4D: M
  //   4E: N
  //   4F: O
  //   50: P
  //   51: Q
  //   52: R
  //   53: S
  //   54: T
  //   55: U
  //   56: V
  //   57: W
  //   58: X
  //   59: Y
  //   5A: Z
  //   ENABLE
  //   CLEAR
  //   20: Space
  //   2C: ,
endmodule

module Counter4Bit (
  input  CLK,
  input  Reset,
  output EndFlag,
  output [3:0] STEP,
  output StartFlag
);

  wire n74161_1_pin1, n74161_1_pin3, n74161_1_pin7, n74161_1_pin10;

  _74161 u_74161_1 (
    .pin1(n74161_1_pin1), .pin2(CLK), .pin3(n74161_1_pin3), .pin4(n74161_1_pin3), .pin5(n74161_1_pin3),
    .pin6(n74161_1_pin3), .pin7(n74161_1_pin7), .pin14(STEP[0]), .pin13(STEP[1]), .pin12(STEP[2]),
    .pin11(STEP[3]), .pin10(n74161_1_pin10), .pin9(Reset));  // open: pin15
  and and_1 (EndFlag, STEP[0], STEP[1], STEP[2], STEP[3]);
  nor nor_1 (StartFlag, STEP[3], STEP[2], STEP[1], STEP[0]);
  // also tied to GND on the sheet: n74161_1_pin3
  // also tied to VCC on the sheet: {n74161_1_pin1, n74161_1_pin10, n74161_1_pin7}
endmodule
