// Logisim project FIFO.circ as structural Verilog: 7 circuits, main circuit main
module main (
  input  RESET,
  input  WRITE,
  input  READ
);

  wire fifo_address_1_empty, fifo_address_1_full, fifo_address_1_half_full;
  wire [3:0] fifo_address_1_count;
  wire [7:0] dipswitch_1_sw8, registerarray_1_data_out;
  wire [15:0] fifo_address_1_read_address, fifo_address_1_write_address;

  DipSwitch dipswitch_1 (
    .sw1(dipswitch_1_sw8[7]), .sw2(dipswitch_1_sw8[6]), .sw3(dipswitch_1_sw8[5]), .sw4(dipswitch_1_sw8[4]),
    .sw5(dipswitch_1_sw8[3]), .sw6(dipswitch_1_sw8[2]), .sw7(dipswitch_1_sw8[1]), .sw8(dipswitch_1_sw8[0]));
  LED led_1 (.in(fifo_address_1_empty));
  FIFO_Address fifo_address_1 (
    .WRITE_ADDRESS(fifo_address_1_write_address), .READ_ADDRESS(fifo_address_1_read_address),
    .EMPTY(fifo_address_1_empty), .FULL(fifo_address_1_full), .HALF_FULL(fifo_address_1_half_full),
    .COUNT(fifo_address_1_count), .RESET(RESET), .WRITE(WRITE), .READ(READ));
  RegisterArray registerarray_1 (
    .DATA_IN(dipswitch_1_sw8), .READ_SELECT(fifo_address_1_read_address),
    .WRITE_SELECT(fifo_address_1_write_address), .DATA_OUT(registerarray_1_data_out));
  LED led_2 (.in(fifo_address_1_full));
  // LedBar #(.inputtype("row"), .matrixcols(16)) ledbar_1: pin names not known; wires that end beside it: fifo_address_1_write_address
  // LedBar #(.inputtype("row"), .matrixcols(16)) ledbar_2: pin names not known; wires that end beside it: fifo_address_1_read_address
  // LedBar #(.inputtype("row")) ledbar_3: pin names not known; wires that end beside it: registerarray_1_data_out
  LED led_3 (.in(fifo_address_1_half_full));
  Hex_Digit_Display hex_digit_display_1 (.value(fifo_address_1_count));  // open: dp
  // LedBar #(.inputtype("row"), .matrixcols(4)) ledbar_4: pin names not known; wires that end beside it: fifo_address_1_count

  // Notes on the sheet:
  //   EMPTY
  //   FULL
  //   HALF
endmodule

module TTL_74LS574 (
  input  [7:0] DATA_IN,
  input  OE,
  input  CP,
  output [7:0] DATA_OUT
);

  wire d_ff_1_q, d_ff_1_qn, d_ff_2_q, d_ff_2_qn, d_ff_3_q, d_ff_3_qn, d_ff_4_q, d_ff_4_qn, d_ff_5_q,
       d_ff_5_qn, d_ff_6_q, d_ff_6_qn, d_ff_7_q, d_ff_7_qn, d_ff_8_q, d_ff_8_qn, not_1_out;

  not not_1 (not_1_out, OE);
  D_Flip_Flop d_ff_1 (.D(DATA_IN[0]), .clk(CP), .Q(d_ff_1_q), .Qn(d_ff_1_qn), .preset(1'b0), .reset(1'b0));
  // NoConnect on d_ff_1_qn
  D_Flip_Flop d_ff_2 (.D(DATA_IN[1]), .clk(CP), .Q(d_ff_2_q), .Qn(d_ff_2_qn), .preset(1'b0), .reset(1'b0));
  // NoConnect on d_ff_2_qn
  D_Flip_Flop d_ff_3 (.D(DATA_IN[2]), .clk(CP), .Q(d_ff_3_q), .Qn(d_ff_3_qn), .preset(1'b0), .reset(1'b0));
  // NoConnect on d_ff_3_qn
  D_Flip_Flop d_ff_4 (.D(DATA_IN[3]), .clk(CP), .Q(d_ff_4_q), .Qn(d_ff_4_qn), .preset(1'b0), .reset(1'b0));
  // NoConnect on d_ff_4_qn
  D_Flip_Flop d_ff_5 (.D(DATA_IN[4]), .clk(CP), .Q(d_ff_5_q), .Qn(d_ff_5_qn), .preset(1'b0), .reset(1'b0));
  // NoConnect on d_ff_5_qn
  D_Flip_Flop d_ff_6 (.D(DATA_IN[5]), .clk(CP), .Q(d_ff_6_q), .Qn(d_ff_6_qn), .preset(1'b0), .reset(1'b0));
  // NoConnect on d_ff_6_qn
  D_Flip_Flop d_ff_7 (.D(DATA_IN[6]), .clk(CP), .Q(d_ff_7_q), .Qn(d_ff_7_qn), .preset(1'b0), .reset(1'b0));
  // NoConnect on d_ff_7_qn
  D_Flip_Flop d_ff_8 (.D(DATA_IN[7]), .clk(CP), .Q(d_ff_8_q), .Qn(d_ff_8_qn), .preset(1'b0), .reset(1'b0));
  // NoConnect on d_ff_8_qn
  assign DATA_OUT[0] = not_1_out ? d_ff_1_q : 1'bz;  // Controlled_Buffer controlled_buffer_1
  assign DATA_OUT[1] = not_1_out ? d_ff_2_q : 1'bz;  // Controlled_Buffer controlled_buffer_2
  assign DATA_OUT[2] = not_1_out ? d_ff_3_q : 1'bz;  // Controlled_Buffer controlled_buffer_3
  assign DATA_OUT[3] = not_1_out ? d_ff_4_q : 1'bz;  // Controlled_Buffer controlled_buffer_4
  assign DATA_OUT[4] = not_1_out ? d_ff_5_q : 1'bz;  // Controlled_Buffer controlled_buffer_5
  assign DATA_OUT[5] = not_1_out ? d_ff_6_q : 1'bz;  // Controlled_Buffer controlled_buffer_6
  assign DATA_OUT[6] = not_1_out ? d_ff_7_q : 1'bz;  // Controlled_Buffer controlled_buffer_7
  assign DATA_OUT[7] = not_1_out ? d_ff_8_q : 1'bz;  // Controlled_Buffer controlled_buffer_8
endmodule

module ActiveLowDecoder4to16 (
  input  EN,
  input  [3:0] ADDRESS,
  output [15:0] out_3
);

  wire decoder_1_out0, decoder_1_out1, decoder_1_out2, decoder_1_out3, decoder_1_out4, decoder_1_out5,
       decoder_1_out6, decoder_1_out7, decoder_1_out8, decoder_1_out9, decoder_1_out10, decoder_1_out11,
       decoder_1_out12, decoder_1_out13, decoder_1_out14, decoder_1_out15, not_1_out;

  not not_1 (not_1_out, EN);
  Decoder #(.select(4)) decoder_1 (
    .out0(decoder_1_out0), .out1(decoder_1_out1), .out2(decoder_1_out2), .out3(decoder_1_out3),
    .out4(decoder_1_out4), .out5(decoder_1_out5), .out6(decoder_1_out6), .out7(decoder_1_out7),
    .out8(decoder_1_out8), .out9(decoder_1_out9), .out10(decoder_1_out10), .out11(decoder_1_out11),
    .out12(decoder_1_out12), .out13(decoder_1_out13), .out14(decoder_1_out14), .out15(decoder_1_out15),
    .sel(ADDRESS), .en(not_1_out));
  not not_2 (out_3[0], decoder_1_out0);
  not not_3 (out_3[1], decoder_1_out1);
  not not_4 (out_3[2], decoder_1_out2);
  not not_5 (out_3[3], decoder_1_out3);
  not not_6 (out_3[4], decoder_1_out4);
  not not_7 (out_3[5], decoder_1_out5);
  not not_8 (out_3[6], decoder_1_out6);
  not not_9 (out_3[7], decoder_1_out7);
  not not_10 (out_3[8], decoder_1_out8);
  not not_11 (out_3[9], decoder_1_out9);
  not not_12 (out_3[10], decoder_1_out10);
  not not_13 (out_3[11], decoder_1_out11);
  not not_14 (out_3[12], decoder_1_out12);
  not not_15 (out_3[13], decoder_1_out13);
  not not_16 (out_3[14], decoder_1_out14);
  not not_17 (out_3[15], decoder_1_out15);
endmodule

module UpDownDecoder (
  input  RESET,
  input  CP,
  output [3:0] COUNT,
  output [15:0] ADDRESS
);

  wire decoder_1_out0, decoder_1_out1, decoder_1_out2, decoder_1_out3, decoder_1_out4, decoder_1_out5,
       decoder_1_out6, decoder_1_out7, decoder_1_out8, decoder_1_out9, decoder_1_out10, decoder_1_out11,
       decoder_1_out12, decoder_1_out13, decoder_1_out14, decoder_1_out15, ttl_74ls193_1_bo, ttl_74ls193_1_co;

  TTL_74LS193 ttl_74ls193_1 (
    .P3(1'b0), .P2(1'b0), .P1(1'b0), .P0(1'b0), .LOAD(RESET), .UP(CP), .DOWN(1'b1), .CLEAR(1'b0),
    .Q3(COUNT[3]), .Q2(COUNT[2]), .Q1(COUNT[1]), .QO(COUNT[0]), .CO(ttl_74ls193_1_co), .BO(ttl_74ls193_1_bo));
  // NoConnect on ttl_74ls193_1_co
  // NoConnect on ttl_74ls193_1_bo
  not not_1 (ADDRESS[0], decoder_1_out0);
  not not_2 (ADDRESS[1], decoder_1_out1);
  not not_3 (ADDRESS[2], decoder_1_out2);
  not not_4 (ADDRESS[3], decoder_1_out3);
  not not_5 (ADDRESS[4], decoder_1_out4);
  not not_6 (ADDRESS[5], decoder_1_out5);
  not not_7 (ADDRESS[6], decoder_1_out6);
  not not_8 (ADDRESS[7], decoder_1_out7);
  not not_9 (ADDRESS[8], decoder_1_out8);
  not not_10 (ADDRESS[9], decoder_1_out9);
  not not_11 (ADDRESS[10], decoder_1_out10);
  not not_12 (ADDRESS[11], decoder_1_out11);
  not not_13 (ADDRESS[12], decoder_1_out12);
  not not_14 (ADDRESS[13], decoder_1_out13);
  not not_15 (ADDRESS[14], decoder_1_out14);
  not not_16 (ADDRESS[15], decoder_1_out15);
  Decoder #(.select(4)) decoder_1 (
    .out0(decoder_1_out0), .out1(decoder_1_out1), .out2(decoder_1_out2), .out3(decoder_1_out3),
    .out4(decoder_1_out4), .out5(decoder_1_out5), .out6(decoder_1_out6), .out7(decoder_1_out7),
    .out8(decoder_1_out8), .out9(decoder_1_out9), .out10(decoder_1_out10), .out11(decoder_1_out11),
    .out12(decoder_1_out12), .out13(decoder_1_out13), .out14(decoder_1_out14), .out15(decoder_1_out15),
    .sel(COUNT), .en(1'b1));
endmodule

module RegisterArray (
  input  [7:0] DATA_IN,
  input  [15:0] READ_SELECT,
  input  [15:0] WRITE_SELECT,
  output [7:0] DATA_OUT
);

  wire not_1_out, not_2_out, not_3_out, not_4_out, not_5_out, not_6_out, not_7_out, not_8_out, not_9_out,
       not_10_out, not_11_out, not_12_out, not_13_out, not_14_out, not_15_out, not_16_out;

  not not_1 (not_1_out, WRITE_SELECT[0]);
  not not_2 (not_2_out, WRITE_SELECT[1]);
  not not_3 (not_3_out, WRITE_SELECT[2]);
  not not_4 (not_4_out, WRITE_SELECT[3]);
  not not_5 (not_5_out, WRITE_SELECT[4]);
  not not_6 (not_6_out, WRITE_SELECT[5]);
  not not_7 (not_7_out, WRITE_SELECT[6]);
  not not_8 (not_8_out, WRITE_SELECT[7]);
  not not_9 (not_9_out, WRITE_SELECT[8]);
  not not_10 (not_10_out, WRITE_SELECT[9]);
  not not_11 (not_11_out, WRITE_SELECT[10]);
  not not_12 (not_12_out, WRITE_SELECT[11]);
  not not_13 (not_13_out, WRITE_SELECT[12]);
  not not_14 (not_14_out, WRITE_SELECT[13]);
  not not_15 (not_15_out, WRITE_SELECT[14]);
  not not_16 (not_16_out, WRITE_SELECT[15]);
  TTL_74LS574 ttl_74ls574_1 (.DATA_IN(DATA_IN), .OE(READ_SELECT[0]), .CP(not_1_out), .DATA_OUT(DATA_OUT));
  TTL_74LS574 ttl_74ls574_2 (.DATA_IN(DATA_IN), .OE(READ_SELECT[1]), .CP(not_2_out), .DATA_OUT(DATA_OUT));
  TTL_74LS574 ttl_74ls574_3 (.DATA_IN(DATA_IN), .OE(READ_SELECT[2]), .CP(not_3_out), .DATA_OUT(DATA_OUT));
  TTL_74LS574 ttl_74ls574_4 (.DATA_IN(DATA_IN), .OE(READ_SELECT[3]), .CP(not_4_out), .DATA_OUT(DATA_OUT));
  TTL_74LS574 ttl_74ls574_5 (.DATA_IN(DATA_IN), .OE(READ_SELECT[4]), .CP(not_5_out), .DATA_OUT(DATA_OUT));
  TTL_74LS574 ttl_74ls574_6 (.DATA_IN(DATA_IN), .OE(READ_SELECT[5]), .CP(not_6_out), .DATA_OUT(DATA_OUT));
  TTL_74LS574 ttl_74ls574_7 (.DATA_IN(DATA_IN), .OE(READ_SELECT[6]), .CP(not_7_out), .DATA_OUT(DATA_OUT));
  TTL_74LS574 ttl_74ls574_8 (.DATA_IN(DATA_IN), .OE(READ_SELECT[7]), .CP(not_8_out), .DATA_OUT(DATA_OUT));
  TTL_74LS574 ttl_74ls574_9 (.DATA_IN(DATA_IN), .OE(READ_SELECT[8]), .CP(not_9_out), .DATA_OUT(DATA_OUT));
  TTL_74LS574 ttl_74ls574_10 (.DATA_IN(DATA_IN), .OE(READ_SELECT[9]), .CP(not_10_out), .DATA_OUT(DATA_OUT));
  TTL_74LS574 ttl_74ls574_11 (.DATA_IN(DATA_IN), .OE(READ_SELECT[10]), .CP(not_11_out), .DATA_OUT(DATA_OUT));
  TTL_74LS574 ttl_74ls574_12 (.DATA_IN(DATA_IN), .OE(READ_SELECT[11]), .CP(not_12_out), .DATA_OUT(DATA_OUT));
  TTL_74LS574 ttl_74ls574_13 (.DATA_IN(DATA_IN), .OE(READ_SELECT[12]), .CP(not_13_out), .DATA_OUT(DATA_OUT));
  TTL_74LS574 ttl_74ls574_14 (.DATA_IN(DATA_IN), .OE(READ_SELECT[13]), .CP(not_14_out), .DATA_OUT(DATA_OUT));
  TTL_74LS574 ttl_74ls574_15 (.DATA_IN(DATA_IN), .OE(READ_SELECT[14]), .CP(not_15_out), .DATA_OUT(DATA_OUT));
  TTL_74LS574 ttl_74ls574_16 (.DATA_IN(DATA_IN), .OE(READ_SELECT[15]), .CP(not_16_out), .DATA_OUT(DATA_OUT));
endmodule

module FIFO_Address (
  input  RESET,
  input  WRITE,
  input  READ,
  output EMPTY,
  output FULL,
  output HALF_FULL,
  output [3:0] COUNT,
  output [15:0] WRITE_ADDRESS,
  output [15:0] READ_ADDRESS
);

  wire not_1_out, or_1_out, or_2_out;
  wire [3:0] updowndecoder_1_count, updowndecoder_2_count;

  not not_1 (not_1_out, READ);
  or or_1 (or_1_out, FULL, WRITE);
  or or_2 (or_2_out, EMPTY, not_1_out);
  UpDownDecoder updowndecoder_1 (.RESET(RESET), .CP(or_1_out), .COUNT(updowndecoder_1_count), .ADDRESS(WRITE_ADDRESS));
  UpDownDecoder updowndecoder_2 (.RESET(RESET), .CP(or_2_out), .COUNT(updowndecoder_2_count), .ADDRESS(READ_ADDRESS));
  Subtractor4Bit subtractor4bit_1 (.A(updowndecoder_1_count), .B(updowndecoder_2_count), .Q(COUNT));
  and and_1 (FULL, COUNT[0], COUNT[1], COUNT[2], COUNT[3]);
  nor nor_1 (EMPTY, COUNT[0], COUNT[1], COUNT[2], COUNT[3]);

  assign HALF_FULL = COUNT[3];
endmodule

module Subtractor4Bit (
  input  [3:0] A,
  input  [3:0] B,
  output [3:0] Q
);

  wire n74283_1_pin7, not_1_out, not_2_out, not_3_out, not_4_out;

  not not_1 (not_1_out, B[0]);
  not not_2 (not_2_out, B[1]);
  not not_3 (not_3_out, B[2]);
  not not_4 (not_4_out, B[3]);
  _74283 u_74283_1 (
    .pin1(Q[1]), .pin2(not_2_out), .pin3(A[1]), .pin4(Q[0]), .pin5(A[0]), .pin6(not_1_out),
    .pin7(n74283_1_pin7), .pin15(not_3_out), .pin14(A[2]), .pin13(Q[2]), .pin12(A[3]), .pin11(not_4_out),
    .pin10(Q[3]));  // open: pin9
  // also tied to VCC on the sheet: n74283_1_pin7
endmodule
