// Logisim project GPR.circ as structural Verilog: 1 circuit, main circuit main
module main (
  input  in_1,
  input  in_2,
  input  in_3,
  input  in_4,
  input  in_5,
  input  in_6,
  input  in_7,
  input  in_8
);

  wire clock_1_out, decoder_1_out0, decoder_1_out1, decoder_1_out2, decoder_1_out3, decoder_1_out4,
       decoder_1_out5, decoder_1_out6, decoder_1_out7, decoder_2_out0, decoder_2_out1, decoder_2_out2,
       decoder_2_out3, decoder_2_out4, decoder_2_out5, decoder_2_out6, decoder_2_out7, decoder_3_out0,
       decoder_3_out1, decoder_3_out2, decoder_3_out3, decoder_3_out4, decoder_3_out5, decoder_3_out6,
       decoder_3_out7, nand_1_out, nand_2_out, nand_3_out, nand_4_out, nand_5_out, nand_6_out, not_1_out,
       not_2_out, not_3_out, not_4_out, not_5_out, not_6_out, not_7_out, not_8_out, not_9_out, not_10_out,
       not_11_out, not_12_out, not_13_out, not_14_out, not_15_out, not_16_out, not_17_out, not_18_out,
       not_19_out, not_20_out, not_21_out, not_22_out;

  not not_1 (not_1_out, in_2);
  Clock clock_1 (.out(clock_1_out));
  not not_2 (not_2_out, clock_1_out);
  not not_3 (not_3_out, in_2);
  not not_4 (not_4_out, not_1_out);
  LED LDS3 (.in(nand_1_out));
  nand nand_1 (nand_1_out, in_1, not_11_out);
  // NoConnect on not_5_out
  not not_5 (not_5_out, decoder_1_out0);
  not not_6 (not_6_out, decoder_1_out1);
  not not_7 (not_7_out, decoder_1_out2);
  not not_8 (not_8_out, decoder_1_out3);
  not not_9 (not_9_out, decoder_1_out4);
  not not_10 (not_10_out, decoder_1_out5);
  not not_11 (not_11_out, decoder_1_out6);
  // NoConnect on not_12_out
  not not_12 (not_12_out, decoder_1_out7);
  Decoder #(.select(3)) decoder_1 (
    .out0(decoder_1_out0), .out1(decoder_1_out1), .out2(decoder_1_out2), .out3(decoder_1_out3),
    .out4(decoder_1_out4), .out5(decoder_1_out5), .out6(decoder_1_out6), .out7(decoder_1_out7),
    .sel({in_6, in_7, in_8}), .en(not_2_out));
  // NoConnect on not_13_out
  not not_13 (not_13_out, decoder_2_out0);
  not not_14 (not_14_out, decoder_2_out1);
  not not_15 (not_15_out, decoder_2_out2);
  not not_16 (not_16_out, decoder_2_out3);
  not not_17 (not_17_out, decoder_2_out4);
  not not_18 (not_18_out, decoder_2_out5);
  not not_19 (not_19_out, decoder_2_out6);
  not not_20 (not_20_out, decoder_2_out7);
  Decoder #(.select(3)) decoder_2 (
    .out0(decoder_2_out0), .out1(decoder_2_out1), .out2(decoder_2_out2), .out3(decoder_2_out3),
    .out4(decoder_2_out4), .out5(decoder_2_out5), .out6(decoder_2_out6), .out7(decoder_2_out7),
    .sel({in_3, in_4, in_5}), .en(not_3_out));
  not not_21 (not_21_out, decoder_3_out0);
  not not_22 (not_22_out, decoder_3_out1);
  // NOT_Gate not_23 has open pins: in=decoder_3_out2, out=open
  // NOT_Gate not_24 has open pins: in=decoder_3_out3, out=open
  // NOT_Gate not_25 has open pins: in=decoder_3_out4, out=open
  // NOT_Gate not_26 has open pins: in=decoder_3_out5, out=open
  // NOT_Gate not_27 has open pins: in=decoder_3_out6, out=open
  // NOT_Gate not_28 has open pins: in=decoder_3_out7, out=open
  Decoder #(.select(3)) decoder_3 (
    .out0(decoder_3_out0), .out1(decoder_3_out1), .out2(decoder_3_out2), .out3(decoder_3_out3),
    .out4(decoder_3_out4), .out5(decoder_3_out5), .out6(decoder_3_out6), .out7(decoder_3_out7),
    .sel({in_3, in_4, in_5}), .en(not_4_out));
  LED LDF (.in(nand_2_out));
  nand nand_2 (nand_2_out, in_1, not_10_out);
  LED S3MSB (.in(not_22_out));
  LED LDS2 (.in(nand_3_out));
  LED LDS1 (.in(nand_4_out));
  nand nand_3 (nand_3_out, in_1, not_9_out);
  nand nand_4 (nand_4_out, in_1, not_8_out);
  LED S3LSB (.in(not_21_out));
  LED S3O (.in(not_20_out));
  LED LDD (.in(nand_5_out));
  nand nand_5 (nand_5_out, in_1, not_7_out);
  LED F0 (.in(not_19_out));
  LED LDC (.in(nand_6_out));
  nand nand_6 (nand_6_out, in_1, not_6_out);
  LED S1S2O (.in(not_18_out));
  LED S2O (.in(not_17_out));
  LED S1O (.in(not_16_out));
  LED DO (.in(not_15_out));
  LED CO (.in(not_14_out));
endmodule
