// Logisim project InstructionRegister_Step_2022.circ as structural Verilog: 3 circuits, main circuit main
module main (
  input  INSTRUCTION_REG_IN_low,
  input  CPU_INT_low,
  input  RESET_low,
  input  [7:0] DATA_BUS,
  input  RESET_STEP_low
);

  wire and_1_out, and_2_out, clock_1_out, not_1_out, not_2_out, not_3_out, or_1_out, or_2_out;
  wire [3:0] step_counter_1_step;
  wire [7:0] controlled_buffer_1_out;

  Clock clock_1 (.out(clock_1_out));
  not not_1 (not_1_out, or_2_out);
  assign controlled_buffer_1_out = not_2_out ? DATA_BUS : 8'bz;  // Controlled_Buffer controlled_buffer_1
  not not_2 (not_2_out, not_1_out);
  assign controlled_buffer_1_out = not_3_out ? {{7{1'b1}}, RESET_low} : 8'bz;  // Controlled_Buffer controlled_buffer_2
  not not_3 (not_3_out, or_2_out);
  and and_1 (and_1_out, INSTRUCTION_REG_IN_low, or_2_out);
  and and_2 (and_2_out, CPU_INT_low, RESET_low);
  STEP_COUNTER step_counter_1 (.RESET_low(RESET_STEP_low), .CLOCK(clock_1_out), .STEP(step_counter_1_step));
  or or_1 (or_1_out, step_counter_1_step[0], step_counter_1_step[1], step_counter_1_step[2], step_counter_1_step[3]);
  // LedBar #(.inputtype("row"), .matrixcols(4)) ledbar_1: pin names not known; wires that end beside it: step_counter_1_step
  LED ZERO_FLAG (.in(or_1_out));
  or or_2 (or_2_out, and_2_out, or_1_out);
  // LedBar #(.inputtype("row")) ledbar_2: pin names not known
  Instruction_Register instruction_register_1 (
    .Data_In(controlled_buffer_1_out), .LATCH_low(and_1_out), .Clock(clock_1_out), .Reset(1'b1));  // open: Q
  LED LOAD_INT_VECTOR (.in(or_2_out));

  // Notes on the sheet:
  //   RESET_STEP_low: pull=up
  //   Int Req Address
endmodule

module STEP_COUNTER (
  input  RESET_low,
  input  CLOCK,
  output [3:0] STEP
);

  wire n74161_1_pin1, n74161_1_pin2, n74161_1_pin3;

  _74161 u_74161_1 (
    .pin1(n74161_1_pin1), .pin2(n74161_1_pin2), .pin3(n74161_1_pin3), .pin4(n74161_1_pin3),
    .pin5(n74161_1_pin3), .pin6(n74161_1_pin3), .pin7(n74161_1_pin1), .pin14(STEP[0]), .pin13(STEP[1]),
    .pin12(STEP[2]), .pin11(STEP[3]), .pin10(n74161_1_pin1), .pin9(RESET_low));  // open: pin15
  nand nand_1 (n74161_1_pin2, CLOCK, CLOCK);
  // also tied to GND on the sheet: n74161_1_pin3
  // also tied to VCC on the sheet: n74161_1_pin1

  // Notes on the sheet:
  //   CLOCK: pull=up
  //   RESET_low: pull=up
endmodule

module Instruction_Register (
  input  [7:0] Data_In,
  input  LATCH_low,
  input  Clock,
  input  Reset,
  output [7:0] Q
);

  wire not_1_out, not_2_out;

  not not_1 (not_1_out, LATCH_low);
  Register register_1 (.D(Data_In), .en(not_1_out), .clk(Clock), .Q(Q), .clr(not_2_out));
  not not_2 (not_2_out, Reset);

  // Notes on the sheet:
  //   LATCH_low: pull=up
  //   Clock: pull=up
  //   Reset: pull=down
endmodule
