// Logisim project Intercom.circ as structural Verilog: 2 circuits, main circuit main
module main (
);

  wire button_1_out, button_2_out, button_3_out, button_4_out, button_5_out, button_6_out, button_7_out,
       button_8_out, button_9_out, button_10_out, button_11_out, button_12_out, button_13_out, button_14_out,
       button_15_out, button_16_out, zone_1_audio_out_all, zone_1_audio_out_za, zone_1_audio_out_zb,
       zone_1_audio_out_zc, zone_1_busy_out, zone_2_audio_out_all, zone_2_audio_out_za, zone_2_busy_out,
       zone_3_audio_out_all, zone_3_busy_out, zone_4_audio_out_all, zone_4_busy_out;

  Button button_1 (.out(button_1_out));
  Button button_2 (.out(button_2_out));
  Button button_3 (.out(button_3_out));
  Button button_4 (.out(button_4_out));
  Zone zone_1 (
    .ZA_BUSY_IN(zone_2_busy_out), .ZB_BUSY_IN(zone_3_busy_out), .ZC_BUSY_IN(zone_4_busy_out),
    .PTT_ZA(button_4_out), .PTT_ZB(button_3_out), .PTT_ZC(button_2_out), .AUDIO_IN_L(button_1_out),
    .AUDIO_IN_R(zone_2_audio_out_za), .BUSY_OUT(zone_1_busy_out), .AUDIO_OUT_ZA(zone_1_audio_out_za),
    .AUDIO_OUT_ZB(zone_1_audio_out_zb), .AUDIO_OUT_ZC(zone_1_audio_out_zc),
    .AUDIO_OUT_ALL(zone_1_audio_out_all));
  Button button_5 (.out(button_5_out));
  Button button_6 (.out(button_6_out));
  Button button_7 (.out(button_7_out));
  Button button_8 (.out(button_8_out));
  Zone zone_2 (
    .ZA_BUSY_IN(zone_1_busy_out), .ZB_BUSY_IN(zone_3_busy_out), .ZC_BUSY_IN(zone_4_busy_out),
    .PTT_ZA(button_8_out), .PTT_ZB(button_7_out), .PTT_ZC(button_6_out), .AUDIO_IN_L(button_5_out),
    .AUDIO_IN_R(zone_1_audio_out_za), .BUSY_OUT(zone_2_busy_out), .AUDIO_OUT_ZA(zone_2_audio_out_za),
    .AUDIO_OUT_ZB(zone_1_audio_out_zb), .AUDIO_OUT_ZC(zone_1_audio_out_zc),
    .AUDIO_OUT_ALL(zone_2_audio_out_all));
  Button button_9 (.out(button_9_out));
  Button button_10 (.out(button_10_out));
  Button button_11 (.out(button_11_out));
  Button button_12 (.out(button_12_out));
  Zone zone_3 (
    .ZA_BUSY_IN(zone_1_busy_out), .ZB_BUSY_IN(zone_2_busy_out), .ZC_BUSY_IN(zone_4_busy_out),
    .PTT_ZA(button_12_out), .PTT_ZB(button_11_out), .PTT_ZC(button_10_out), .AUDIO_IN_L(button_9_out),
    .AUDIO_IN_R(zone_1_audio_out_zb), .BUSY_OUT(zone_3_busy_out), .AUDIO_OUT_ZA(zone_2_audio_out_za),
    .AUDIO_OUT_ZB(zone_1_audio_out_za), .AUDIO_OUT_ZC(zone_1_audio_out_zc),
    .AUDIO_OUT_ALL(zone_3_audio_out_all));
  Button button_13 (.out(button_13_out));
  Button button_14 (.out(button_14_out));
  Button button_15 (.out(button_15_out));
  Button button_16 (.out(button_16_out));
  Zone zone_4 (
    .ZA_BUSY_IN(zone_1_busy_out), .ZB_BUSY_IN(zone_2_busy_out), .ZC_BUSY_IN(zone_3_busy_out),
    .PTT_ZA(button_16_out), .PTT_ZB(button_15_out), .PTT_ZC(button_14_out), .AUDIO_IN_L(button_13_out),
    .AUDIO_IN_R(zone_1_audio_out_zc), .BUSY_OUT(zone_4_busy_out), .AUDIO_OUT_ZA(zone_2_audio_out_za),
    .AUDIO_OUT_ZB(zone_1_audio_out_za), .AUDIO_OUT_ALL(zone_4_audio_out_all));  // open: AUDIO_OUT_ZC
endmodule

module Zone (
  input  ZA_BUSY_IN,
  input  ZB_BUSY_IN,
  input  ZC_BUSY_IN,
  input  PTT_ZA,
  input  PTT_ZB,
  input  PTT_ZC,
  input  AUDIO_IN_L,
  input  AUDIO_IN_R,
  output BUSY_OUT,
  output AUDIO_OUT_ZA,
  output AUDIO_OUT_ZB,
  output AUDIO_OUT_ZC,
  output AUDIO_OUT_ALL
);

  wire not_1_out, not_3_out, or_1_out, or_2_out, or_3_out;

  LED led_1 (.in(ZA_BUSY_IN));
  LED led_2 (.in(ZB_BUSY_IN));
  LED led_3 (.in(ZC_BUSY_IN));
  LED led_4 (.in(BUSY_OUT));
  not not_1 (not_1_out, or_1_out);
  or or_1 (or_1_out, PTT_ZA, PTT_ZB, PTT_ZC);
  Pull_Resistor pull_resistor_1 (.node(ZA_BUSY_IN));
  Pull_Resistor pull_resistor_2 (.node(ZB_BUSY_IN));
  Pull_Resistor pull_resistor_3 (.node(ZC_BUSY_IN));
  LED led_5 (.in(not_1_out));
  LED led_6 (.in(PTT_ZA));
  or or_2 (or_2_out, ZA_BUSY_IN, ZB_BUSY_IN, ZC_BUSY_IN);
  LED led_7 (.in(PTT_ZB));
  LED led_8 (.in(PTT_ZC));
  or or_3 (or_3_out, or_2_out, not_1_out);
  not not_2 (BUSY_OUT, or_3_out);
  LED ENABLE_MIC (.in(or_3_out));
  not not_3 (not_3_out, or_3_out);
  Decoder #(.select(3)) decoder_1 (
    .out1(AUDIO_OUT_ZA), .out2(AUDIO_OUT_ZB), .out4(AUDIO_OUT_ZC), .out7(AUDIO_OUT_ALL),
    .sel({PTT_ZC, PTT_ZB, PTT_ZA}), .en(not_3_out));  // open: out0, out3, out5, out6
  LED led_9 (.in(AUDIO_OUT_ZA));
  LED led_10 (.in(AUDIO_OUT_ZB));
  LED led_11 (.in(AUDIO_OUT_ZC));
  LED led_12 (.in(AUDIO_OUT_ALL));

  // Notes on the sheet:
  //   PTT_ZA: pull=down
  //   PTT_ZB: pull=down
  //   PTT_ZC: pull=down
  //   AUDIO_IN_L: pull=down
  //   AUDIO_IN_R: pull=down
  //   BUSY
  //   REQ_LOW
  //   Z2
  //   Z4
  //   Z3
endmodule
