// Logisim project Microcode_EEPROM_Address.circ as structural Verilog: 4 circuits, main circuit Op_Counter
module main (
  input  IRQ,
  input  [7:0] in_2,
  input  CLR_IRQ,
  input  [7:0] in_4,
  input  CLR_TIMER_INT,
  input  SET_TIMER,
  input  [7:0] DATA_BUS,
  input  RESET_OP_COUNTER,
  input  INSTRUCTION_IN,
  output [11:0] CURRENT_INSTRUCTION
);

  wire and_1_out, and_2_out, clock_1_out, nand_1_out, nand_2_out, not_1_out, not_2_out, not_3_out, not_4_out,
       op_counter_1_zero_flag, timer_interupt_1_timer_intr;
  wire [7:0] multiplexer_1_out, register_1_q;

  Clock clock_1 (.out(clock_1_out));
  not not_1 (not_1_out, clock_1_out);
  nand nand_1 (nand_1_out, IRQ, nand_2_out);
  nand nand_2 (nand_2_out, nand_1_out, CLR_IRQ);
  LED led_1 (.in(nand_2_out));
  Timer_Interupt timer_interupt_1 (
    .CLOCK(clock_1_out), .CLEAR_TIMER_INT(CLR_TIMER_INT), .SET_TIMER_FREQ(SET_TIMER), .BUS_DATA(DATA_BUS),
    .TIMER_INTR(timer_interupt_1_timer_intr));
  LED led_2 (.in(op_counter_1_zero_flag));
  Op_Counter op_counter_1 (
    .RESET_OP_COUNTER(RESET_OP_COUNTER), .CLOCK(not_1_out), .CUR_STEP(CURRENT_INSTRUCTION[3:0]),
    .ZERO_FLAG(op_counter_1_zero_flag));
  Instruction_Register instruction_register_1 (
    .DATA_IN(DATA_BUS), .LOAD(INSTRUCTION_IN), .CLOCK(clock_1_out), .INSTRUCTION(CURRENT_INSTRUCTION[11:4]));
  LED led_3 (.in(timer_interupt_1_timer_intr));
  // LedBar #(.inputtype("row"), .matrixcols(4)) ledbar_1: pin names not known; wires that end beside it: CURRENT_INSTRUCTION[3:0]
  Multiplexer #(.enable("true"), .width(8)) multiplexer_1 (
    .in0(in_4), .in1(in_2), .out(multiplexer_1_out), .sel(timer_interupt_1_timer_intr), .en(not_2_out));
  not not_2 (not_2_out, and_1_out);
  and and_1 (and_1_out, nand_2_out, timer_interupt_1_timer_intr);
  // LedBar #(.inputtype("row")) ledbar_2: pin names not known; wires that end beside it: multiplexer_1_out
  not not_3 (not_3_out, op_counter_1_zero_flag);
  and and_2 (and_2_out, and_1_out, not_3_out);
  Register register_1 (
    .D(multiplexer_1_out), .en(not_4_out), .clk(op_counter_1_zero_flag), .Q(register_1_q));  // open: clr
  not not_4 (not_4_out, and_2_out);
  // LedBar #(.inputtype("row"), .matrixcols(12)) ledbar_3: pin names not known; wires that end beside it: CURRENT_INSTRUCTION
  // LedBar #(.inputtype("row")) ledbar_4: pin names not known; wires that end beside it: register_1_q

  // Notes on the sheet:
  //   IRQ: pull=up
  //   CLR_IRQ: pull=up
  //   CLR_TIMER_INT: pull=up
  //   SET_TIMER: pull=up
  //   DATA_BUS: pull=down
  //   RESET_OP_COUNTER: pull=up
  //   INSTRUCTION_IN: pull=up
  //   ACTIVE LOW
  //   ACTIVE LOW
endmodule

module Op_Counter (
  input  RESET_OP_COUNTER,
  input  CLOCK,
  output [3:0] CUR_STEP,
  output ZERO_FLAG
);

  wire n74161_1_pin1, n74161_1_pin2, n74161_1_pin3, n74161_1_pin7, n74161_1_pin15, or_1_out;

  // NoConnect on n74161_1_pin15
  _74161 u_74161_1 (
    .pin1(n74161_1_pin1), .pin2(n74161_1_pin2), .pin3(n74161_1_pin3), .pin4(n74161_1_pin3),
    .pin5(n74161_1_pin3), .pin6(n74161_1_pin3), .pin7(n74161_1_pin7), .pin15(n74161_1_pin15),
    .pin14(CUR_STEP[0]), .pin13(CUR_STEP[1]), .pin12(CUR_STEP[2]), .pin11(CUR_STEP[3]),
    .pin10(n74161_1_pin7), .pin9(RESET_OP_COUNTER));
  not not_1 (n74161_1_pin2, CLOCK);
  // LedBar #(.inputtype("row"), .matrixcols(4)) ledbar_1: pin names not known; wires that end beside it: CUR_STEP
  or or_1 (or_1_out, CUR_STEP[0], CUR_STEP[1], CUR_STEP[2], CUR_STEP[3]);
  nand nand_1 (ZERO_FLAG, or_1_out, or_1_out);
  // also tied to GND on the sheet: n74161_1_pin3
  // also tied to VCC on the sheet: {n74161_1_pin1, n74161_1_pin7}

  // Notes on the sheet:
  //   RESET_OP_COUNTER: pull=up
  //   CLOCK: pull=up
  //   ACTIVE LOW
endmodule

module Instruction_Register (
  input  [7:0] DATA_IN,
  input  LOAD,
  input  CLOCK,
  output [7:0] INSTRUCTION
);

  wire not_1_out;

  Register InstructionRegister (.D(DATA_IN), .en(not_1_out), .clk(CLOCK), .Q(INSTRUCTION), .clr(1'b0));
  not not_1 (not_1_out, LOAD);
endmodule

module Timer_Interupt (
  input  CLOCK,
  input  CLEAR_TIMER_INT,
  input  SET_TIMER_FREQ,
  input  [7:0] BUS_DATA,
  output TIMER_INTR
);

  wire counter_1_carry, n74161_1_pin1, n74161_1_pin3, n74161_1_pin7, n74161_1_pin13, nand_2_out, not_1_out,
       not_2_out, or_1_out;
  wire [7:0] counter_1_q, TIMER_REGISTER_q;

  _74161 u_74161_1 (
    .pin1(n74161_1_pin1), .pin2(CLOCK), .pin3(n74161_1_pin3), .pin4(n74161_1_pin3), .pin5(n74161_1_pin3),
    .pin6(n74161_1_pin3), .pin7(n74161_1_pin7), .pin13(n74161_1_pin13), .pin10(n74161_1_pin7),
    .pin9(n74161_1_pin7));  // open: pin15, pin14, pin12, pin11
  Register TIMER_REGISTER (.D(BUS_DATA), .en(not_1_out), .clk(CLOCK), .Q(TIMER_REGISTER_q), .clr(1'b0));
  not not_1 (not_1_out, SET_TIMER_FREQ);
  not not_2 (not_2_out, n74161_1_pin13);
  Counter counter_1 (
    .clr(1'b0), .load(counter_1_carry), .up(1'b0), .count(1'b1), .clk(not_2_out), .D(TIMER_REGISTER_q),
    .carry(counter_1_carry), .Q(counter_1_q));
  // LedBar #(.inputtype("row")) ledbar_1: pin names not known; wires that end beside it: counter_1_q
  or or_1 (or_1_out, counter_1_q[0], counter_1_q[1], counter_1_q[2], counter_1_q[3], counter_1_q[4], counter_1_q[5], counter_1_q[6], counter_1_q[7]);
  nand nand_1 (TIMER_INTR, CLEAR_TIMER_INT, nand_2_out);
  nand nand_2 (nand_2_out, TIMER_INTR, or_1_out);
  // also tied to GND on the sheet: n74161_1_pin3
  // also tied to VCC on the sheet: {n74161_1_pin1, n74161_1_pin7}

  // Notes on the sheet:
  //   CLEAR_TIMER_INT: pull=down
  //   SET_TIMER_FREQ: pull=down
  //   CLOCK: pull=down
  //   BUS_DATA: pull=down
  //   ACTIVE LOW
  //   ACTIVE LOW
endmodule
