// Logisim project Midi.circ as structural Verilog: 1 circuit, main circuit main
module main (
);

  wire and_1_out, and_2_out, and_3_out, and_4_out, clock_1_out, clock_2_out, n74161_1_pin1, n74161_1_pin2,
       n74161_1_pin7, n74161_1_pin10, n74161_1_pin14, n74161_2_pin1, n74161_2_pin2, n74161_2_pin7,
       n74161_2_pin10, n74161_2_pin14, not_1_out, not_2_out, not_3_out, not_4_out, not_5_out,
       ttl_74ls169_1_co;
  wire [3:0] ttl_74ls169_1_q, ttl_74ls169_2_q, xor_1_out;

  Clock clock_1 (.out(clock_1_out));
  Clock clock_2 (.out(clock_2_out));
  _74161 u_74161_1 (
    .pin1(n74161_1_pin1), .pin2(n74161_1_pin2), .pin7(n74161_1_pin7), .pin14(n74161_1_pin14),
    .pin10(n74161_1_pin10), .pin9(n74161_1_pin10));  // open: pin3, pin4, pin5, pin6, pin15, pin13, pin12, pin11
  TTL_74LS169 ttl_74ls169_1 (
    .UP_DOWN(n74161_2_pin14), .LOAD(1'b1), .ENP(1'b0), .ENT(1'b0), .CLOCK(clock_1_out), .Data_In(4'b0000),
    .Q(ttl_74ls169_1_q), .CO(ttl_74ls169_1_co));
  // NoConnect on ttl_74ls169_1_co
  LED led_1 (.in(n74161_1_pin14));
  // LedBar #(.inputtype("row"), .matrixcols(4)) ledbar_1: pin names not known; wires that end beside it: ttl_74ls169_1_q
  not not_1 (not_1_out, ttl_74ls169_1_q[0]);
  not not_2 (not_2_out, n74161_2_pin14);
  TTL_74LS169 ttl_74ls169_2 (
    .UP_DOWN(1'b0), .LOAD(1'b1), .ENP(1'b0), .ENT(1'b0), .CLOCK(clock_2_out), .Data_In(4'b0000),
    .Q(ttl_74ls169_2_q), .CO(n74161_1_pin2));
  LED led_2 (.in(n74161_2_pin14));
  _74161 u_74161_2 (
    .pin1(n74161_2_pin1), .pin2(n74161_2_pin2), .pin7(n74161_2_pin7), .pin14(n74161_2_pin14),
    .pin10(n74161_2_pin10), .pin9(n74161_2_pin10));  // open: pin3, pin4, pin5, pin6, pin15, pin13, pin12, pin11
  and and_1 (and_1_out, not_1_out, ttl_74ls169_1_q[1], ttl_74ls169_1_q[2], ttl_74ls169_1_q[3]);
  not not_3 (not_3_out, ttl_74ls169_1_q[1]);
  and and_2 (and_2_out, ttl_74ls169_1_q[0], not_3_out, not_4_out, not_5_out);
  not not_4 (not_4_out, ttl_74ls169_1_q[2]);
  not not_5 (not_5_out, ttl_74ls169_1_q[3]);
  and and_3 (and_3_out, and_1_out, not_2_out);
  xor xor_1 (xor_1_out[0], ttl_74ls169_2_q[0], n74161_1_pin14);
  xor xor_2 (xor_1_out[1], ttl_74ls169_2_q[1], n74161_1_pin14);
  xor xor_3 (xor_1_out[2], ttl_74ls169_2_q[2], n74161_1_pin14);
  xor xor_4 (xor_1_out[3], ttl_74ls169_2_q[3], n74161_1_pin14);
  or or_1 (n74161_2_pin2, and_3_out, and_4_out);
  and and_4 (and_4_out, and_2_out, n74161_2_pin14);
  // LedBar #(.inputtype("row"), .matrixcols(4)) ledbar_2: pin names not known; wires that end beside it: ttl_74ls169_2_q
  // LedBar #(.inputtype("row"), .matrixcols(4)) ledbar_3: pin names not known; wires that end beside it: xor_1_out
  // also tied to VCC on the sheet: {n74161_1_pin1, n74161_1_pin7, n74161_1_pin10, n74161_2_pin1, n74161_2_pin7, n74161_2_pin10}
endmodule
