// Logisim project TTL_Ram_Circuit.circ as structural Verilog: 4 circuits, main circuit main
module main (
);

  wire OE_out, twobitdecoder_1_e0, twobitdecoder_1_e1, twobitdecoder_1_e2, twobitdecoder_1_e3, WR_out;
  wire [1:0] dipswitch_1_sw2;
  wire [7:0] dipswitch_2_sw8;

  DipSwitch #(.number(2)) dipswitch_1 (.sw1(dipswitch_1_sw2[1]), .sw2(dipswitch_1_sw2[0]));
  DipSwitch dipswitch_2 (
    .sw1(dipswitch_2_sw8[7]), .sw2(dipswitch_2_sw8[6]), .sw3(dipswitch_2_sw8[5]), .sw4(dipswitch_2_sw8[4]),
    .sw5(dipswitch_2_sw8[3]), .sw6(dipswitch_2_sw8[2]), .sw7(dipswitch_2_sw8[1]), .sw8(dipswitch_2_sw8[0]));
  Button WR (.out(WR_out));
  Button OE (.out(OE_out));
  TwoBitDecoder twobitdecoder_1 (
    .ADR(dipswitch_1_sw2), .E3(twobitdecoder_1_e3), .E2(twobitdecoder_1_e2), .E1(twobitdecoder_1_e1),
    .E0(twobitdecoder_1_e0));
  // LedBar #(.inputtype("row")) ledbar_1: pin names not known
  Eight_Bit_Memory eight_bit_memory_1 (
    .DATA(dipswitch_2_sw8), .EN(twobitdecoder_1_e0), .CP(WR_out), .OE(OE_out));  // open: Q
  // LedBar #(.inputtype("row")) ledbar_2: pin names not known
  Eight_Bit_Memory eight_bit_memory_2 (
    .DATA(dipswitch_2_sw8), .EN(twobitdecoder_1_e1), .CP(WR_out), .OE(OE_out));  // open: Q
  // LedBar #(.inputtype("row")) ledbar_3: pin names not known
  Eight_Bit_Memory eight_bit_memory_3 (
    .DATA(dipswitch_2_sw8), .EN(twobitdecoder_1_e2), .CP(WR_out), .OE(OE_out));  // open: Q
  // LedBar #(.inputtype("row")) ledbar_4: pin names not known
  Eight_Bit_Memory eight_bit_memory_4 (
    .DATA(dipswitch_2_sw8), .EN(twobitdecoder_1_e3), .CP(WR_out), .OE(OE_out));  // open: Q
endmodule

module OneBitMemory (
  input  D,
  input  CP,
  input  EN,
  output Q
);

  wire and_1_out, nand_1_out, nand_2_out, nand_3_out, nand_5_out;

  and and_1 (and_1_out, CP, EN);
  nand nand_1 (nand_1_out, D, and_1_out);
  nand nand_2 (nand_2_out, and_1_out, nand_3_out);
  nand nand_3 (nand_3_out, D, D);
  nand nand_4 (Q, nand_1_out, nand_5_out);
  nand nand_5 (nand_5_out, Q, nand_2_out);
endmodule

module Eight_Bit_Memory (
  input  [7:0] DATA,
  input  EN,
  input  CP,
  input  OE,
  output [7:0] Q
);

  wire and_1_out, onebitmemory_1_q, onebitmemory_2_q, onebitmemory_3_q, onebitmemory_4_q, onebitmemory_5_q,
       onebitmemory_6_q, onebitmemory_7_q, onebitmemory_8_q;

  and and_1 (and_1_out, EN, OE);
  OneBitMemory onebitmemory_1 (.D(DATA[0]), .CP(CP), .EN(EN), .Q(onebitmemory_1_q));
  OneBitMemory onebitmemory_2 (.D(DATA[1]), .CP(CP), .EN(EN), .Q(onebitmemory_2_q));
  OneBitMemory onebitmemory_3 (.D(DATA[2]), .CP(CP), .EN(EN), .Q(onebitmemory_3_q));
  OneBitMemory onebitmemory_4 (.D(DATA[3]), .CP(CP), .EN(EN), .Q(onebitmemory_4_q));
  OneBitMemory onebitmemory_5 (.D(DATA[4]), .CP(CP), .EN(EN), .Q(onebitmemory_5_q));
  OneBitMemory onebitmemory_6 (.D(DATA[5]), .CP(CP), .EN(EN), .Q(onebitmemory_6_q));
  OneBitMemory onebitmemory_7 (.D(DATA[6]), .CP(CP), .EN(EN), .Q(onebitmemory_7_q));
  OneBitMemory onebitmemory_8 (.D(DATA[7]), .CP(CP), .EN(EN), .Q(onebitmemory_8_q));
  assign Q[0] = and_1_out ? onebitmemory_1_q : 1'bz;  // Controlled_Buffer controlled_buffer_1
  assign Q[1] = and_1_out ? onebitmemory_2_q : 1'bz;  // Controlled_Buffer controlled_buffer_2
  assign Q[2] = and_1_out ? onebitmemory_3_q : 1'bz;  // Controlled_Buffer controlled_buffer_3
  assign Q[3] = and_1_out ? onebitmemory_4_q : 1'bz;  // Controlled_Buffer controlled_buffer_4
  assign Q[4] = and_1_out ? onebitmemory_5_q : 1'bz;  // Controlled_Buffer controlled_buffer_5
  assign Q[5] = and_1_out ? onebitmemory_6_q : 1'bz;  // Controlled_Buffer controlled_buffer_6
  assign Q[6] = and_1_out ? onebitmemory_7_q : 1'bz;  // Controlled_Buffer controlled_buffer_7
  assign Q[7] = and_1_out ? onebitmemory_8_q : 1'bz;  // Controlled_Buffer controlled_buffer_8
endmodule

module TwoBitDecoder (
  input  [1:0] ADR,
  output E3,
  output E2,
  output E1,
  output E0
);

  wire not_1_out, not_2_out;

  not not_1 (not_1_out, ADR[1]);
  not not_2 (not_2_out, ADR[0]);
  and and_1 (E0, not_1_out, not_2_out);
  and and_2 (E1, not_1_out, ADR[0]);
  and and_3 (E2, ADR[1], not_2_out);
  and and_4 (E3, ADR[0], ADR[1]);
endmodule
