// Logisim project UART.circ as structural Verilog: 1 circuit, main circuit main
module main (
);

  wire clock_1_out, nand_1_out, nand_2_out, SERIAL_DATA_out, ttl_74ls193_1_bo, ttl_74ls193_2_bo,
       ttl_74ls193_2_co, ttl_74ls193_2_q1, ttl_74ls193_2_q2, ttl_74ls193_2_q3, ttl_74ls193_2_qo;

  Clock clock_1 (.out(clock_1_out));
  Button #(.press("passive")) SERIAL_DATA (.out(SERIAL_DATA_out));
  TTL_74LS193 ttl_74ls193_1 (.BO(ttl_74ls193_1_bo));  // open: P3, P2, P1, P0, LOAD, UP, DOWN, CLEAR, Q3, Q2, Q1, QO, CO
  TTL_74LS193 ttl_74ls193_2 (
    .P3(1'b0), .P2(1'b0), .P1(1'b0), .P0(1'b0), .LOAD(1'b1), .UP(clock_1_out), .DOWN(1'b1),
    .CLEAR(nand_1_out), .Q3(ttl_74ls193_2_q3), .Q2(ttl_74ls193_2_q2), .Q1(ttl_74ls193_2_q1),
    .QO(ttl_74ls193_2_qo), .CO(ttl_74ls193_2_co), .BO(ttl_74ls193_2_bo));
  // NoConnect on ttl_74ls193_2_q2
  // NoConnect on ttl_74ls193_2_q1
  // NoConnect on ttl_74ls193_2_qo
  // NoConnect on ttl_74ls193_2_co
  // NoConnect on ttl_74ls193_2_bo
  nand nand_1 (nand_1_out, ttl_74ls193_1_bo, nand_2_out);
  nand nand_2 (nand_2_out, nand_1_out, SERIAL_DATA_out);
endmodule
