// Logisim project Up_Down_Counter.circ as structural Verilog: 1 circuit, main circuit main
module main (
);

  wire and_1_out, and_2_out, clock_1_out, j_k_ff_1_q, j_k_ff_1_qn, j_k_ff_2_q, j_k_ff_2_qn, j_k_ff_3_q,
       j_k_ff_3_qn, j_k_ff_4_q, j_k_ff_4_qn, j_k_ff_5_q, j_k_ff_5_qn, j_k_ff_6_q, j_k_ff_6_qn, j_k_ff_7_q,
       j_k_ff_7_qn, j_k_ff_8_q, j_k_ff_8_qn, j_k_ff_9_q, j_k_ff_9_qn, j_k_ff_10_q, j_k_ff_10_qn, j_k_ff_11_q,
       j_k_ff_11_qn, j_k_ff_12_q, j_k_ff_12_qn, j_k_ff_13_q, j_k_ff_13_qn, j_k_ff_14_q, j_k_ff_14_qn,
       j_k_ff_15_q, j_k_ff_15_qn, j_k_ff_16_q, j_k_ff_17_q, j_k_ff_18_q, nand_1_out, nand_2_out, nand_3_out,
       not_1_out, not_2_out, not_3_out, not_4_out, not_5_out, not_6_out, not_7_out, not_8_out, not_9_out,
       not_10_out, not_11_out, not_12_out, not_13_out, not_14_out, not_15_out, not_16_out, not_17_out,
       not_18_out;

  Clock clock_1 (.out(clock_1_out));
  J_K_Flip_Flop j_k_ff_1 (
    .J(1'b1), .K(1'b1), .clk(clock_1_out), .Q(j_k_ff_1_q), .Qn(j_k_ff_1_qn), .reset(not_1_out));  // open: preset
  not not_1 (not_1_out, nand_1_out);
  J_K_Flip_Flop j_k_ff_2 (
    .J(1'b1), .K(1'b1), .clk(and_1_out), .Q(j_k_ff_2_q), .Qn(j_k_ff_2_qn), .reset(not_2_out));  // open: preset
  not not_2 (not_2_out, nand_2_out);
  J_K_Flip_Flop j_k_ff_3 (
    .J(1'b1), .K(1'b1), .clk(and_2_out), .Q(j_k_ff_3_q), .Qn(j_k_ff_3_qn), .reset(not_3_out));  // open: preset
  not not_3 (not_3_out, nand_3_out);
  LED led_1 (.in(j_k_ff_1_q));
  J_K_Flip_Flop j_k_ff_4 (
    .J(1'b1), .K(1'b1), .clk(j_k_ff_1_qn), .Q(j_k_ff_4_q), .Qn(j_k_ff_4_qn), .reset(not_4_out));  // open: preset
  not not_4 (not_4_out, nand_1_out);
  LED led_2 (.in(j_k_ff_2_q));
  J_K_Flip_Flop j_k_ff_5 (
    .J(1'b1), .K(1'b1), .clk(j_k_ff_2_qn), .Q(j_k_ff_5_q), .Qn(j_k_ff_5_qn), .reset(not_5_out));  // open: preset
  not not_5 (not_5_out, nand_2_out);
  LED led_3 (.in(j_k_ff_3_q));
  J_K_Flip_Flop j_k_ff_6 (
    .J(1'b1), .K(1'b1), .clk(j_k_ff_3_qn), .Q(j_k_ff_6_q), .Qn(j_k_ff_6_qn), .reset(not_6_out));  // open: preset
  not not_6 (not_6_out, nand_3_out);
  LED led_4 (.in(j_k_ff_4_q));
  J_K_Flip_Flop j_k_ff_7 (
    .J(1'b1), .K(1'b1), .clk(j_k_ff_4_qn), .Q(j_k_ff_7_q), .Qn(j_k_ff_7_qn), .reset(not_7_out));  // open: preset
  not not_7 (not_7_out, nand_1_out);
  LED led_5 (.in(j_k_ff_5_q));
  J_K_Flip_Flop j_k_ff_8 (
    .J(1'b1), .K(1'b1), .clk(j_k_ff_5_qn), .Q(j_k_ff_8_q), .Qn(j_k_ff_8_qn), .reset(not_8_out));  // open: preset
  not not_8 (not_8_out, nand_2_out);
  LED led_6 (.in(j_k_ff_6_q));
  J_K_Flip_Flop j_k_ff_9 (
    .J(1'b1), .K(1'b1), .clk(j_k_ff_6_qn), .Q(j_k_ff_9_q), .Qn(j_k_ff_9_qn), .reset(not_9_out));  // open: preset
  not not_9 (not_9_out, nand_3_out);
  LED led_7 (.in(j_k_ff_7_q));
  J_K_Flip_Flop j_k_ff_10 (
    .J(1'b1), .K(1'b1), .clk(j_k_ff_7_qn), .Q(j_k_ff_10_q), .Qn(j_k_ff_10_qn), .reset(not_10_out));  // open: preset
  not not_10 (not_10_out, nand_1_out);
  LED led_8 (.in(j_k_ff_8_q));
  J_K_Flip_Flop j_k_ff_11 (
    .J(1'b1), .K(1'b1), .clk(j_k_ff_8_qn), .Q(j_k_ff_11_q), .Qn(j_k_ff_11_qn), .reset(not_11_out));  // open: preset
  not not_11 (not_11_out, nand_2_out);
  LED led_9 (.in(j_k_ff_9_q));
  J_K_Flip_Flop j_k_ff_12 (
    .J(1'b1), .K(1'b1), .clk(j_k_ff_9_qn), .Q(j_k_ff_12_q), .Qn(j_k_ff_12_qn), .reset(not_12_out));  // open: preset
  not not_12 (not_12_out, nand_3_out);
  LED led_10 (.in(j_k_ff_10_q));
  J_K_Flip_Flop j_k_ff_13 (
    .J(1'b1), .K(1'b1), .clk(j_k_ff_10_qn), .Q(j_k_ff_13_q), .Qn(j_k_ff_13_qn), .reset(not_13_out));  // open: preset
  not not_13 (not_13_out, nand_1_out);
  LED led_11 (.in(j_k_ff_11_q));
  J_K_Flip_Flop j_k_ff_14 (
    .J(1'b1), .K(1'b1), .clk(j_k_ff_11_qn), .Q(j_k_ff_14_q), .Qn(j_k_ff_14_qn), .reset(not_14_out));  // open: preset
  not not_14 (not_14_out, nand_2_out);
  LED led_12 (.in(j_k_ff_12_q));
  J_K_Flip_Flop j_k_ff_15 (
    .J(1'b1), .K(1'b1), .clk(j_k_ff_12_qn), .Q(j_k_ff_15_q), .Qn(j_k_ff_15_qn), .reset(not_15_out));  // open: preset
  not not_15 (not_15_out, nand_3_out);
  LED led_13 (.in(j_k_ff_13_q));
  J_K_Flip_Flop j_k_ff_16 (
    .J(1'b1), .K(1'b1), .clk(j_k_ff_13_qn), .Q(j_k_ff_16_q), .reset(not_16_out));  // open: Qn, preset
  not not_16 (not_16_out, nand_1_out);
  LED led_14 (.in(j_k_ff_14_q));
  J_K_Flip_Flop j_k_ff_17 (
    .J(1'b1), .K(1'b1), .clk(j_k_ff_14_qn), .Q(j_k_ff_17_q), .reset(not_17_out));  // open: Qn, preset
  not not_17 (not_17_out, nand_2_out);
  LED led_15 (.in(j_k_ff_15_q));
  J_K_Flip_Flop j_k_ff_18 (
    .J(1'b1), .K(1'b1), .clk(j_k_ff_15_qn), .Q(j_k_ff_18_q), .reset(not_18_out));  // open: Qn, preset
  not not_18 (not_18_out, nand_3_out);
  LED led_16 (.in(j_k_ff_16_q));
  LED led_17 (.in(j_k_ff_17_q));
  LED led_18 (.in(j_k_ff_18_q));
  and and_1 (and_1_out, j_k_ff_16_q, j_k_ff_13_q, j_k_ff_10_q, j_k_ff_7_q);
  nand nand_1 (nand_1_out, and_1_out, j_k_ff_1_q);
  and and_2 (and_2_out, j_k_ff_17_q, j_k_ff_14_q, j_k_ff_11_q, j_k_ff_8_q);
  nand nand_2 (nand_2_out, and_2_out, j_k_ff_2_q);
  nand nand_3 (nand_3_out, j_k_ff_15_q, j_k_ff_12_q, j_k_ff_3_q);

  // Notes on the sheet:
  //   INSTEAD, I THINK I NEED TO and THE CLOCK WITH THE AND GATES
  //   SECONDS
  //   MINUTES
  //   HOURS
  //   111100
  //   (60)
  //   111100
  //   (60)
  //   11000
  //   (24)
endmodule
