// Logisim project VGA.circ as structural Verilog: 3 circuits, main circuit main
module main (
);

  wire clock_1_out, compare_1_equal, compare_2_equal, compare_3_equal, compare_4_equal, s_r_ff_1_q,
       s_r_ff_2_q;
  wire [11:0] dipswitch_1_sw12, timing_counter_1_count;

  Clock clock_1 (.out(clock_1_out));
  DipSwitch #(.number(12)) dipswitch_1 (
    .sw1(dipswitch_1_sw12[11]), .sw2(dipswitch_1_sw12[10]), .sw3(dipswitch_1_sw12[9]),
    .sw4(dipswitch_1_sw12[8]), .sw5(dipswitch_1_sw12[7]), .sw6(dipswitch_1_sw12[6]),
    .sw7(dipswitch_1_sw12[5]), .sw8(dipswitch_1_sw12[4]), .sw9(dipswitch_1_sw12[3]),
    .sw10(dipswitch_1_sw12[2]), .sw11(dipswitch_1_sw12[1]), .sw12(dipswitch_1_sw12[0]));
  TIMING_COUNTER timing_counter_1 (.LOAD(compare_4_equal), .CLOCK(clock_1_out), .COUNT(timing_counter_1_count));
  // LedBar #(.inputtype("row"), .matrixcols(12)) ledbar_1: pin names not known; wires that end beside it: timing_counter_1_count, timing_counter_1_count
  LED led_1 (.in(compare_1_equal));
  COMPARE compare_1 (.COUNT(timing_counter_1_count), .TRIGGER(12'h140), .EQUAL(compare_1_equal));
  LED led_2 (.in(compare_2_equal));
  COMPARE compare_2 (.COUNT(timing_counter_1_count), .TRIGGER(12'h150), .EQUAL(compare_2_equal));
  LED led_3 (.in(compare_3_equal));
  COMPARE compare_3 (.COUNT(timing_counter_1_count), .TRIGGER(12'h1b0), .EQUAL(compare_3_equal));
  LED led_4 (.in(compare_4_equal));
  COMPARE compare_4 (.COUNT(timing_counter_1_count), .TRIGGER(12'h1e0), .EQUAL(compare_4_equal));
  LED led_5 (.in(s_r_ff_1_q));
  S_R_Flip_Flop s_r_ff_1 (
    .S(compare_1_equal), .R(compare_4_equal), .clk(clock_1_out), .Q(s_r_ff_1_q), .reset(1'b0));  // open: Qn, preset
  S_R_Flip_Flop s_r_ff_2 (
    .S(compare_2_equal), .R(compare_3_equal), .clk(clock_1_out), .Q(s_r_ff_2_q), .reset(1'b0));  // open: Qn, preset
  LED led_6 (.in(s_r_ff_2_q));

  // Notes on the sheet:
  //   FRONT PORCH
  //   SYNC
  //   BACKPORCH
  //   VISIBLE AREA
  //   VISIBLE AREA
  //   SYNC PULSE
endmodule

module TIMING_COUNTER (
  input  LOAD,
  input  CLOCK,
  output [11:0] COUNT
);

  wire not_1_out;

  not not_1 (not_1_out, LOAD);
  Counter #(.max('hfff), .width(12)) counter_1 (
    .load(not_1_out), .D({12{1'b0}}), .count(1'b1), .Q(COUNT), .up(1'b1), .clk(CLOCK), .clr(1'b0));  // open: carry
endmodule

module COMPARE (
  input  [11:0] COUNT,
  input  [11:0] TRIGGER,
  output EQUAL
);

  wire comparator_1_eq;

  Comparator #(.width(12)) comparator_1 (.a(COUNT), .b(TRIGGER), .eq(comparator_1_eq));  // open: gt, lt
  not not_1 (EQUAL, comparator_1_eq);
endmodule
