// Logisim project VGA2.circ as structural Verilog: 2 circuits, main circuit main
module main (
);

  wire and_1_out, and_2_out, and_3_out, and_4_out, and_5_out, and_6_out, and_7_out, and_8_out, and_9_out,
       button_1_out, button_2_out, button_3_out, clock_1_out, clock_2_out, d_ff_1_q, d_ff_1_qn, d_ff_2_q,
       d_ff_2_qn, d_ff_3_q, d_ff_3_qn, d_ff_4_q, d_ff_4_qn, d_ff_5_q, n74163_1_pin1, n74163_1_pin3,
       n74163_1_pin7, n74163_1_pin10, n74163_1_pin15, n74163_2_pin3, n74163_2_pin10, n74163_2_pin12,
       n74163_2_pin14, n74163_2_pin15, n74163_3_pin3, n74163_3_pin13, n74163_3_pin14, nand_1_out, nand_2_out,
       nand_4_out, nand_5_out, nand_6_out, not_1_out, not_2_out, not_3_out, not_4_out, not_5_out, not_6_out,
       not_7_out, not_8_out, not_9_out, not_10_out, s_r_ff_1_q, s_r_ff_1_qn, sync_counter_1_flag_16;
  wire [7:0] sync_counter_1_count;
  wire [11:0] counter_1_q;

  Button #(.press("passive")) button_1 (.out(button_1_out));
  Clock clock_1 (.out(clock_1_out));
  not not_1 (not_1_out, button_1_out);
  D_Flip_Flop d_ff_1 (
    .D(and_1_out), .clk(clock_1_out), .Q(d_ff_1_q), .Qn(d_ff_1_qn), .preset(not_1_out), .reset(not_2_out));
  not not_2 (not_2_out, 1'b1);
  _74163 u_74163_1 (
    .pin1(n74163_1_pin1), .pin2(clock_1_out), .pin3(n74163_1_pin3), .pin4(n74163_1_pin3),
    .pin5(n74163_1_pin3), .pin6(n74163_1_pin3), .pin7(n74163_1_pin7), .pin15(n74163_1_pin15),
    .pin10(n74163_1_pin10), .pin9(button_1_out));  // open: pin14, pin13, pin12, pin11
  Button #(.press("passive")) button_2 (.out(button_2_out));
  Button #(.press("passive")) button_3 (.out(button_3_out));
  Clock clock_2 (.out(clock_2_out));
  nand nand_1 (nand_1_out, d_ff_1_qn, d_ff_1_qn, nand_2_out);
  nand nand_2 (nand_2_out, n74163_1_pin15, n74163_2_pin14, n74163_2_pin12);
  _74163 u_74163_2 (
    .pin1(n74163_1_pin1), .pin2(clock_1_out), .pin3(n74163_2_pin3), .pin4(n74163_2_pin3),
    .pin5(n74163_2_pin3), .pin6(n74163_2_pin3), .pin7(n74163_1_pin15), .pin15(n74163_2_pin15),
    .pin14(n74163_2_pin14), .pin12(n74163_2_pin12), .pin10(n74163_2_pin10), .pin9(button_1_out));  // open: pin13, pin11
  and and_1 (and_1_out, nand_1_out, n74163_1_pin1);
  and and_2 (and_2_out, n74163_1_pin15, n74163_2_pin14);
  nand nand_3 (n74163_1_pin1, and_2_out, n74163_3_pin14, n74163_3_pin13);
  _74163 u_74163_3 (
    .pin1(n74163_1_pin1), .pin2(clock_1_out), .pin3(n74163_3_pin3), .pin4(n74163_3_pin3),
    .pin5(n74163_3_pin3), .pin6(n74163_3_pin3), .pin7(n74163_1_pin15), .pin14(n74163_3_pin14),
    .pin13(n74163_3_pin13), .pin10(n74163_2_pin15), .pin9(button_1_out));  // open: pin15, pin12, pin11
  SYNC_COUNTER sync_counter_1 (
    .LOAD(button_2_out), .RESET(button_3_out), .PIXEL_CLOCK(clock_2_out), .FLAG_16(sync_counter_1_flag_16),
    .COUNT(sync_counter_1_count));
  LED HSYNC (.in(d_ff_1_q));
  and and_3 (and_3_out, sync_counter_1_flag_16, sync_counter_1_count[0]);
  nand nand_4 (nand_4_out, and_3_out, sync_counter_1_count[4], sync_counter_1_count[5]);
  and and_4 (and_4_out, sync_counter_1_flag_16, sync_counter_1_count[0]);
  and and_5 (and_5_out, sync_counter_1_count[0], sync_counter_1_count[1]);
  and and_6 (and_6_out, sync_counter_1_count[2], sync_counter_1_count[5]);
  Counter #(.max('hfff), .width(12)) counter_1 (
    .clr(d_ff_4_q), .load(d_ff_4_q), .up(1'b1), .count(1'b1), .clk(d_ff_1_q), .D({12{1'b0}}), .Q(counter_1_q));  // open: carry
  nand nand_5 (nand_5_out, and_4_out, sync_counter_1_count[4], sync_counter_1_count[5]);
  nand nand_6 (nand_6_out, sync_counter_1_flag_16, and_5_out, and_6_out);
  and and_7 (and_7_out, nand_4_out, nand_5_out);
  not not_3 (not_3_out, button_2_out);
  D_Flip_Flop d_ff_2 (
    .D(and_7_out), .clk(clock_2_out), .Q(d_ff_2_q), .Qn(d_ff_2_qn), .preset(not_3_out), .reset(not_4_out));
  not not_4 (not_4_out, 1'b1);
  S_R_Flip_Flop s_r_ff_1 (
    .S(nand_6_out), .R(nand_5_out), .clk(clock_2_out), .Q(s_r_ff_1_q), .reset(1'b0), .Qn(s_r_ff_1_qn),
    .preset(1'b0));
  // LedBar #(.inputtype("row"), .matrixcols(12)) ledbar_1: pin names not known; wires that end beside it: counter_1_q
  LED SYNC_PULSE (.in(d_ff_2_q));
  D_Flip_Flop d_ff_3 (
    .D(and_8_out), .clk(clock_2_out), .Q(d_ff_3_q), .Qn(d_ff_3_qn), .preset(not_5_out), .reset(not_6_out));
  and and_8 (and_8_out, nand_5_out, s_r_ff_1_q);
  and and_9 (and_9_out, counter_1_q[2], counter_1_q[3], counter_1_q[9]);
  not not_5 (not_5_out, button_2_out);
  not not_6 (not_6_out, 1'b1);
  D_Flip_Flop d_ff_4 (
    .D(and_9_out), .clk(d_ff_1_q), .Q(d_ff_4_q), .Qn(d_ff_4_qn), .preset(not_9_out), .reset(not_10_out));
  not not_7 (not_7_out, button_1_out);
  D_Flip_Flop d_ff_5 (.D(1'b1), .clk(d_ff_1_qn), .Q(d_ff_5_q), .preset(not_7_out), .reset(not_8_out));  // open: Qn
  LED VSYNC (.in(d_ff_5_q));
  not not_8 (not_8_out, d_ff_4_qn);
  LED VISIBLE_AREA (.in(d_ff_3_qn));
  not not_9 (not_9_out, button_1_out);
  not not_10 (not_10_out, 1'b1);
  // also tied to GND on the sheet: {n74163_1_pin3, n74163_2_pin3, n74163_3_pin3}
  // also tied to VCC on the sheet: {n74163_1_pin10, n74163_1_pin7, n74163_2_pin10}

  // Notes on the sheet:
  //   SYNC 95
  //   RESET 799
  //   VISIBLE AREA 639
  //   1000001100
endmodule

module SYNC_COUNTER (
  input  LOAD,
  input  RESET,
  input  PIXEL_CLOCK,
  output FLAG_16,
  output [7:0] COUNT
);

  wire n74163_1_pin3, n74163_1_pin7, n74163_1_pin10, n74163_2_pin3, n74163_2_pin10, n74163_2_pin15,
       n74163_3_pin3;

  _74163 u_74163_1 (
    .pin1(RESET), .pin2(PIXEL_CLOCK), .pin3(n74163_1_pin3), .pin4(n74163_1_pin3), .pin5(n74163_1_pin3),
    .pin6(n74163_1_pin3), .pin7(n74163_1_pin7), .pin15(FLAG_16), .pin10(n74163_1_pin10), .pin9(LOAD));  // open: pin14, pin13, pin12, pin11
  _74163 u_74163_2 (
    .pin1(RESET), .pin2(PIXEL_CLOCK), .pin3(n74163_2_pin3), .pin4(n74163_2_pin3), .pin5(n74163_2_pin3),
    .pin6(n74163_2_pin3), .pin7(FLAG_16), .pin15(n74163_2_pin15), .pin14(COUNT[0]), .pin13(COUNT[1]),
    .pin12(COUNT[2]), .pin11(COUNT[3]), .pin10(n74163_2_pin10), .pin9(LOAD));
  _74163 u_74163_3 (
    .pin1(RESET), .pin2(PIXEL_CLOCK), .pin3(n74163_3_pin3), .pin4(n74163_3_pin3), .pin5(n74163_3_pin3),
    .pin6(n74163_3_pin3), .pin7(FLAG_16), .pin14(COUNT[4]), .pin13(COUNT[5]), .pin12(COUNT[6]),
    .pin11(COUNT[7]), .pin10(n74163_2_pin15), .pin9(LOAD));  // open: pin15
  // also tied to GND on the sheet: {n74163_1_pin3, n74163_2_pin3, n74163_3_pin3}
  // also tied to VCC on the sheet: {n74163_1_pin10, n74163_1_pin7, n74163_2_pin10}
endmodule
