// Logisim project VGA_counter_dips.circ as structural Verilog: 2 circuits, main circuit main
module main (
);

  wire buffer_1_out, clock_1_out, presettablecounter_1_zero_flag, presettablecounter_2_zero_flag,
       presettablecounter_3_zero_flag, s_r_ff_1_q, s_r_ff_1_qn, s_r_ff_2_q, s_r_ff_2_qn, undriven;

  Clock clock_1 (.out(clock_1_out));
  buf buffer_1 (buffer_1_out, presettablecounter_3_zero_flag);
  // LedBar #(.inputtype("row"), .matrixcols(4)) ledbar_1: pin names not known
  PresettableCounter presettablecounter_1 (
    .PRELOAD_VALUE(4'b0111), .CLOCK(clock_1_out), .ENABLE(s_r_ff_1_qn), .LOAD_PRESET(s_r_ff_1_q),
    .ZERO_FLAG(presettablecounter_1_zero_flag));  // open: COUNT
  // LedBar #(.inputtype("row"), .matrixcols(4)) ledbar_2: pin names not known
  PresettableCounter presettablecounter_2 (
    .PRELOAD_VALUE(4'b1000), .CLOCK(clock_1_out), .ENABLE(s_r_ff_2_qn), .LOAD_PRESET(s_r_ff_2_q),
    .ZERO_FLAG(presettablecounter_2_zero_flag));  // open: COUNT
  // LedBar #(.inputtype("row"), .matrixcols(4)) ledbar_3: pin names not known
  PresettableCounter presettablecounter_3 (
    .PRELOAD_VALUE(4'b1110), .CLOCK(clock_1_out), .ENABLE(1'b0), .LOAD_PRESET(buffer_1_out),
    .ZERO_FLAG(presettablecounter_3_zero_flag));  // open: COUNT
  S_R_Flip_Flop s_r_ff_1 (
    .S(presettablecounter_1_zero_flag), .R(undriven), .clk(clock_1_out), .Q(s_r_ff_1_q), .Qn(s_r_ff_1_qn));  // open: reset, preset
  S_R_Flip_Flop s_r_ff_2 (
    .S(presettablecounter_2_zero_flag), .R(undriven), .clk(clock_1_out), .Q(s_r_ff_2_q), .Qn(s_r_ff_2_qn));  // open: reset, preset
  LED led_1 (.in(s_r_ff_1_q));
  LED led_2 (.in(s_r_ff_1_qn));
  LED led_3 (.in(s_r_ff_2_q));
  LED led_4 (.in(s_r_ff_2_qn));
endmodule

module PresettableCounter (
  input  [3:0] PRELOAD_VALUE,
  input  CLOCK,
  input  ENABLE,
  input  LOAD_PRESET,
  output [3:0] COUNT,
  output ZERO_FLAG
);

  wire or_1_out, ttl_74ls193_1_co;

  or or_1 (or_1_out, CLOCK, ENABLE);
  TTL_74LS193 ttl_74ls193_1 (
    .P3(PRELOAD_VALUE[3]), .P2(PRELOAD_VALUE[2]), .P1(PRELOAD_VALUE[1]), .P0(PRELOAD_VALUE[0]),
    .LOAD(LOAD_PRESET), .UP(1'b1), .DOWN(or_1_out), .CLEAR(1'b0), .Q3(COUNT[3]), .Q2(COUNT[2]),
    .Q1(COUNT[1]), .QO(COUNT[0]), .CO(ttl_74ls193_1_co), .BO(ZERO_FLAG));
  // NoConnect on ttl_74ls193_1_co
endmodule
