// Logisim project alu_new.circ as structural Verilog: 9 circuits, main circuit main
module main (
  input  FI,
  input  [7:0] in_2,
  input  [7:0] A,
  input  [7:0] B
);

  wire adder_module_1_carry_out, and_1_out, and_2_out, and_3_out, CF_p1, clock_1_out, decoder_1_out0,
       decoder_1_out1, decoder_1_out2, decoder_1_out3, decoder_1_out4, decoder_1_out5, decoder_1_out6,
       decoder_1_out7, not_1_out, not_2_out, not_3_out, not_4_out, not_5_out, not_6_out, not_10_out,
       not_11_out, or_1_out, OVF_p1, SF_p1, shifter_module_1_lco, ZF_p1;
  wire [7:0] and_module_1_and_output, not_module_1_invert_output, Result_p1;

  Clock clock_1 (.out(clock_1_out));
  not not_1 (not_1_out, in_2[3]);
  Decoder #(.select(3)) decoder_1 (
    .out0(decoder_1_out0), .out1(decoder_1_out1), .out2(decoder_1_out2), .out3(decoder_1_out3),
    .out4(decoder_1_out4), .out5(decoder_1_out5), .out6(decoder_1_out6), .out7(decoder_1_out7),
    .sel(in_2[2:0]), .en(in_2[7]));
  and and_1 (and_1_out, in_2[0], not_1_out);
  and and_2 (and_2_out, CF_p1, in_2[3]);
  not not_2 (not_2_out, decoder_1_out0);
  not not_3 (not_3_out, decoder_1_out1);
  not not_4 (not_4_out, decoder_1_out2);
  not not_5 (not_5_out, decoder_1_out3);
  not not_6 (not_6_out, decoder_1_out4);
  // NOT_Gate not_7 has open pins: in=decoder_1_out5, out=open
  // NOT_Gate not_8 has open pins: in=decoder_1_out6, out=open
  // NOT_Gate not_9 has open pins: in=decoder_1_out7, out=open
  not not_10 (not_10_out, in_2[7]);
  or or_1 (or_1_out, and_1_out, and_2_out);
  and and_3 (and_3_out, not_10_out, or_1_out);
  // LedBar #(.inputtype("row")) A_Indicator: pin names not known; wires that end beside it: A
  // LedBar #(.inputtype("row")) B_Indicator: pin names not known; wires that end beside it: B
  // LedBar #(.inputtype("row")) Result: pin names not known; wires that end beside it: Result_p1
  AND_Module and_module_1 (.A(A), .B(B), .AND_OUT(not_2_out), .AND_Output(and_module_1_and_output));
  OR_Module or_module_1 (.A(A), .B(B), .OR_OUT(not_3_out), .OR_Output(and_module_1_and_output));
  XOR_Module xor_module_1 (.A(A), .B(B), .XOR_OUT(not_4_out), .XOR_Output(and_module_1_and_output));
  SHIFTER_Module shifter_module_1 (
    .ROTATE_OUT(not_6_out), .SHIFT_OUT(not_5_out), .SHIFT_SELECT(in_2[5:4]), .A_Data(A),
    .Result(and_module_1_and_output), .LCO(shifter_module_1_lco));
  ADDER_Module adder_module_1 (
    .A(A), .TWOS_COMPLEMENT(in_2[1]), .B(B), .ADDER_MUL_SELECT(in_2[2]), .CARRY_IN(and_3_out),
    .ADDER_OUT(in_2[7]), .Adder_Result(and_module_1_and_output), .CARRY_OUT(adder_module_1_carry_out));
  // LedBar #(.inputtype("row"), .matrixcols(1)) CF: pin names not known; wires that end beside it: CF_p1
  // LedBar #(.inputtype("row"), .matrixcols(1)) OVF: pin names not known; wires that end beside it: OVF_p1
  // LedBar #(.inputtype("row"), .matrixcols(1)) SF: pin names not known; wires that end beside it: SF_p1
  // LedBar #(.inputtype("row"), .matrixcols(1)) ZF: pin names not known; wires that end beside it: ZF_p1
  Flags_Module flags_module_1 (
    .Logical_Carry_Out(shifter_module_1_lco), .Carry_Out(adder_module_1_carry_out), .ALU_Result(Result_p1),
    .Clock(clock_1_out), .WE(FI), .A7(A[7]), .B7(B[7]), .CF(CF_p1), .OVERFLOW(OVF_p1), .SIGN(SF_p1),
    .ZERO(ZF_p1));
  NOT_Module not_module_1 (.A(and_module_1_and_output), .Invert_Output(not_module_1_invert_output));
  not not_11 (not_11_out, in_2[6]);
  LS_245 ls_245_1 (.Data(not_module_1_invert_output), .EN(in_2[6]), .Res(Result_p1));
  LS_245 ls_245_2 (.Data(and_module_1_and_output), .EN(not_11_out), .Res(Result_p1));
endmodule

module AND_Module (
  input  [7:0] A,
  input  [7:0] B,
  input  AND_OUT,
  output [7:0] AND_Output
);

  wire [7:0] and_1_out;

  and and_1 (and_1_out[0], B[0], A[0]);
  and and_2 (and_1_out[1], B[1], A[1]);
  and and_3 (and_1_out[2], B[2], A[2]);
  and and_4 (and_1_out[3], B[3], A[3]);
  and and_5 (and_1_out[4], B[4], A[4]);
  and and_6 (and_1_out[5], B[5], A[5]);
  and and_7 (and_1_out[6], B[6], A[6]);
  and and_8 (and_1_out[7], B[7], A[7]);
  LS_245 ls_245_1 (.Data(and_1_out), .EN(AND_OUT), .Res(AND_Output));
endmodule

module OR_Module (
  input  [7:0] A,
  input  [7:0] B,
  input  OR_OUT,
  output [7:0] OR_Output
);

  wire [7:0] or_1_out;

  or or_1 (or_1_out[0], B[0], A[0]);
  or or_2 (or_1_out[1], B[1], A[1]);
  or or_3 (or_1_out[2], B[2], A[2]);
  or or_4 (or_1_out[3], B[3], A[3]);
  or or_5 (or_1_out[4], B[4], A[4]);
  or or_6 (or_1_out[5], B[5], A[5]);
  or or_7 (or_1_out[6], B[6], A[6]);
  or or_8 (or_1_out[7], B[7], A[7]);
  LS_245 ls_245_1 (.Data(or_1_out), .EN(OR_OUT), .Res(OR_Output));
endmodule

module XOR_Module (
  input  [7:0] A,
  input  [7:0] B,
  input  XOR_OUT,
  output [7:0] XOR_Output
);

  wire [7:0] xor_1_out;

  xor xor_1 (xor_1_out[0], B[0], A[0]);
  xor xor_2 (xor_1_out[1], B[1], A[1]);
  xor xor_3 (xor_1_out[2], B[2], A[2]);
  xor xor_4 (xor_1_out[3], B[3], A[3]);
  xor xor_5 (xor_1_out[4], B[4], A[4]);
  xor xor_6 (xor_1_out[5], B[5], A[5]);
  xor xor_7 (xor_1_out[6], B[6], A[6]);
  xor xor_8 (xor_1_out[7], B[7], A[7]);
  LS_245 ls_245_1 (.Data(xor_1_out), .EN(XOR_OUT), .Res(XOR_Output));
endmodule

module LS_245 (
  input  [7:0] Data,
  input  EN,
  output [7:0] Res
);

  wire not_1_out;

  not not_1 (not_1_out, EN);
  assign Res[7] = not_1_out ? Data[7] : 1'bz;  // Controlled_Buffer controlled_buffer_1
  assign Res[6] = not_1_out ? Data[6] : 1'bz;  // Controlled_Buffer controlled_buffer_2
  assign Res[5] = not_1_out ? Data[5] : 1'bz;  // Controlled_Buffer controlled_buffer_3
  assign Res[4] = not_1_out ? Data[4] : 1'bz;  // Controlled_Buffer controlled_buffer_4
  assign Res[3] = not_1_out ? Data[3] : 1'bz;  // Controlled_Buffer controlled_buffer_5
  assign Res[2] = not_1_out ? Data[2] : 1'bz;  // Controlled_Buffer controlled_buffer_6
  assign Res[1] = not_1_out ? Data[1] : 1'bz;  // Controlled_Buffer controlled_buffer_7
  assign Res[0] = not_1_out ? Data[0] : 1'bz;  // Controlled_Buffer controlled_buffer_8
endmodule

module NOT_Module (
  input  [7:0] A,
  output [7:0] Invert_Output
);

  not not_1 (Invert_Output[0], A[0]);
  not not_2 (Invert_Output[1], A[1]);
  not not_3 (Invert_Output[2], A[2]);
  not not_4 (Invert_Output[3], A[3]);
  not not_5 (Invert_Output[4], A[4]);
  not not_6 (Invert_Output[5], A[5]);
  not not_7 (Invert_Output[6], A[6]);
  not not_8 (Invert_Output[7], A[7]);
endmodule

module SHIFTER_Module (
  input  ROTATE_OUT,
  input  SHIFT_OUT,
  input  [1:0] SHIFT_SELECT,
  input  [7:0] A_Data,
  output [7:0] Result,
  output LCO
);

  wire and_1_out, and_2_out, and_3_out, and_4_out, and_5_out, and_6_out, and_7_out, decoder_1_out0,
       decoder_1_out1, decoder_1_out2, decoder_1_out3, not_1_out, not_2_out, not_3_out, not_4_out, not_5_out,
       not_6_out, not_7_out, not_8_out, not_9_out, not_10_out, not_11_out, not_12_out, not_13_out, not_14_out;
  wire [3:0] multiplexer_1_out;

  and and_1 (and_1_out, A_Data[0], not_5_out);
  and and_2 (and_2_out, A_Data[7], not_5_out);
  and and_3 (and_3_out, A_Data[7], not_1_out);
  not not_1 (not_1_out, not_9_out);
  and and_4 (and_4_out, A_Data[3], not_2_out);
  not not_2 (not_2_out, not_10_out);
  and and_5 (and_5_out, A_Data[0], not_3_out);
  not not_3 (not_3_out, not_11_out);
  and and_6 (and_6_out, A_Data[2], not_4_out);
  not not_4 (not_4_out, not_12_out);
  not not_5 (not_5_out, ROTATE_OUT);
  and and_7 (and_7_out, ROTATE_OUT, SHIFT_OUT);
  not not_6 (not_6_out, not_11_out);
  LED led_1 (.in(not_5_out));
  not not_7 (not_7_out, not_9_out);
  or or_1 (LCO, and_3_out, and_4_out, and_5_out, and_6_out);
  Decoder #(.select(2)) decoder_1 (
    .out0(decoder_1_out0), .out1(decoder_1_out1), .out2(decoder_1_out2), .out3(decoder_1_out3),
    .sel(SHIFT_SELECT), .en(not_8_out));
  not not_8 (not_8_out, and_7_out);
  assign Result[7] = not_7_out ? A_Data[6] : 1'bz;  // Controlled_Buffer controlled_buffer_1
  assign Result[6] = not_7_out ? A_Data[5] : 1'bz;  // Controlled_Buffer controlled_buffer_2
  assign Result[5] = not_7_out ? A_Data[4] : 1'bz;  // Controlled_Buffer controlled_buffer_3
  assign Result[4] = not_7_out ? A_Data[3] : 1'bz;  // Controlled_Buffer controlled_buffer_4
  assign Result[3] = not_7_out ? A_Data[2] : 1'bz;  // Controlled_Buffer controlled_buffer_5
  assign Result[2] = not_7_out ? A_Data[1] : 1'bz;  // Controlled_Buffer controlled_buffer_6
  assign Result[1] = not_7_out ? A_Data[0] : 1'bz;  // Controlled_Buffer controlled_buffer_7
  assign Result[0] = not_7_out ? and_2_out : 1'bz;  // Controlled_Buffer controlled_buffer_8
  assign Result[7] = not_6_out ? and_1_out : 1'bz;  // Controlled_Buffer controlled_buffer_9
  assign Result[6] = not_6_out ? A_Data[7] : 1'bz;  // Controlled_Buffer controlled_buffer_10
  assign Result[5] = not_6_out ? A_Data[6] : 1'bz;  // Controlled_Buffer controlled_buffer_11
  assign Result[4] = not_6_out ? A_Data[5] : 1'bz;  // Controlled_Buffer controlled_buffer_12
  assign Result[3] = not_6_out ? A_Data[4] : 1'bz;  // Controlled_Buffer controlled_buffer_13
  assign Result[2] = not_6_out ? A_Data[3] : 1'bz;  // Controlled_Buffer controlled_buffer_14
  assign Result[1] = not_6_out ? A_Data[2] : 1'bz;  // Controlled_Buffer controlled_buffer_15
  assign Result[0] = not_6_out ? A_Data[1] : 1'bz;  // Controlled_Buffer controlled_buffer_16
  LED led_2 (.in(not_12_out));
  not not_9 (not_9_out, decoder_1_out0);
  not not_10 (not_10_out, decoder_1_out1);
  not not_11 (not_11_out, decoder_1_out2);
  not not_12 (not_12_out, decoder_1_out3);
  LED led_3 (.in(not_11_out));
  LED led_4 (.in(not_10_out));
  LED led_5 (.in(not_9_out));
  // LedBar #(.inputtype("row")) ledbar_1: pin names not known; wires that end beside it: Result
  Multiplexer #(.width(4)) multiplexer_1 (.in0(4'b0000), .in1(A_Data[7:4]), .out(multiplexer_1_out), .sel(not_5_out));
  assign Result[4] = not_13_out ? A_Data[0] : 1'bz;  // Controlled_Buffer controlled_buffer_17
  assign Result[5] = not_13_out ? A_Data[1] : 1'bz;  // Controlled_Buffer controlled_buffer_18
  assign Result[6] = not_13_out ? A_Data[2] : 1'bz;  // Controlled_Buffer controlled_buffer_19
  assign Result[7] = not_13_out ? A_Data[3] : 1'bz;  // Controlled_Buffer controlled_buffer_20
  assign Result[0] = not_13_out ? multiplexer_1_out[0] : 1'bz;  // Controlled_Buffer controlled_buffer_21
  assign Result[1] = not_13_out ? multiplexer_1_out[1] : 1'bz;  // Controlled_Buffer controlled_buffer_22
  assign Result[2] = not_13_out ? multiplexer_1_out[2] : 1'bz;  // Controlled_Buffer controlled_buffer_23
  assign Result[3] = not_13_out ? multiplexer_1_out[3] : 1'bz;  // Controlled_Buffer controlled_buffer_24
  not not_13 (not_13_out, not_10_out);
  assign Result[4] = not_14_out ? 1'b0 : 1'bz;  // Controlled_Buffer controlled_buffer_25
  assign Result[7] = not_14_out ? 1'b0 : 1'bz;  // Controlled_Buffer controlled_buffer_26
  assign Result[6] = not_14_out ? 1'b0 : 1'bz;  // Controlled_Buffer controlled_buffer_27
  assign Result[5] = not_14_out ? 1'b0 : 1'bz;  // Controlled_Buffer controlled_buffer_28
  assign Result[0] = not_14_out ? A_Data[4] : 1'bz;  // Controlled_Buffer controlled_buffer_29
  assign Result[1] = not_14_out ? A_Data[5] : 1'bz;  // Controlled_Buffer controlled_buffer_30
  assign Result[2] = not_14_out ? A_Data[6] : 1'bz;  // Controlled_Buffer controlled_buffer_31
  assign Result[3] = not_14_out ? A_Data[7] : 1'bz;  // Controlled_Buffer controlled_buffer_32
  not not_14 (not_14_out, not_12_out);

  // Notes on the sheet:
  //   ROTATE_OUT: pull=up
  //   SHIFT_OUT: pull=up
  //   Rotate_Enable
  //   SHIFT RIGHT 1
  //   SHIFT LEFT 1
  //   SHR4
  //   SHR
  //   SHL4
  //   SHL
  //   SHIFT LEFT 4
  //   SHIFT RIGHT 4
endmodule

module ADDER_Module (
  input  [7:0] A,
  input  TWOS_COMPLEMENT,
  input  [7:0] B,
  input  ADDER_MUL_SELECT,
  input  CARRY_IN,
  input  ADDER_OUT,
  output [7:0] Adder_Result,
  output CARRY_OUT
);

  wire and_1_out, and_2_out, n74283_1_pin9, n74283_2_pin9, not_1_out, not_2_out;
  wire [7:0] multiplexer_1_out, n74283_1_pin4, n74283_1_pin6;

  Multiplexer #(.width(8)) multiplexer_1 (.in0(B), .in1({8{1'b1}}), .out(multiplexer_1_out), .sel(ADDER_MUL_SELECT));
  _74283 u_74283_1 (
    .pin1(n74283_1_pin4[1]), .pin2(n74283_1_pin6[1]), .pin3(A[1]), .pin4(n74283_1_pin4[0]), .pin5(A[0]),
    .pin6(n74283_1_pin6[0]), .pin7(CARRY_IN), .pin15(n74283_1_pin6[2]), .pin14(A[2]),
    .pin13(n74283_1_pin4[2]), .pin12(A[3]), .pin11(n74283_1_pin6[3]), .pin10(n74283_1_pin4[3]),
    .pin9(n74283_1_pin9));
  _74283 u_74283_2 (
    .pin1(n74283_1_pin4[5]), .pin2(n74283_1_pin6[5]), .pin3(A[5]), .pin4(n74283_1_pin4[4]), .pin5(A[4]),
    .pin6(n74283_1_pin6[4]), .pin7(n74283_1_pin9), .pin15(n74283_1_pin6[6]), .pin14(A[6]),
    .pin13(n74283_1_pin4[6]), .pin12(A[7]), .pin11(n74283_1_pin6[7]), .pin10(n74283_1_pin4[7]),
    .pin9(n74283_2_pin9));
  XOR_Module xor_module_1 (.A({8{TWOS_COMPLEMENT}}), .B(multiplexer_1_out), .XOR_OUT(1'b0), .XOR_Output(n74283_1_pin6));
  LED led_1 (.in(n74283_2_pin9));
  // LedBar #(.inputtype("row")) ledbar_1: pin names not known; wires that end beside it: n74283_1_pin4
  LS_245 ls_245_1 (.Data(n74283_1_pin4), .EN(ADDER_OUT), .Res(Adder_Result));
  not not_1 (not_1_out, n74283_2_pin9);
  and and_1 (and_1_out, not_1_out, TWOS_COMPLEMENT);
  and and_2 (and_2_out, n74283_2_pin9, not_2_out);
  not not_2 (not_2_out, TWOS_COMPLEMENT);
  or or_1 (CARRY_OUT, and_1_out, and_2_out);

  // Notes on the sheet:
  //   LSN
  //   MSN
endmodule

module Flags_Module (
  input  Logical_Carry_Out,
  input  Carry_Out,
  input  [7:0] ALU_Result,
  input  Clock,
  input  WE,
  input  A7,
  input  B7,
  output CF,
  output OVERFLOW,
  output SIGN,
  output ZERO
);

  wire not_1_out, xor_1_out, xor_2_out;
  wire [3:0] or_1_out;

  xor xor_1 (xor_1_out, A7, ALU_Result[7]);
  xor xor_2 (xor_2_out, B7, ALU_Result[7]);
  or or_1 (or_1_out[0], Logical_Carry_Out, Carry_Out);
  nor nor_1 (or_1_out[3], ALU_Result[0], ALU_Result[1], ALU_Result[2], ALU_Result[3], ALU_Result[4], ALU_Result[5], ALU_Result[6], ALU_Result[7]);
  and and_1 (or_1_out[1], xor_1_out, xor_2_out);
  not not_1 (not_1_out, WE);
  Register #(.width(4)) register_1 (
    .D({or_1_out[3], ALU_Result[7], or_1_out[1:0]}), .en(not_1_out), .clk(Clock),
    .Q({ZERO, SIGN, OVERFLOW, CF}));  // open: clr
endmodule
