// Logisim project alu_shift_circuit.circ as structural Verilog: 1 circuit, main circuit main
module main (
  input  [5:0] in_1,
  output A_OUT,
  output ADDER_OUT,
  output ADC_SUB,
  output OP_MUX_SEL,
  output TWOS_COMP,
  output AND_OUT,
  output OR_OUT,
  output XOR_OUT,
  output ALU_OUT,
  output SHL,
  output INVERT_OUT,
  output SHR,
  output ROTATE,
  output ARITHMETIC
);

  wire and_1_out, and_2_out, and_7_out, decoder_1_out0, decoder_1_out1, decoder_1_out2, decoder_1_out3,
       decoder_1_out4, decoder_1_out5, decoder_1_out6, decoder_1_out7, decoder_1_out8, decoder_1_out9,
       decoder_1_out10, decoder_1_out11, decoder_1_out12, decoder_1_out13, decoder_1_out14, decoder_1_out15,
       nand_1_out, nand_4_out, nand_7_out, not_2_out, not_3_out, not_4_out, not_5_out, not_6_out, not_7_out,
       not_11_out, not_12_out, not_13_out, not_14_out, not_15_out, not_16_out, not_17_out;

  nand nand_1 (nand_1_out, in_1[5], in_1[5]);
  nand nand_2 (INVERT_OUT, in_1[5], in_1[4]);
  nand nand_3 (ALU_OUT, INVERT_OUT, in_1[5]);
  not not_1 (A_OUT, decoder_1_out0);
  not not_2 (not_2_out, decoder_1_out1);
  not not_3 (not_3_out, decoder_1_out2);
  not not_4 (not_4_out, decoder_1_out3);
  not not_5 (not_5_out, decoder_1_out4);
  not not_6 (not_6_out, decoder_1_out5);
  not not_7 (not_7_out, decoder_1_out6);
  not not_8 (AND_OUT, decoder_1_out7);
  not not_9 (OR_OUT, decoder_1_out8);
  not not_10 (XOR_OUT, decoder_1_out9);
  not not_11 (not_11_out, decoder_1_out10);
  not not_12 (not_12_out, decoder_1_out11);
  not not_13 (not_13_out, decoder_1_out12);
  not not_14 (not_14_out, decoder_1_out13);
  not not_15 (not_15_out, decoder_1_out14);
  not not_16 (not_16_out, decoder_1_out15);
  not not_17 (not_17_out, nand_1_out);
  Decoder #(.select(4)) decoder_1 (
    .out0(decoder_1_out0), .out1(decoder_1_out1), .out2(decoder_1_out2), .out3(decoder_1_out3),
    .out4(decoder_1_out4), .out5(decoder_1_out5), .out6(decoder_1_out6), .out7(decoder_1_out7),
    .out8(decoder_1_out8), .out9(decoder_1_out9), .out10(decoder_1_out10), .out11(decoder_1_out11),
    .out12(decoder_1_out12), .out13(decoder_1_out13), .out14(decoder_1_out14), .out15(decoder_1_out15),
    .sel(in_1[3:0]), .en(not_17_out));
  nand nand_4 (nand_4_out, not_4_out, not_5_out);
  and and_1 (and_1_out, not_11_out, not_13_out);
  and and_2 (and_2_out, not_12_out, not_14_out);
  and and_3 (ROTATE, not_15_out, not_16_out);
  and and_4 (ARITHMETIC, not_13_out, not_14_out);
  nand nand_5 (ADC_SUB, not_3_out, not_5_out);
  nand nand_6 (OP_MUX_SEL, not_7_out, not_6_out);
  nand nand_7 (nand_7_out, nand_4_out, nand_4_out);
  and and_5 (SHL, and_1_out, not_16_out);
  and and_6 (SHR, and_2_out, not_15_out);
  nand nand_8 (TWOS_COMP, nand_7_out, not_6_out);
  and and_7 (and_7_out, not_2_out, not_3_out, not_4_out, not_5_out);
  and and_8 (ADDER_OUT, and_7_out, not_6_out, not_7_out, 1'b1);
endmodule
