// Logisim project control_unit_test_v6.circ as structural Verilog
module main (
  input  [7:0] BUS_DATA,
  output LATCH_MAR_LOW,
  output MEM_WRITE_LOW,
  output USE_DATA_SEG_LOW,
  output USE_STACK_SEG_LOW,
  output USE_CODE_SEG_LOW,
  output MEM_READ_LOW,
  output LATCH_CODE_SEG_LOW,
  output CODE_SEG_OUT_LOW,
  output LATCH_DATA_SEG_LOW,
  output DATA_SEG_OUT_LOW,
  output LATCH_STACK_SEG_LOW,
  output STACK_SEG_OUT_LOW,
  output LATCH_FLAGS_LOW,
  output RESTORE_FLAGS_HIGH,
  output FLAGS_OUT_LOW,
  output LATCH_ACC_LOW,
  output LATCH_B_LOW,
  output PC_DEC_LOW,
  output PC_INC_LOW,
  output PC_LOAD_LOW,
  output PC_OUT_LOW,
  output SP_DEC_LOW,
  output SP_INC_LOW,
  output SP_LOAD_LOW,
  output SP_OUT_LOW,
  output MEM_CART_REQ_LOW,
  output MEM_REQ_LOW,
  output IO_REQ_LOW,
  output IRQ_MASK_PORT_EN_LOW,
  output WRITE_LOW,
  output READ_LOW,
  output SPR_FLAGS_ACC_B_EN,
  output JCC_ADR0,
  output JCC_ADR1,
  output JCC_ADR2,
  output JCC_ADR3,
  output GPR0,
  output GPR1,
  output GPR2,
  output GPR3,
  output GPR4,
  output GPR5,
  output GPR6,
  output GPR7_SOFTWARE_RST_LOW,
  output INST_REG_IN_LOW,
  output ALU_FUNC_0,
  output ALU_FUNC_1,
  output ALU_FUNC_2,
  output ALU_FUNC_3,
  output ALU_FUNC_4,
  output ALU_FUNC_5_EN_LOW
);

  wire and_1_out, inst_multiplexer_1_reset, inst_multiplexer_1_reset_step,
       interrupt_req_timing_1_interrupt_req_low, IREQ_out, JCC_JUMP_EN_LOW_out, Main_Clock_out, not_1_out,
       RESET_BTN_out;
  wire [7:0] instruction_register_1_ir_data;
  wire [11:0] ledbar_4_p2;
  wire [39:0] ledbar_4_p3;

  Clock Main_Clock (.out(Main_Clock_out));
  Button #(.press("passive")) RESET_BTN (.out(RESET_BTN_out));
  Button #(.press("passive")) IREQ (.out(IREQ_out));
  Button #(.press("passive")) JCC_JUMP_EN_LOW (.out(JCC_JUMP_EN_LOW_out));
  not not_1 (not_1_out, Main_Clock_out);
  and and_1 (and_1_out, inst_multiplexer_1_reset_step, ledbar_4_p3[7]);
  // LedBar #(.inputtype("row"), .matrixcols(40)) ledbar_1: pin names not known
  LedBar #(.matrixcols(52)) ledbar_2 (
    .led0(LATCH_MAR_LOW), .led1(MEM_WRITE_LOW), .led2(USE_DATA_SEG_LOW), .led3(USE_STACK_SEG_LOW),
    .led4(USE_CODE_SEG_LOW), .led5(MEM_READ_LOW), .led6(LATCH_CODE_SEG_LOW), .led7(CODE_SEG_OUT_LOW),
    .led8(LATCH_DATA_SEG_LOW), .led9(DATA_SEG_OUT_LOW), .led10(LATCH_STACK_SEG_LOW),
    .led11(STACK_SEG_OUT_LOW), .led12(LATCH_FLAGS_LOW), .led13(RESTORE_FLAGS_HIGH), .led14(FLAGS_OUT_LOW),
    .led15(LATCH_ACC_LOW), .led16(LATCH_B_LOW), .led17(PC_DEC_LOW), .led18(PC_INC_LOW), .led19(PC_LOAD_LOW),
    .led20(PC_OUT_LOW), .led21(SP_DEC_LOW), .led22(SP_INC_LOW), .led23(SP_LOAD_LOW), .led24(SP_OUT_LOW),
    .led25(MEM_CART_REQ_LOW), .led26(MEM_REQ_LOW), .led27(IO_REQ_LOW), .led28(IRQ_MASK_PORT_EN_LOW),
    .led29(WRITE_LOW), .led30(READ_LOW), .led31(SPR_FLAGS_ACC_B_EN), .led32(JCC_ADR0), .led33(JCC_ADR1),
    .led34(JCC_ADR2), .led35(JCC_ADR3), .led36(GPR0), .led37(GPR1), .led38(GPR2), .led39(GPR3), .led40(GPR4),
    .led41(GPR5), .led42(GPR6), .led43(GPR7_SOFTWARE_RST_LOW), .led44(INST_REG_IN_LOW), .led45(ALU_FUNC_0),
    .led46(ALU_FUNC_1), .led47(ALU_FUNC_2), .led48(ALU_FUNC_3), .led49(ALU_FUNC_4),
    .led50(ALU_FUNC_5_EN_LOW), .led51(ledbar_4_p3[39]));
  // LedBar #(.inputtype("row")) ledbar_3: pin names not known
  // LedBar #(.inputtype("row"), .matrixcols(4)) ledbar_4: pin names not known; wires that end beside it: ledbar_4_p2[11:4], ledbar_4_p2[3:0], {ledbar_4_p3[39], ALU_FUNC_5_EN_LOW, ALU_FUNC_4, ALU_FUNC_3, ALU_FUNC_2, ALU_FUNC_1, ALU_FUNC_0, INST_REG_IN_LOW, GPR7_SOFTWARE_RST_LOW, GPR6, GPR5, GPR4, GPR3, GPR2, GPR1, GPR0, ledbar_4_p3[23:22], READ_LOW, WRITE_LOW, IRQ_MASK_PORT_EN_LOW, IO_REQ_LOW, MEM_REQ_LOW, MEM_CART_REQ_LOW, JCC_ADR3, JCC_ADR2, JCC_ADR1, JCC_ADR0, ledbar_4_p3[11:7], SPR_FLAGS_ACC_B_EN, ledbar_4_p3[5:0]}
  Instruction_Register instruction_register_1 (
    .Bus_data(BUS_DATA), .Inst_reg_in_LOW(INST_REG_IN_LOW), .Clock(Main_Clock_out),
    .IR_Data(instruction_register_1_ir_data));
  Interrupt_Req_Timing interrupt_req_timing_1 (
    .IRQ_Low(IREQ_out), .Step_Counter(ledbar_4_p2[3:0]),
    .Interrupt_Req_Low(interrupt_req_timing_1_interrupt_req_low));
  Step_Counter step_counter_1 (.RESET_STEP(and_1_out), .NOT_CLOCK(not_1_out), .STEP(ledbar_4_p2[3:0]));
  Memory_Decode_Logic memory_decode_logic_1 (
    .MEM0(ledbar_4_p3[0]), .MEM1(ledbar_4_p3[1]), .MEM2(ledbar_4_p3[2]), .MEM_EN_LOW(ledbar_4_p3[3]),
    .SEGMENT_REG_EN_LOW(ledbar_4_p3[4]), .RESET_LOW(inst_multiplexer_1_reset), .MEM_READ_LOW(MEM_READ_LOW),
    .USE_CODE_SEG_LOW(USE_CODE_SEG_LOW), .USE_STACK_SEG_LOW(USE_STACK_SEG_LOW),
    .USE_DATA_SEG_LOW(USE_DATA_SEG_LOW), .MEM_WRITE_LOW(MEM_WRITE_LOW), .LATCH_MAR_LOW(LATCH_MAR_LOW),
    .LATCH_CODE_SEG_LOW(LATCH_CODE_SEG_LOW), .CODE_SEG_OUT(CODE_SEG_OUT_LOW),
    .LATCH_DATA_SEG_LOW(LATCH_DATA_SEG_LOW), .DATA_SEG_OUT(DATA_SEG_OUT_LOW),
    .LATCH_STACK_SEG_LOW(LATCH_STACK_SEG_LOW), .STACK_SEG_OUT(STACK_SEG_OUT_LOW));
  // NoConnect on ledbar_4_p3[22]
  // NoConnect on ledbar_4_p3[23]
  Inst_Multiplexer inst_multiplexer_1 (
    .Inst_Data_Bits(instruction_register_1_ir_data), .Reset_In_Low(RESET_BTN_out),
    .Software_Reset_Low(GPR7_SOFTWARE_RST_LOW),
    .Interrupt_Enable_Low(interrupt_req_timing_1_interrupt_req_low), .Current_Instruction(ledbar_4_p2[11:4]),
    .RESET_STEP(inst_multiplexer_1_reset_step), .RESET(inst_multiplexer_1_reset));
  GPR_FLAGS_ACC_B_DECODER gpr_flags_acc_b_decoder_1 (
    .RESET(inst_multiplexer_1_reset), .EN_SPR_FLAGS_ACC_B_LOW(ledbar_4_p3[5]),
    .CNTL_0_SPR_FLAGS_ACC_B(ledbar_4_p3[8]), .CNTL_1_SPR_FLAGS_ACC_B(ledbar_4_p3[9]),
    .CNTL_2_SPR_FLAGS_ACC_B(ledbar_4_p3[10]), .CNTL_3_SPR_FLAGS_ACC_B(ledbar_4_p3[11]),
    .JCC_LD_PC_COND(JCC_JUMP_EN_LOW_out), .LATCH_FLAGS(LATCH_FLAGS_LOW), .RESTORE_FLAGS(RESTORE_FLAGS_HIGH),
    .FLAGS_OUT_LOW(FLAGS_OUT_LOW), .LATCH_ACC_LOW(LATCH_ACC_LOW), .LATCH_B_LOW(LATCH_B_LOW),
    .PC_DEC_LOW(PC_DEC_LOW), .PC_INC_LOW(PC_INC_LOW), .PC_LOAD_LOW(PC_LOAD_LOW), .PC_OUT_LOW(PC_OUT_LOW),
    .SP_DEC_LOW(SP_DEC_LOW), .SP_INC_LOW(SP_INC_LOW), .SP_LOAD_LOW(SP_LOAD_LOW), .SP_OUT_LOW(SP_OUT_LOW));
  ROM #(.addrWidth(12)) rom_1 (.addr(ledbar_4_p2), .data({ledbar_4_p3[7], SPR_FLAGS_ACC_B_EN, ledbar_4_p3[5:0]}));
  ROM #(.addrWidth(12)) rom_2 (.addr(ledbar_4_p2), .data({JCC_ADR3, JCC_ADR2, JCC_ADR1, JCC_ADR0, ledbar_4_p3[11:8]}));
  ROM #(.addrWidth(12)) rom_3 (
    .addr(ledbar_4_p2),
    .data({ledbar_4_p3[23:22], READ_LOW, WRITE_LOW, IRQ_MASK_PORT_EN_LOW, IO_REQ_LOW, MEM_REQ_LOW, MEM_CART_REQ_LOW}));
  ROM #(.addrWidth(12)) rom_4 (
    .addr(ledbar_4_p2), .data({GPR7_SOFTWARE_RST_LOW, GPR6, GPR5, GPR4, GPR3, GPR2, GPR1, GPR0}));
  ROM #(.addrWidth(12)) rom_5 (
    .addr(ledbar_4_p2),
    .data({ledbar_4_p3[39], ALU_FUNC_5_EN_LOW, ALU_FUNC_4, ALU_FUNC_3, ALU_FUNC_2, ALU_FUNC_1, ALU_FUNC_0, INST_REG_IN_LOW}));

  // Notes on the sheet:
  //   USE_STACK_SEG_LOW: pull=up
  //   PC_DEC_LOW: pull=up
  //   READ_LOW: pull=up
  //   BUS_DATA: pull=down
  //   CURRENT INSTRUCTION
  //   MEMORY DECODER
  //   CONTROL UNIT
  //   MICROCODE CONTROL WORD
  //   STEP
  //   CONTROL LINES OUTPUT
  //   contents of rom_1 (hex, n*v repeats v):
  //   24*f8
  //   contents of rom_3 (hex, n*v repeats v):
  //   24*3f 4070*0 f3 ff
  //   contents of rom_4 (hex, n*v repeats v):
  //   24*80 4040*0 13*80 17*0 f3 ff
  //   NOP
endmodule

module Instruction_Register (
  input  [7:0] Bus_data,
  input  Inst_reg_in_LOW,
  input  Clock,
  output [7:0] IR_Data
);

  wire nand_1_out, nand_2_out;

  nand nand_1 (nand_1_out, Inst_reg_in_LOW, Inst_reg_in_LOW);
  nand nand_2 (nand_2_out, nand_1_out, Clock);
  Register Instruction_Register (.D(Bus_data), .en(1'b1), .clk(nand_2_out), .Q(IR_Data), .clr(1'b0));

  // Notes on the sheet:
  //   Inst_reg_in_LOW: pull=up
  //   Clock: pull=down
endmodule

module Inst_Multiplexer (
  input  [7:0] Inst_Data_Bits,
  input  Reset_In_Low,
  input  Software_Reset_Low,
  input  Interrupt_Enable_Low,
  output [7:0] Current_Instruction,
  output RESET_STEP,
  output RESET
);

  wire nand_1_out, nand_2_out, not_1_out;

  and and_1 (RESET, Reset_In_Low, Software_Reset_Low);
  nand nand_1 (nand_1_out, Reset_In_Low, Software_Reset_Low);
  not not_1 (not_1_out, nand_1_out);
  and and_2 (RESET_STEP, RESET, Interrupt_Enable_Low);
  nand nand_2 (nand_2_out, not_1_out, Interrupt_Enable_Low);
  Multiplexer #(.width(8)) multiplexer_1 (
    .in0(Inst_Data_Bits), .in1({{7{1'b1}}, RESET}), .out(Current_Instruction), .sel(nand_2_out));

  // Notes on the sheet:
  //   Reset_In_Low: pull=up
  //   Software_Reset_Low: pull=up
  //   Interrupt_Enable_Low: pull=up
endmodule

module Interrupt_Req_Timing (
  input  IRQ_Low,
  input  [3:0] Step_Counter,
  output Interrupt_Req_Low
);

  wire nand_1_out, nand_2_out, or_1_out;

  or or_1 (or_1_out, Step_Counter[0], Step_Counter[1], Step_Counter[2], Step_Counter[3]);
  nand nand_1 (nand_1_out, IRQ_Low, IRQ_Low);
  nand nand_2 (nand_2_out, or_1_out, or_1_out);
  nand nand_3 (Interrupt_Req_Low, nand_1_out, nand_2_out);

  // Notes on the sheet:
  //   IRQ_Low: pull=up
endmodule

module Step_Counter (
  input  RESET_STEP,
  input  NOT_CLOCK,
  output [3:0] STEP
);

  wire n74161_1_pin1, n74161_1_pin3, n74161_1_pin4, n74161_1_pin5, n74161_1_pin6, n74161_1_pin7,
       n74161_1_pin10, n74161_1_pin15;

  // NoConnect on n74161_1_pin15
  _74161 u_74161_1 (
    .pin1(n74161_1_pin1), .pin2(NOT_CLOCK), .pin3(n74161_1_pin3), .pin4(n74161_1_pin4), .pin5(n74161_1_pin5),
    .pin6(n74161_1_pin6), .pin7(n74161_1_pin7), .pin15(n74161_1_pin15), .pin14(STEP[0]), .pin13(STEP[1]),
    .pin12(STEP[2]), .pin11(STEP[3]), .pin10(n74161_1_pin10), .pin9(RESET_STEP));
  // also tied to GND on the sheet: {n74161_1_pin3, n74161_1_pin4, n74161_1_pin5, n74161_1_pin6}
  // also tied to VCC on the sheet: {n74161_1_pin1, n74161_1_pin10, n74161_1_pin7}

  // Notes on the sheet:
  //   RESET_STEP: pull=up
  //   NOT_CLOCK: pull=up
endmodule

module Memory_Decode_Logic (
  input  MEM0,
  input  MEM1,
  input  MEM2,
  input  MEM_EN_LOW,
  input  SEGMENT_REG_EN_LOW,
  input  RESET_LOW,
  output MEM_READ_LOW,
  output USE_CODE_SEG_LOW,
  output USE_STACK_SEG_LOW,
  output USE_DATA_SEG_LOW,
  output MEM_WRITE_LOW,
  output LATCH_MAR_LOW,
  output LATCH_CODE_SEG_LOW,
  output CODE_SEG_OUT,
  output LATCH_DATA_SEG_LOW,
  output DATA_SEG_OUT,
  output LATCH_STACK_SEG_LOW,
  output STACK_SEG_OUT
);

  wire and_1_out, decoder_1_out0, decoder_1_out1, decoder_1_out2, decoder_1_out3, decoder_1_out4,
       decoder_1_out5, decoder_1_out6, decoder_1_out7, decoder_2_out0, decoder_2_out1, decoder_2_out2,
       decoder_2_out3, decoder_2_out4, decoder_2_out5, decoder_2_out6, decoder_2_out7, not_1_out, not_2_out,
       not_4_out, not_5_out, not_6_out, not_7_out, not_9_out, not_10_out, not_11_out, not_13_out, not_15_out;

  not not_1 (not_1_out, MEM_EN_LOW);
  Decoder #(.select(3)) decoder_1 (
    .out0(decoder_1_out0), .out1(decoder_1_out1), .out2(decoder_1_out2), .out3(decoder_1_out3),
    .out4(decoder_1_out4), .out5(decoder_1_out5), .out6(decoder_1_out6), .out7(decoder_1_out7),
    .sel({MEM2, MEM1, MEM0}), .en(not_1_out));
  not not_2 (not_2_out, SEGMENT_REG_EN_LOW);
  Decoder #(.select(3)) decoder_2 (
    .out0(decoder_2_out0), .out1(decoder_2_out1), .out2(decoder_2_out2), .out3(decoder_2_out3),
    .out4(decoder_2_out4), .out5(decoder_2_out5), .out6(decoder_2_out6), .out7(decoder_2_out7),
    .sel({MEM2, MEM1, MEM0}), .en(not_2_out));
  not not_3 (USE_CODE_SEG_LOW, decoder_1_out0);
  not not_4 (not_4_out, decoder_1_out1);
  not not_5 (not_5_out, decoder_1_out2);
  not not_6 (not_6_out, decoder_1_out3);
  not not_7 (not_7_out, decoder_1_out4);
  not not_8 (LATCH_MAR_LOW, decoder_1_out5);
  // NoConnect on not_9_out
  not not_9 (not_9_out, decoder_1_out6);
  // NoConnect on not_10_out
  not not_10 (not_10_out, decoder_1_out7);
  // NoConnect on decoder_2_out0
  not not_11 (not_11_out, decoder_2_out1);
  not not_12 (CODE_SEG_OUT, decoder_2_out2);
  not not_13 (not_13_out, decoder_2_out3);
  not not_14 (DATA_SEG_OUT, decoder_2_out4);
  not not_15 (not_15_out, decoder_2_out5);
  not not_16 (STACK_SEG_OUT, decoder_2_out6);
  // NoConnect on decoder_2_out7
  and and_1 (and_1_out, USE_CODE_SEG_LOW, not_4_out);
  and and_2 (USE_STACK_SEG_LOW, not_5_out, not_7_out);
  and and_3 (USE_DATA_SEG_LOW, not_4_out, not_6_out);
  and and_4 (MEM_WRITE_LOW, not_6_out, not_7_out);
  and and_5 (LATCH_CODE_SEG_LOW, not_11_out, RESET_LOW);
  and and_6 (LATCH_DATA_SEG_LOW, not_13_out, RESET_LOW);
  and and_7 (LATCH_STACK_SEG_LOW, not_15_out, RESET_LOW);
  and and_8 (MEM_READ_LOW, and_1_out, not_5_out);

  // Notes on the sheet:
  //   MEM0: pull=down
  //   MEM1: pull=down
  //   MEM2: pull=down
  //   MEM_EN_LOW: pull=up
  //   SEGMENT_REG_EN_LOW: pull=up
  //   RESET_LOW: pull=up
  //   NOP
  //   NOP
endmodule

module GPR_FLAGS_ACC_B_DECODER (
  input  RESET,
  input  EN_SPR_FLAGS_ACC_B_LOW,
  input  CNTL_0_SPR_FLAGS_ACC_B,
  input  CNTL_1_SPR_FLAGS_ACC_B,
  input  CNTL_2_SPR_FLAGS_ACC_B,
  input  CNTL_3_SPR_FLAGS_ACC_B,
  input  JCC_LD_PC_COND,
  output LATCH_FLAGS,
  output RESTORE_FLAGS,
  output FLAGS_OUT_LOW,
  output LATCH_ACC_LOW,
  output LATCH_B_LOW,
  output PC_DEC_LOW,
  output PC_INC_LOW,
  output PC_LOAD_LOW,
  output PC_OUT_LOW,
  output SP_DEC_LOW,
  output SP_INC_LOW,
  output SP_LOAD_LOW,
  output SP_OUT_LOW
);

  wire decoder_1_out0, decoder_1_out1, decoder_1_out2, decoder_1_out3, decoder_1_out4, decoder_1_out5,
       decoder_1_out6, decoder_1_out7, decoder_1_out8, decoder_1_out9, decoder_1_out10, decoder_1_out11,
       decoder_1_out12, decoder_1_out13, decoder_1_out14, decoder_1_out15, not_1_out, not_3_out, not_5_out,
       not_6_out, not_9_out, not_15_out, not_16_out, not_17_out;

  Decoder #(.select(4)) decoder_1 (
    .out0(decoder_1_out0), .out1(decoder_1_out1), .out2(decoder_1_out2), .out3(decoder_1_out3),
    .out4(decoder_1_out4), .out5(decoder_1_out5), .out6(decoder_1_out6), .out7(decoder_1_out7),
    .out8(decoder_1_out8), .out9(decoder_1_out9), .out10(decoder_1_out10), .out11(decoder_1_out11),
    .out12(decoder_1_out12), .out13(decoder_1_out13), .out14(decoder_1_out14), .out15(decoder_1_out15),
    .sel({CNTL_3_SPR_FLAGS_ACC_B, CNTL_2_SPR_FLAGS_ACC_B, CNTL_1_SPR_FLAGS_ACC_B, CNTL_0_SPR_FLAGS_ACC_B}),
    .en(not_1_out));
  not not_1 (not_1_out, EN_SPR_FLAGS_ACC_B_LOW);
  not not_2 (RESTORE_FLAGS, decoder_1_out0);
  not not_3 (not_3_out, decoder_1_out1);
  not not_4 (FLAGS_OUT_LOW, decoder_1_out2);
  not not_5 (not_5_out, decoder_1_out3);
  not not_6 (not_6_out, decoder_1_out4);
  not not_7 (PC_DEC_LOW, decoder_1_out5);
  not not_8 (PC_INC_LOW, decoder_1_out6);
  not not_9 (not_9_out, decoder_1_out7);
  not not_10 (PC_OUT_LOW, decoder_1_out8);
  not not_11 (SP_DEC_LOW, decoder_1_out9);
  not not_12 (SP_INC_LOW, decoder_1_out10);
  not not_13 (SP_LOAD_LOW, decoder_1_out11);
  not not_14 (SP_OUT_LOW, decoder_1_out12);
  not not_15 (not_15_out, decoder_1_out13);
  not not_16 (not_16_out, decoder_1_out14);
  not not_17 (not_17_out, decoder_1_out15);
  // NoConnect on not_17_out
  // NoConnect on not_16_out
  // NoConnect on not_15_out
  and and_1 (LATCH_ACC_LOW, RESET, not_5_out);
  and and_2 (LATCH_B_LOW, RESET, not_6_out);
  and and_3 (PC_LOAD_LOW, not_9_out, JCC_LD_PC_COND);
  and and_4 (LATCH_FLAGS, RESTORE_FLAGS, not_3_out);

  // Notes on the sheet:
  //   RESET: pull=up
  //   EN_SPR_FLAGS_ACC_B_LOW: pull=up
  //   CNTL_0_SPR_FLAGS_ACC_B: pull=down
  //   CNTL_1_SPR_FLAGS_ACC_B: pull=down
  //   CNTL_2_SPR_FLAGS_ACC_B: pull=down
  //   CNTL_3_SPR_FLAGS_ACC_B: pull=down
  //   JCC_LD_PC_COND: pull=up
  //   NOP
endmodule
