// Logisim project displacement_register.circ as structural Verilog: 5 circuits, main circuit main
module main (
  input  LATCH_BASE,
  input  BASE_OUT,
  input  INDEX_DIR,
  input  INDEX_CNT_EN,
  input  INDEX_LATCH,
  input  [15:0] in_6,
  input  INDEX_BASE_EN,
  input  INDEX_OFFSET_EN,
  input  DISPLACE_OUT,
  input  [7:0] in_10,
  input  LATCH_OFFSET,
  input  OFFSET_EN
);

  wire clock_1_out, not_1_out, not_2_out;
  wire [3:0] displacement_reg_1_q, displacement_reg_1_q_2, displacement_reg_1_q_3, displacement_reg_1_q_4,
       index_register_1_q_base, index_register_1_q_base_2, index_register_1_q_base_3,
       index_register_1_q_base_4, index_register_1_q_displace, index_register_1_q_displace_2,
       index_register_1_q_displace_3, index_register_1_q_displace_4;
  wire [7:0] offset_register_1_q_offset_lsb, offset_register_1_q_offset_msb;
  wire [15:0] BASE_REGISTER_q;

  Clock clock_1 (.out(clock_1_out));
  Register #(.width(16)) BASE_REGISTER (.D(in_6), .en(not_1_out), .clk(clock_1_out), .Q(BASE_REGISTER_q), .clr(1'b0));
  not not_1 (not_1_out, LATCH_BASE);
  not not_2 (not_2_out, BASE_OUT);
  Hex_Digit_Display hex_digit_display_1 (.value(index_register_1_q_base_4));  // open: dp
  Index_Register index_register_1 (
    .DIRECTION(INDEX_DIR), .CNT_EN(INDEX_CNT_EN), .LATCH(INDEX_LATCH), .CLOCK(clock_1_out), .DATA_IN(in_6),
    .Q_OUT(INDEX_BASE_EN), .LSBO(INDEX_OFFSET_EN),
    .Q_BASE({index_register_1_q_base_4, index_register_1_q_base_3, index_register_1_q_base_2, index_register_1_q_base}),
    .Q_DISPLACE({index_register_1_q_displace_4, index_register_1_q_displace_3, index_register_1_q_displace_2, index_register_1_q_displace}));
  OFFSET_REGISTER offset_register_1 (
    .DATA_BUS_8(in_10), .LATCH_OFFSET_low(LATCH_OFFSET), .CLOCK(clock_1_out), .OFFSET_BUS_OUT_low(OFFSET_EN),
    .OFFSET_MSB_OUT_low(1'b1), .OFFSET_LSB_OUT_low(1'b1),
    .Q_DATA_BUS({index_register_1_q_displace_4, index_register_1_q_displace_3, index_register_1_q_displace_2, index_register_1_q_displace}),
    .Q_OFFSET_MSB(offset_register_1_q_offset_msb), .Q_OFFSET_LSB(offset_register_1_q_offset_lsb));
  // NoConnect on offset_register_1_q_offset_msb
  // NoConnect on offset_register_1_q_offset_lsb
  Hex_Digit_Display hex_digit_display_2 (.value(index_register_1_q_base_3));  // open: dp
  Hex_Digit_Display hex_digit_display_3 (.value(index_register_1_q_base_2));  // open: dp
  assign {index_register_1_q_base_4, index_register_1_q_base_3, index_register_1_q_base_2, index_register_1_q_base} = not_2_out ? BASE_REGISTER_q : 16'bz;  // Controlled_Buffer controlled_buffer_1
  Hex_Digit_Display hex_digit_display_4 (.value(index_register_1_q_base));  // open: dp
  Hex_Digit_Display hex_digit_display_5 (.value(index_register_1_q_displace_4));  // open: dp
  Hex_Digit_Display hex_digit_display_6 (.value(index_register_1_q_displace_3));  // open: dp
  Hex_Digit_Display hex_digit_display_7 (.value(index_register_1_q_displace_2));  // open: dp
  Hex_Digit_Display hex_digit_display_8 (.value(index_register_1_q_displace));  // open: dp
  DISPLACEMENT_REG displacement_reg_1 (
    .BASE_DATA_IN({index_register_1_q_base_4, index_register_1_q_base_3, index_register_1_q_base_2, index_register_1_q_base}),
    .OFFSET_DATA_IN({index_register_1_q_displace_4, index_register_1_q_displace_3, index_register_1_q_displace_2, index_register_1_q_displace}),
    .DISP_OUT_low(DISPLACE_OUT),
    .Q({displacement_reg_1_q_4, displacement_reg_1_q_3, displacement_reg_1_q_2, displacement_reg_1_q}));
  Hex_Digit_Display hex_digit_display_9 (.value(displacement_reg_1_q_4));  // open: dp
  Hex_Digit_Display hex_digit_display_10 (.value(displacement_reg_1_q_3));  // open: dp
  Hex_Digit_Display hex_digit_display_11 (.value(displacement_reg_1_q_2));  // open: dp
  Hex_Digit_Display hex_digit_display_12 (.value(displacement_reg_1_q));  // open: dp
endmodule

module DISPLACEMENT_REG (
  input  [15:0] BASE_DATA_IN,
  input  [15:0] OFFSET_DATA_IN,
  input  DISP_OUT_low,
  output [15:0] Q
);

  wire adder_1_cout, not_1_out;
  wire [3:0] adder_1_out, adder_1_out_2, adder_1_out_3, adder_1_out_4;

  Pull_Resistor pull_resistor_1 (.node(BASE_DATA_IN));
  Pull_Resistor pull_resistor_2 (.node(OFFSET_DATA_IN));
  Hex_Digit_Display hex_digit_display_1 (.value(adder_1_out_4));  // open: dp
  Hex_Digit_Display hex_digit_display_2 (.value(adder_1_out_3));  // open: dp
  Adder #(.width(16)) adder_1 (
    .a(BASE_DATA_IN), .b(OFFSET_DATA_IN), .out({adder_1_out_4, adder_1_out_3, adder_1_out_2, adder_1_out}),
    .cin(1'b0), .cout(adder_1_cout));
  // NoConnect on adder_1_cout
  Hex_Digit_Display hex_digit_display_3 (.value(adder_1_out_2));  // open: dp
  Hex_Digit_Display hex_digit_display_4 (.value(adder_1_out));  // open: dp
  assign Q = not_1_out ? {adder_1_out_4, adder_1_out_3, adder_1_out_2, adder_1_out} : 16'bz;  // Controlled_Buffer controlled_buffer_1
  not not_1 (not_1_out, DISP_OUT_low);

  // Notes on the sheet:
  //   DISP_OUT_low: pull=up
  //   BASE_DATA_IN: pull=up
  //   OFFSET_DATA_IN: pull=up
  //   Q: pull=up
endmodule

module OFFSET_REGISTER (
  input  [7:0] DATA_BUS_8,
  input  LATCH_OFFSET_low,
  input  CLOCK,
  input  OFFSET_BUS_OUT_low,
  input  OFFSET_MSB_OUT_low,
  input  OFFSET_LSB_OUT_low,
  output [15:0] Q_DATA_BUS,
  output [7:0] Q_OFFSET_MSB,
  output [7:0] Q_OFFSET_LSB
);

  wire not_1_out, not_2_out, not_3_out;
  wire [7:0] OFFSET_REGISTER_q;

  Register OFFSET_REGISTER (.D(DATA_BUS_8), .en(LATCH_OFFSET_low), .clk(CLOCK), .Q(OFFSET_REGISTER_q), .clr(1'b0));
  assign {Q_DATA_BUS[15], Q_DATA_BUS[6:0]} = not_1_out ? OFFSET_REGISTER_q : 8'bz;  // Controlled_Buffer controlled_buffer_1
  not not_1 (not_1_out, OFFSET_BUS_OUT_low);
  assign Q_OFFSET_MSB = not_2_out ? OFFSET_REGISTER_q : 8'bz;  // Controlled_Buffer controlled_buffer_2
  assign Q_OFFSET_LSB = not_3_out ? OFFSET_REGISTER_q : 8'bz;  // Controlled_Buffer controlled_buffer_3
  not not_2 (not_2_out, OFFSET_MSB_OUT_low);
  not not_3 (not_3_out, OFFSET_LSB_OUT_low);

  assign Q_DATA_BUS[14:7] = {8{Q_DATA_BUS[15]}};
endmodule

module UPDOWN_CNTR (
  input  UP_DOWN,
  input  LOAD,
  input  ENP,
  input  ENT,
  input  CLOCK,
  input  [3:0] Data_In,
  output [3:0] Q,
  output CO
);

  wire and_1_out, and_2_out, and_3_out, and_4_out, and_5_out, and_6_out, and_7_out, and_8_out, and_9_out,
       and_10_out, and_11_out, and_12_out, and_13_out, and_14_out, and_15_out, and_16_out, and_17_out,
       d_ff_1_q, d_ff_1_qn, d_ff_2_q, d_ff_2_qn, d_ff_3_q, d_ff_3_qn, d_ff_4_q, d_ff_4_qn, nor_1_out,
       nor_2_out, nor_3_out, nor_4_out, nor_5_out, nor_6_out, nor_7_out, nor_8_out, nor_9_out, nor_10_out,
       nor_11_out, nor_12_out, not_1_out, not_2_out, not_3_out, not_4_out, not_5_out, not_6_out, not_7_out,
       not_8_out, not_9_out, not_10_out, not_11_out, not_12_out, not_13_out, not_14_out, not_15_out,
       not_16_out, not_17_out, not_18_out, or_1_out, or_2_out, or_3_out;

  not not_1 (not_1_out, UP_DOWN);
  not not_2 (not_2_out, LOAD);
  not not_3 (not_3_out, not_1_out);
  not not_4 (not_4_out, not_2_out);
  not not_5 (not_5_out, not_2_out);
  not not_6 (not_6_out, ENP);
  and and_1 (and_1_out, not_5_out, not_6_out, not_7_out);
  not not_7 (not_7_out, ENT);
  not not_8 (not_8_out, ENT);
  nor nor_1 (nor_1_out, not_4_out, Data_In[0]);
  nor nor_2 (nor_2_out, not_4_out, Data_In[1]);
  nor nor_3 (nor_3_out, not_4_out, Data_In[2]);
  nor nor_4 (nor_4_out, not_4_out, Data_In[3]);
  and and_2 (and_2_out, d_ff_3_q, not_3_out);
  and and_3 (and_3_out, not_1_out, d_ff_3_qn);
  and and_4 (and_4_out, d_ff_4_q, not_3_out);
  and and_5 (and_5_out, not_1_out, d_ff_4_qn);
  and and_6 (and_6_out, d_ff_1_q, not_3_out);
  and and_7 (and_7_out, not_1_out, d_ff_1_qn);
  and and_8 (and_8_out, d_ff_2_q, not_3_out);
  and and_9 (and_9_out, not_1_out, d_ff_2_qn);
  nor nor_5 (nor_5_out, and_2_out, and_3_out);
  nor nor_6 (nor_6_out, and_4_out, and_5_out);
  nor nor_7 (nor_7_out, and_6_out, and_7_out);
  nor nor_8 (nor_8_out, and_8_out, and_9_out);
  not not_9 (not_9_out, and_1_out);
  not not_10 (not_10_out, nor_7_out);
  not not_11 (not_11_out, and_1_out);
  not not_12 (not_12_out, nor_7_out);
  or or_1 (or_1_out, not_11_out, not_12_out, not_13_out);
  not not_13 (not_13_out, nor_8_out);
  not not_14 (not_14_out, and_1_out);
  not not_15 (not_15_out, nor_7_out);
  not not_16 (not_16_out, nor_8_out);
  not not_17 (not_17_out, nor_5_out);
  nand nand_1 (CO, nor_7_out, nor_8_out, nor_5_out, nor_6_out, not_8_out);
  not not_18 (not_18_out, and_1_out);
  or or_2 (or_2_out, not_9_out, not_10_out);
  or or_3 (or_3_out, not_14_out, not_15_out, not_16_out, not_17_out);
  and and_10 (and_10_out, d_ff_1_q, and_1_out);
  and and_11 (and_11_out, not_18_out, not_4_out, d_ff_1_qn);
  and and_12 (and_12_out, d_ff_2_q, and_1_out, nor_7_out);
  and and_13 (and_13_out, or_2_out, not_4_out, d_ff_2_qn);
  and and_14 (and_14_out, d_ff_3_q, and_1_out, nor_7_out, nor_8_out);
  and and_15 (and_15_out, or_1_out, not_4_out, d_ff_3_qn);
  and and_16 (and_16_out, d_ff_4_q, and_1_out, nor_7_out, nor_8_out, nor_5_out);
  and and_17 (and_17_out, or_3_out, not_4_out, d_ff_4_qn);
  nor nor_9 (nor_9_out, and_10_out, and_11_out, nor_1_out);
  nor nor_10 (nor_10_out, and_12_out, and_13_out, nor_2_out);
  nor nor_11 (nor_11_out, and_14_out, and_15_out, nor_3_out);
  nor nor_12 (nor_12_out, and_16_out, and_17_out, nor_4_out);
  D_Flip_Flop d_ff_1 (.D(nor_9_out), .clk(CLOCK), .Q(d_ff_1_q), .Qn(d_ff_1_qn), .preset(1'b0), .reset(1'b0));
  D_Flip_Flop d_ff_2 (.D(nor_10_out), .clk(CLOCK), .Q(d_ff_2_q), .Qn(d_ff_2_qn), .preset(1'b0), .reset(1'b0));
  D_Flip_Flop d_ff_3 (.D(nor_11_out), .clk(CLOCK), .Q(d_ff_3_q), .Qn(d_ff_3_qn), .preset(1'b0), .reset(1'b0));
  D_Flip_Flop d_ff_4 (.D(nor_12_out), .clk(CLOCK), .Q(d_ff_4_q), .Qn(d_ff_4_qn), .preset(1'b0), .reset(1'b0));
  not not_19 (Q[0], d_ff_1_qn);
  not not_20 (Q[1], d_ff_2_qn);
  not not_21 (Q[2], d_ff_3_qn);
  not not_22 (Q[3], d_ff_4_qn);
endmodule

module Index_Register (
  input  DIRECTION,
  input  CNT_EN,
  input  LATCH,
  input  CLOCK,
  input  [15:0] DATA_IN,
  input  Q_OUT,
  input  LSBO,
  output [15:0] Q_BASE,
  output [15:0] Q_DISPLACE
);

  wire not_1_out, not_2_out, undriven, updown_cntr_1_co, updown_cntr_2_co, updown_cntr_3_co;
  wire [3:0] updown_cntr_1_q, updown_cntr_2_q, updown_cntr_3_q, updown_cntr_4_q;

  UPDOWN_CNTR updown_cntr_1 (
    .UP_DOWN(DIRECTION), .LOAD(LATCH), .ENP(CNT_EN), .ENT(1'b0), .CLOCK(CLOCK), .Data_In(DATA_IN[3:0]),
    .Q(updown_cntr_1_q), .CO(updown_cntr_1_co));
  UPDOWN_CNTR updown_cntr_2 (
    .UP_DOWN(DIRECTION), .LOAD(LATCH), .ENP(undriven), .ENT(updown_cntr_1_co), .CLOCK(CLOCK),
    .Data_In(DATA_IN[7:4]), .Q(updown_cntr_2_q), .CO(updown_cntr_2_co));
  UPDOWN_CNTR updown_cntr_3 (
    .UP_DOWN(DIRECTION), .LOAD(LATCH), .ENP(undriven), .ENT(updown_cntr_2_co), .CLOCK(CLOCK),
    .Data_In(DATA_IN[11:8]), .Q(updown_cntr_3_q), .CO(updown_cntr_3_co));
  UPDOWN_CNTR updown_cntr_4 (
    .UP_DOWN(DIRECTION), .LOAD(LATCH), .ENP(undriven), .ENT(updown_cntr_3_co), .CLOCK(CLOCK),
    .Data_In(DATA_IN[15:12]), .Q(updown_cntr_4_q));  // open: CO
  // LedBar #(.inputtype("row"), .matrixcols(16)) ledbar_1: pin names not known; wires that end beside it: {updown_cntr_4_q, updown_cntr_3_q, updown_cntr_2_q, updown_cntr_1_q}
  not not_1 (not_1_out, LSBO);
  not not_2 (not_2_out, Q_OUT);
  assign Q_BASE = not_2_out ? {updown_cntr_4_q, updown_cntr_3_q, updown_cntr_2_q, updown_cntr_1_q} : 16'bz;  // Controlled_Buffer controlled_buffer_1
  assign Q_DISPLACE = not_1_out ? {updown_cntr_4_q, updown_cntr_3_q, updown_cntr_2_q, updown_cntr_1_q} : 16'bz;  // Controlled_Buffer controlled_buffer_2
endmodule
