// Logisim project eeprom_to_ram.circ as structural Verilog: 1 circuit, main circuit main
module main (
);

  wire button_1_out, clock_1_out, nand_1_out, nand_2_out, ttl_74ls169_1_co, ttl_74ls169_2_co,
       ttl_74ls169_3_co, ttl_74ls169_4_co;
  wire [3:0] ttl_74ls169_1_q, ttl_74ls169_2_q, ttl_74ls169_3_q, ttl_74ls169_4_q;

  Button #(.press("passive")) button_1 (.out(button_1_out));
  Clock clock_1 (.out(clock_1_out));
  TTL_74LS169 ttl_74ls169_1 (
    .UP_DOWN(1'b0), .LOAD(nand_1_out), .ENP(1'b0), .ENT(1'b0), .CLOCK(clock_1_out), .Data_In(4'b0000),
    .Q(ttl_74ls169_1_q), .CO(ttl_74ls169_1_co));
  nand nand_1 (nand_1_out, button_1_out, nand_2_out);
  Hex_Digit_Display hex_digit_display_1 (.value(ttl_74ls169_4_q));  // open: dp
  Hex_Digit_Display hex_digit_display_2 (.value(ttl_74ls169_3_q));  // open: dp
  nand nand_2 (nand_2_out, nand_1_out, ttl_74ls169_4_co);
  Hex_Digit_Display hex_digit_display_3 (.value(ttl_74ls169_2_q));  // open: dp
  Hex_Digit_Display hex_digit_display_4 (.value(ttl_74ls169_1_q));  // open: dp
  TTL_74LS169 ttl_74ls169_2 (
    .UP_DOWN(1'b0), .LOAD(nand_1_out), .ENP(1'b0), .ENT(ttl_74ls169_1_co), .CLOCK(clock_1_out),
    .Data_In(4'b0000), .Q(ttl_74ls169_2_q), .CO(ttl_74ls169_2_co));
  TTL_74LS169 ttl_74ls169_3 (
    .UP_DOWN(1'b0), .LOAD(nand_1_out), .ENP(1'b0), .ENT(ttl_74ls169_2_co), .CLOCK(clock_1_out),
    .Data_In(4'b0000), .Q(ttl_74ls169_3_q), .CO(ttl_74ls169_3_co));
  TTL_74LS169 ttl_74ls169_4 (
    .UP_DOWN(1'b0), .LOAD(nand_1_out), .ENP(1'b0), .ENT(ttl_74ls169_3_co), .CLOCK(clock_1_out),
    .Data_In(4'b0000), .Q(ttl_74ls169_4_q), .CO(ttl_74ls169_4_co));
endmodule
