// Logisim project flag-logic.circ as structural Verilog: 4 circuits, main circuit main
module main (
  input  MR,
  input  AI,
  input  BI,
  input  CI,
  input  AO,
  input  BO,
  input  CO,
  input  [7:0] in_8,
  output [7:0] out_9
);

  wire clock_1_out;

  Clock clock_1 (.out(clock_1_out));
  REGISTER_ARRAY register_array_1 (
    .AI(AI), .AO(AO), .BI(BI), .BO(BO), .CI(CI), .CO(CO), .MR(MR), .BUS(in_8), .CLOCK(clock_1_out));

  assign out_9 = in_8;
endmodule

module GPR_s (
  input  [7:0] in_1,
  input  ENABLE,
  input  CLOCK,
  input  RESET,
  input  OE,
  output [7:0] out_6
);

  wire [7:0] register_1_q;

  Register register_1 (.D(in_1), .en(ENABLE), .Q(register_1_q), .clk(CLOCK), .clr(RESET));
  _74LS245 u_74ls245_1 (.in_1(register_1_q), .OE(OE), .out_3(out_6));
endmodule

module _74LS245 (
  input  [7:0] in_1,
  input  OE,
  output [7:0] out_3
);

  assign out_3[0] = OE ? in_1[0] : 1'bz;  // Controlled_Buffer controlled_buffer_1
  assign out_3[1] = OE ? in_1[1] : 1'bz;  // Controlled_Buffer controlled_buffer_2
  assign out_3[2] = OE ? in_1[2] : 1'bz;  // Controlled_Buffer controlled_buffer_3
  assign out_3[3] = OE ? in_1[3] : 1'bz;  // Controlled_Buffer controlled_buffer_4
  assign out_3[4] = OE ? in_1[4] : 1'bz;  // Controlled_Buffer controlled_buffer_5
  assign out_3[5] = OE ? in_1[5] : 1'bz;  // Controlled_Buffer controlled_buffer_6
  assign out_3[6] = OE ? in_1[6] : 1'bz;  // Controlled_Buffer controlled_buffer_7
  assign out_3[7] = OE ? in_1[7] : 1'bz;  // Controlled_Buffer controlled_buffer_8
endmodule

module REGISTER_ARRAY (
  input  MR,
  input  CLOCK,
  input  AI,
  input  AO,
  input  BI,
  input  BO,
  input  CI,
  input  CO,
  output [7:0] BUS
);

  GPR_s gpr_s_1 (.in_1(BUS), .ENABLE(AI), .CLOCK(CLOCK), .RESET(MR), .OE(AO), .out_6(BUS));
  GPR_s gpr_s_2 (.in_1(BUS), .ENABLE(BI), .CLOCK(CLOCK), .RESET(MR), .OE(BO), .out_6(BUS));
  GPR_s gpr_s_3 (.in_1(BUS), .ENABLE(CI), .CLOCK(CLOCK), .RESET(MR), .OE(CO), .out_6(BUS));
endmodule
