// Logisim project memory_chip_enable_logic.circ as structural Verilog: 1 circuit, main circuit main
module main (
  input  SEG0,
  input  SEG1,
  input  SEG2,
  input  SEG3,
  input  MAR15
);

  wire not_1_out, not_2_out, or_1_out, or_2_out, or_3_out, or_4_out, or_5_out;

  or or_1 (or_1_out, SEG0, SEG1);
  or or_2 (or_2_out, SEG2, SEG3);
  or or_3 (or_3_out, or_1_out, or_2_out);
  not not_1 (not_1_out, or_4_out);
  not not_2 (not_2_out, SEG3);
  or or_4 (or_4_out, or_3_out, MAR15);
  or or_5 (or_5_out, not_1_out, SEG3);
  LED ENABLE_ROM (.in(or_4_out));
  LED ENABLE_RAM_LOW (.in(or_5_out));
  LED ENABLE_RAM_HIGH (.in(not_2_out));
endmodule
