// Logisim project register_controller_board.circ as structural Verilog: 1 circuit, main circuit main
module main (
  input  Enable_Clock
);

  wire and_1_out, clock_1_out, decoder_1_out0, decoder_1_out1, decoder_1_out2, decoder_1_out3,
       decoder_1_out4, decoder_1_out5, decoder_1_out6, decoder_1_out7, decoder_2_out0, decoder_2_out1,
       decoder_2_out2, decoder_2_out3, decoder_2_out4, decoder_2_out5, decoder_2_out6, decoder_2_out7,
       decoder_2_out8, decoder_2_out9, decoder_2_out10, decoder_2_out11, decoder_2_out12, decoder_2_out13,
       decoder_2_out14, decoder_2_out15, decoder_3_out0, decoder_3_out1, decoder_3_out2, decoder_3_out3,
       decoder_3_out4, decoder_3_out5, decoder_3_out6, decoder_3_out7, decoder_4_out0, decoder_4_out1,
       decoder_4_out2, decoder_4_out3, decoder_4_out4, decoder_4_out5, decoder_4_out6, decoder_4_out7,
       dipswitch_1_sw1, dipswitch_1_sw2, dipswitch_1_sw3, dipswitch_1_sw4, dipswitch_1_sw5, dipswitch_1_sw6,
       dipswitch_1_sw7, dipswitch_1_sw8, n74161_1_pin9, n74161_1_pin15, nor_1_out, not_1_out, not_2_out,
       not_8_out, not_9_out, not_22_out, not_23_out, not_30_out, not_31_out, not_35_out, not_37_out,
       not_40_out, or_1_out, or_2_out;
  wire [3:0] n74161_1_pin14, n74161_2_pin12;
  wire [4:0] not_3_out;
  wire [5:0] ledbar_3_p1, ledbar_4_p1;
  wire [10:0] ledbar_2_p1;

  Clock clock_1 (.out(clock_1_out));
  not not_1 (not_1_out, n74161_1_pin9);
  or or_1 (or_1_out, clock_1_out, not_1_out);
  DipSwitch dipswitch_1 (
    .sw1(dipswitch_1_sw1), .sw2(dipswitch_1_sw2), .sw3(dipswitch_1_sw3), .sw4(dipswitch_1_sw4),
    .sw5(dipswitch_1_sw5), .sw6(dipswitch_1_sw6), .sw7(dipswitch_1_sw7), .sw8(dipswitch_1_sw8));
  _74161 u_74161_1 (
    .pin2(or_1_out), .pin3(dipswitch_1_sw8), .pin4(dipswitch_1_sw7), .pin5(dipswitch_1_sw6),
    .pin6(dipswitch_1_sw5), .pin7(Enable_Clock), .pin15(n74161_1_pin15), .pin14(n74161_1_pin14[0]),
    .pin13(n74161_1_pin14[1]), .pin12(n74161_1_pin14[2]), .pin11(n74161_1_pin14[3]), .pin10(Enable_Clock),
    .pin9(n74161_1_pin9));  // open: pin1
  _74161 u_74161_2 (
    .pin2(or_1_out), .pin3(dipswitch_1_sw4), .pin4(dipswitch_1_sw3), .pin5(dipswitch_1_sw2),
    .pin6(dipswitch_1_sw1), .pin7(n74161_1_pin15), .pin14(n74161_2_pin12[0]), .pin13(n74161_2_pin12[1]),
    .pin12(n74161_2_pin12[2]), .pin11(n74161_2_pin12[3]), .pin10(n74161_1_pin15), .pin9(n74161_1_pin9));  // open: pin1, pin15
  Button #(.press("passive")) Load (.out(n74161_1_pin9));
  not not_2 (not_2_out, n74161_2_pin12[3]);
  // LedBar #(.inputtype("row"), .matrixcols(11)) ledbar_1: pin names not known
  and and_1 (and_1_out, n74161_2_pin12[2], not_2_out);
  nor nor_1 (nor_1_out, n74161_2_pin12[2], n74161_2_pin12[3]);
  // LedBar #(.inputtype("row"), .matrixcols(5)) ledbar_2: pin names not known; wires that end beside it: ledbar_2_p1
  not not_3 (not_3_out[0], decoder_1_out0);
  not not_4 (not_3_out[1], decoder_1_out1);
  not not_5 (not_3_out[2], decoder_1_out2);
  not not_6 (not_3_out[3], decoder_1_out3);
  not not_7 (not_3_out[4], decoder_1_out4);
  not not_8 (not_8_out, decoder_1_out5);
  not not_9 (not_9_out, decoder_1_out6);
  // NOT_Gate not_10 has open pins: in=decoder_1_out7, out=open
  Decoder #(.select(3)) decoder_1 (
    .out0(decoder_1_out0), .out1(decoder_1_out1), .out2(decoder_1_out2), .out3(decoder_1_out3),
    .out4(decoder_1_out4), .out5(decoder_1_out5), .out6(decoder_1_out6), .out7(decoder_1_out7),
    .sel(n74161_1_pin14[2:0]), .en(and_1_out));
  not not_11 (ledbar_2_p1[0], decoder_2_out0);
  not not_12 (ledbar_2_p1[1], decoder_2_out1);
  not not_13 (ledbar_2_p1[2], decoder_2_out2);
  not not_14 (ledbar_2_p1[3], decoder_2_out3);
  not not_15 (ledbar_2_p1[4], decoder_2_out4);
  not not_16 (ledbar_2_p1[5], decoder_2_out5);
  not not_17 (ledbar_2_p1[6], decoder_2_out6);
  not not_18 (ledbar_2_p1[7], decoder_2_out7);
  not not_19 (ledbar_2_p1[8], decoder_2_out8);
  not not_20 (ledbar_2_p1[9], decoder_2_out9);
  not not_21 (ledbar_2_p1[10], decoder_2_out10);
  // NoConnect on decoder_2_out11
  // NoConnect on decoder_2_out12
  // NoConnect on decoder_2_out13
  // NoConnect on decoder_2_out14
  // NoConnect on decoder_2_out15
  Decoder #(.select(4)) decoder_2 (
    .out0(decoder_2_out0), .out1(decoder_2_out1), .out2(decoder_2_out2), .out3(decoder_2_out3),
    .out4(decoder_2_out4), .out5(decoder_2_out5), .out6(decoder_2_out6), .out7(decoder_2_out7),
    .out8(decoder_2_out8), .out9(decoder_2_out9), .out10(decoder_2_out10), .out11(decoder_2_out11),
    .out12(decoder_2_out12), .out13(decoder_2_out13), .out14(decoder_2_out14), .out15(decoder_2_out15),
    .sel(n74161_1_pin14), .en(nor_1_out));
  not not_22 (not_22_out, not_8_out);
  not not_23 (not_23_out, not_9_out);
  // LedBar #(.inputtype("row"), .matrixcols(6)) ledbar_3: pin names not known; wires that end beside it: ledbar_3_p1
  // LedBar #(.inputtype("row"), .matrixcols(6)) ledbar_4: pin names not known; wires that end beside it: ledbar_4_p1
  or or_2 (or_2_out, not_22_out, not_23_out);
  not not_24 (ledbar_3_p1[0], decoder_3_out0);
  not not_25 (ledbar_3_p1[1], decoder_3_out1);
  not not_26 (ledbar_3_p1[2], decoder_3_out2);
  not not_27 (ledbar_3_p1[3], decoder_3_out3);
  not not_28 (ledbar_3_p1[4], decoder_3_out4);
  not not_29 (ledbar_3_p1[5], decoder_3_out5);
  // NoConnect on not_30_out
  not not_30 (not_30_out, decoder_3_out6);
  // NoConnect on not_31_out
  not not_31 (not_31_out, decoder_3_out7);
  Decoder #(.select(3)) decoder_3 (
    .out0(decoder_3_out0), .out1(decoder_3_out1), .out2(decoder_3_out2), .out3(decoder_3_out3),
    .out4(decoder_3_out4), .out5(decoder_3_out5), .out6(decoder_3_out6), .out7(decoder_3_out7),
    .sel({n74161_2_pin12[1:0], n74161_1_pin14[3]}), .en(or_2_out));
  not not_32 (ledbar_4_p1[0], decoder_4_out0);
  not not_33 (ledbar_4_p1[1], decoder_4_out1);
  not not_34 (ledbar_4_p1[2], decoder_4_out2);
  // NoConnect on not_35_out
  not not_35 (not_35_out, decoder_4_out3);
  not not_36 (ledbar_4_p1[3], decoder_4_out4);
  // NoConnect on not_37_out
  not not_37 (not_37_out, decoder_4_out5);
  not not_38 (ledbar_4_p1[4], decoder_4_out6);
  not not_39 (ledbar_4_p1[5], decoder_4_out7);
  not not_40 (not_40_out, not_9_out);
  Decoder #(.select(3)) decoder_4 (
    .out0(decoder_4_out0), .out1(decoder_4_out1), .out2(decoder_4_out2), .out3(decoder_4_out3),
    .out4(decoder_4_out4), .out5(decoder_4_out5), .out6(decoder_4_out6), .out7(decoder_4_out7),
    .sel({n74161_2_pin12[1:0], n74161_1_pin14[3]}), .en(not_40_out));
endmodule
