# Fritzing sketch sound-controller (saved by Fritzing 0.9.6b)
breadboards: 3

parts:
  IS61C1 = IS61C1024 [package="DIP (Dual Inline) [THT]"]
  74LS1 = 74LS273 [package="DIP (Dual Inline) [THT]"]
  74LS2 = 74LS273 [package="DIP (Dual Inline) [THT]"]
  74LS3 = 74LS173 4-bit Storage Register [package="DIP (Dual Inline) [THT]"]
  74LS4 = 74LS173 4-bit Storage Register [package="DIP (Dual Inline) [THT]"]
  D1 = LED_BARGRAPH_10 [package=led_bargaph_10]
  D2 = LED_BARGRAPH_10 [package=led_bargaph_10]
  D3 = LED_BARGRAPH_10 [package=led_bargaph_10]
  U1 = 555 Timer [package="DIP8 [THT]"]
  CD4023 = CD4022 [package="DIP (Dual Inline) [THT]"]
  D5 = LED_BARGRAPH_10 [package=led_bargaph_10]
  74LS02 = IC, DIP package, 14 pins [chip_label=74LS02]
  IC1 = DIP - 14 pins [chip_label=74LS00 package="DIP (Dual Inline) [THT]"]
  74LS5 = 74LS08 [package="DIP (Dual Inline) [THT]"]
  C1 = Electrolytic Capacitor [capacitance=1µF voltage=35V package="100 mil [THT, electrolytic]"]
  R1 = Trimmer Potentiometer [maximum_resistance=10kΩ package=THT]
  R2 = Resistor [tolerance=±5% power=0.25 resistance=220 package=THT]
  IC2 = DIP - 20 pins [chip_label="74LS245 (BUS)" package="DIP (Dual Inline) [THT]"]
  J1 = female pin header, 8 pins [form="♀ (female)"]
  J2 = female pin header, 8 pins [form="♀ (female)"]
  R3 = Resistor [tolerance=±5% power=0.25 resistance=220 package=THT]
  R4 = Resistor [tolerance=±5% power=0.25 resistance=220 package=THT]
  R5 = Resistor [tolerance=±5% power=0.25 resistance=220 package=THT]
  R6 = Resistor [tolerance=±5% power=0.25 resistance=220 package=THT]
  R7 = Resistor [tolerance=±5% power=0.25 resistance=220 package=THT]
  R8 = Resistor [tolerance=±5% power=0.25 resistance=220 package=THT]
  R9 = Resistor [tolerance=±5% power=0.25 resistance=220 package=THT]
  R10 = Resistor [tolerance=±5% power=0.25 resistance=220 package=THT]
  R11 = Resistor [tolerance=±5% power=0.25 resistance=220 package=THT]
  R12 = Resistor [tolerance=±5% power=0.25 resistance=220 package=THT]
  R13 = Resistor [tolerance=±5% power=0.25 resistance=220 package=THT]
  R14 = Resistor [tolerance=±5% power=0.25 resistance=220 package=THT]
  R15 = Resistor [tolerance=±5% power=0.25 resistance=220 package=THT]
  R16 = Resistor [tolerance=±5% power=0.25 resistance=220 package=THT]
  R17 = Resistor [tolerance=±5% power=0.25 resistance=220 package=THT]
  R18 = Resistor [tolerance=±5% power=0.25 resistance=220 package=THT]
  R19 = Resistor [tolerance=±5% power=0.25 resistance=220 package=THT]
  R20 = Resistor [tolerance=±5% power=0.25 resistance=220 package=THT]
  R21 = Resistor [tolerance=±5% power=0.25 resistance=220 package=THT]
  R22 = Resistor [tolerance=±5% power=0.25 resistance=220 package=THT]
  R23 = Resistor [tolerance=±5% power=0.25 resistance=220 package=THT]
  R24 = Resistor [tolerance=±5% power=0.25 resistance=220 package=THT]
  R25 = Resistor [tolerance=±5% power=0.25 resistance=220 package=THT]
  R26 = Resistor [tolerance=±5% power=0.25 resistance=220 package=THT]
  J3 = female pin header, 1 pin [form="♀ (female)"]
  Part1 = 74LS32 [package="DIP (Dual Inline) [THT]"]

nets:
  N1: IS61C1.I/O0, IC2.B8
  N2: IS61C1.I/O1, IC2.B7
  N3: IS61C1.I/02, IC2.B6
  GND: IS61C1.GND, IS61C1.CE1, IS61C1.OE, 74LS3.GND, 74LS3.CLR, 74LS4.GND, 74LS4.CLR, IC2.DIR, IC2.GND, R3.Pin_0, R4.Pin_0, R5.Pin_0, R6.Pin_0, R7.Pin_0, R8.Pin_0, R9.Pin_0, R10.Pin_0
  N4: IS61C1.I/O3, IC2.B5
  N5: IS61C1.I/O4, IC2.B4
  N6: IS61C1.I/O5, IC2.B3
  N7: IS61C1.I/O6, IC2.B2
  N8: IS61C1.I/O7, IC2.B1
  N9: IS61C1.WE, 74LS3.74LS173_4-bit_Storage_Register, 74LS3.N, 74LS4.74LS173_4-bit_Storage_Register, 74LS4.N, IC1.pin11
  VCC: IS61C1.CE2, IS61C1.VCC, 74LS3.VCC, 74LS4.VCC, IC2.VCC
  VCC_2: 74LS1.MR, 74LS1.VCC, 74LS2.MR, 74LS2.VCC
  N10: 74LS1.QO, D1.A_A
  N11: 74LS1.DO, 74LS2.DO, J2.pin8
  N12: 74LS1.D1, 74LS2.D1, J2.pin7
  N13: 74LS1.Q1, D1.B_A
  N14: 74LS1.Q2, D1.C_A
  N15: 74LS1.D2, 74LS2.D2, J2.pin6
  N16: 74LS1.D3, 74LS2.D3, J2.pin5
  N17: 74LS1.Q3, D1.D_A
  GND_2: 74LS1.GND, 74LS2.GND, R11.Pin_0, R12.Pin_0, R13.Pin_0, R14.Pin_0, R15.Pin_0, R16.Pin_0, R17.Pin_0, R18.Pin_0, R19.Pin_0, R20.Pin_0, R21.Pin_0, R22.Pin_0, R23.Pin_0, R24.Pin_0, R25.Pin_0, R26.Pin_0
  N18: 74LS1.CP, CD4023.O2, D5.C_A
  N19: 74LS1.Q4, D1.E_A
  N20: 74LS1.D4, 74LS2.D4, J2.pin4
  N21: 74LS1.D5, 74LS2.D5, J2.pin3
  N22: 74LS1.Q5, D1.F_A
  N23: 74LS1.Q6, D1.G_A
  N24: 74LS1.D6, 74LS2.D6, J2.pin2
  N25: 74LS1.D7, 74LS2.D7, J2.pin1
  N26: 74LS1.Q7, D1.H_A
  N27: 74LS2.QO, D1.I_A
  N28: 74LS2.Q1, D1.J_A
  N29: 74LS2.Q2, D2.A_A
  N30: 74LS2.Q3, D2.B_A
  N31: 74LS2.CP, CD4023.O1, D5.B_A
  N32: 74LS3.1Q, D3.A_A
  N33: 74LS3.2Q, D3.B_A
  N34: 74LS3.3Q, D3.C_A
  N35: 74LS3.4Q, D3.D_A
  N36: 74LS3.CLK, 74LS4.CLK
  N37: 74LS3.G1, 74LS3.G2, 74LS4.G1, 74LS4.G2, 74LS5.Y1
  N38: 74LS4.1Q, D3.E_A
  N39: 74LS4.2Q, D3.F_A
  N40: 74LS4.3Q, D3.G_A
  N41: 74LS4.4Q, D3.H_A
  N42: D1.J_C, R17.Pin_1
  N43: D1.I_C, R20.Pin_1
  N44: D1.H_C, R21.Pin_1
  N45: D1.G_C, R13.Pin_1
  N46: D1.F_C, R14.Pin_1
  N47: D1.E_C, R11.Pin_1
  N48: D1.D_C, R12.Pin_1
  N49: D1.C_C, R15.Pin_1
  N50: D1.B_C, R22.Pin_1
  N51: D1.A_C, R23.Pin_1
  N52: D2.F_C, R24.Pin_1
  N53: D2.E_C, R25.Pin_1
  N54: D2.D_C, R26.Pin_1
  N55: D2.C_C, R18.Pin_1
  N56: D2.B_C, R19.Pin_1
  N57: D2.A_C, R16.Pin_1
  N58: D3.H_C, R10.Pin_1
  N59: D3.G_C, R9.Pin_1
  N60: D3.F_C, R8.Pin_1
  N61: D3.E_C, R7.Pin_1
  N62: D3.D_C, R6.Pin_1
  N63: D3.C_C, R5.Pin_1
  N64: D3.B_C, R4.Pin_1
  N65: D3.A_C, R3.Pin_1
  GND_3: U1.Ground, CD4023.GND, CD4023.CE, 74LS02.pin7, IC1.pin7, IC1.pin9, 74LS5.GND, C1.-, Part1.GND
  N66: U1.Trigger, U1.Threshold, C1.+, R1.wiper
  N67: U1.Output, CD4023.CP
  N68: U1.Discharge, R1.leg1, R2.Pin_1
  VCC_3: U1.Vcc_Supply_Voltage, CD4023.VCC, 74LS02.pin14, IC1.pin14, 74LS5.VCC, R2.Pin_0, Part1.VCC
  N69: CD4023.O0, D5.A_A
  N70: CD4023.O5, D5.F_A, 74LS02.pin12
  N71: CD4023.O6, Part1.B4
  N72: CD4023.O3, D5.D_A, 74LS5.A1, 74LS5.A4
  N73: CD4023.O4, D5.E_A, 74LS02.pin8
  N74: CD4023.RS, Part1.Y4
  N75: 74LS02.pin9, 74LS02.pin13, IC1.pin13
  N76: 74LS02.pin10, 74LS02.pin11
  N77: IC1.pin8, 74LS5.B4
  N78: IC1.pin10, IC1.pin12, 74LS5.B1, J3.pin1
  N79: 74LS5.Y4, Part1.A4
  N80: IC2.A1, J1.pin1
  N81: IC2.A2, J1.pin2
  N82: IC2.A3, J1.pin3
  N83: IC2.A4, J1.pin4
  N84: IC2.A5, J1.pin5
  N85: IC2.A6, J1.pin6
  N86: IC2.A7, J1.pin7
  N87: IC2.A8, J1.pin8

notes:
  OE
  WE
  BUS
  OUTPUT
  PROGRAM MODE?
  HIGH=Programming
  LOW=Reading
  Counter
  1.  MAR Low Bits
  2.  MAR High Bits
  3.  Data Register (if ProgamMode true)
  0.  Do Nothing
  4.  Write RAM (if ProgamMode true)
  5.  Reset Counter (if ProgamMode true)
  3.  Reset (if ProgramMode false)
  TODO
  MAR IN w/ an OR on a control line,
  or program mode counter

custom parts:
  IS61C1024: 128K x 8 HIGH-SPEED CMOS STATIC RAM
  74LS273: 8-Bit Register with Clear
  74LS173 4-bit Storage Register: A DIP stand-in part for whatever IC you want. With 16 pins on a 300mil dual inline package (DIP) footprint.
  CD4022: CD4022BM/CD4022BC Divide-by-8 Counter/Divider with 8 Decoded Outputs
  DIP - 14 pins: A DIP stand-in part for whatever IC you want. With 14 pins on a 300mil dual inline package (DIP) footprint.
  DIP - 20 pins: A DIP stand-in part for whatever IC you want. With 20 pins on a 300mil dual inline package (DIP) footprint.
  74LS32: Quad 2-Input OR Gate
