# Fritzing sketch sound-controller 3 (saved by Fritzing 0.9.6b)
breadboards: 3

parts:
  IS61C1 = IS61C1024 [package="DIP (Dual Inline) [THT]"]
  74LS1 = 74LS273 [package="DIP (Dual Inline) [THT]"]
  74LS2 = 74LS273 [package="DIP (Dual Inline) [THT]"]
  74LS3 = 74LS173 4-bit Storage Register [package="DIP (Dual Inline) [THT]"]
  74LS4 = 74LS173 4-bit Storage Register [package="DIP (Dual Inline) [THT]"]
  D1 = LED_BARGRAPH_10 [package=led_bargaph_10]  # not connected
  D2 = LED_BARGRAPH_10 [package=led_bargaph_10]  # not connected
  D3 = LED_BARGRAPH_10 [package=led_bargaph_10]  # not connected
  D4 = LED_BARGRAPH_10 [package=led_bargaph_10]  # not connected
  U1 = 555 Timer [package="DIP8 [THT]"]
  CD4023 = CD4022 [package="DIP (Dual Inline) [THT]"]
  D5 = LED_BARGRAPH_10 [package=led_bargaph_10]  # not connected

nets:
  GND: IS61C1.GND, 74LS3.GND, 74LS4.GND
  VCC: IS61C1.VCC, 74LS3.VCC, 74LS4.VCC
  GND_2: 74LS1.GND, 74LS2.GND
  VCC_2: 74LS1.VCC, 74LS2.VCC
  N1: U1.Ground, CD4023.GND
  N2: U1.Vcc_Supply_Voltage, CD4023.VCC

custom parts:
  IS61C1024: 128K x 8 HIGH-SPEED CMOS STATIC RAM
  74LS273: 8-Bit Register with Clear
  74LS173 4-bit Storage Register: A DIP stand-in part for whatever IC you want. With 16 pins on a 300mil dual inline package (DIP) footprint.
  CD4022: CD4022BM/CD4022BC Divide-by-8 Counter/Divider with 8 Decoded Outputs
