# Fritzing sketch Waveform Function Generator (saved by Fritzing 0.9.6b)
breadboards: 1

parts:
  ICL1 = ICL8038 [chip_label=ICL8038 package="DIP (Dual Inline) [THT]"]
  R1 = TRIMPOT [package=trimpot_pth_s3_lock]
  R2 = TRIMPOT [package=trimpot_pth_s3_lock]
  R3 = TRIMPOT [package=trimpot_pth_s3_lock]
  R4 = Resistor [tolerance=±5% power=0.25 resistance=10k package=THT]
  Power_plug1 = Power plug
  S1 = Toggle Switch [package=THT]
  C1 = Ceramic Capacitor [capacitance=3.3nF voltage=50V package="100 mil [THT, multilayer]"]

nets:
  N1: ICL1.Duty_Cycle_Freq_Adjust#3, R1.WIPER
  N2: ICL1.Duty_Cycle_Freq_Adjust#4, R3.WIPER
  N3: ICL1.V+, R1.CCW, R2.CCW, R3.CCW, R4.Pin_0, Power_plug1.GND
  N4: ICL1.FM_Bias, S1.COM
  N5: ICL1.Square_Wave_Out, R4.Pin_1
  N6: ICL1.Timing_Capacitor, C1.1
  N7: ICL1.V-_/_Gnd, Power_plug1.VCC, C1.0
  N8: ICL1.Sine_Wave_Adjust, R2.WIPER

notes:
  3.3nF
  10kΩ
  100kΩ
  12V DC
  Triangle
  Sine
  Square
  Sine Adjust
  Duty Cycle

custom parts:
  ICL8038: Precision Waveform Generator/Voltage Controlled Oscillator
